// Logisim project 15puzzleSB.circ as structural Verilog: 2 circuits, main circuit Digit
module main (
);

  wire _011, _012, _013, _014, _021, _022, _023, _024, _031, _032, _033, _034, _041, _042, _043, _044, _051,
       _052, _053, _054, _111, _112, _113, _114, _121, _122, _123, _124, _131, _132, _133, _134, _141, _142,
       _143, _144, _151, _152, _153, _154, _211, _212, _213, _214, _221, _222, _223, _224, _231, _232, _233,
       _234, _241, _242, _243, _244, _251, _252, _253, _254, _311, _312, _313, _314, _321, _322, _323, _324,
       _331, _332, _333, _334, _341, _342, _343, _344, _351, _352, _353, _354, _411, _412, _413, _414, _421,
       _422, _423, _424, _431, _432, _433, _434, _441, _442, _443, _444, _451, _452, _453, _454, _511, _512,
       _513, _514, _521, _522, _523, _524, _531, _532, _533, _534, _541, _542, _543, _544, _551, _552, _553,
       _554, _611, _612, _613, _614, _621, _622, _623, _624, _631, _632, _633, _634, _641, _642, _643, _644,
       _651, _652, _653, _654, _711, _712, _713, _714, _721, _722, _723, _724, _731, _732, _733, _734, _741,
       _742, _743, _744, _751, _752, _753, _754, _811, _812, _813, _814, _821, _822, _823, _824, _831, _832,
       _833, _834, _841, _842, _843, _844, _851, _852, _853, _854, _911, _912, _913, _914, _921, _922, _923,
       _924, _931, _932, _933, _934, _941, _942, _943, _944, _951, _952, _953, _954, A11, A12, A13, A14, A21,
       A22, A23, A24, A31, A32, A33, A34, A41, A42, A43, A44, A51, A52, A53, A54, B11, B12, B13, B14, B21,
       B22, B23, B24, B31, B32, B33, B34, B41, B42, B43, B44, B51, B52, B53, B54, C11, C12, C13, C14, C21,
       C22, C23, C24, C31, C32, C33, C34, C41, C42, C43, C44, C51, C52, C53, C54, D11, D12, D13, D14, D21,
       D22, D23, D24, D31, D32, D33, D34, D41, D42, D43, D44, D51, D52, D53, D54, E11, E12, E13, E14, E21,
       E22, E23, E24, E31, E32, E33, E34, E41, E42, E43, E44, E51, E52, E53, E54, F11, F12, F13, F14, F21,
       F22, F23, F24, F31, F32, F33, F34, F41, F42, F43, F44, F51, F52, F53, F54, undriven, undriven_2,
       undriven_3, undriven_4, undriven_5, undriven_6;
  wire [3:0] r0, r1, r2, r3, r4, r5, r6, r7, r8, r9, rA, rB, rC, rD, rE, rF;

  TTY #(.rows(1), .cols(73)) tty_1 ();  // open: data, clk, we, clr
  LED led_1 (.in(_111));
  LED led_2 (.in(_112));
  LED led_3 (.in(_121));
  LED led_4 (.in(_122));
  LED led_5 (.in(_131));
  LED led_6 (.in(_132));
  LED led_7 (.in(_142));
  LED led_8 (.in(_141));
  LED led_9 (.in(_152));
  LED led_10 (.in(_151));
  TTY #(.rows(2), .cols(73)) tty_2 ();  // open: data, clk, we, clr
  LED led_11 (.in(_512));
  LED led_12 (.in(_511));
  LED led_13 (.in(_521));
  LED led_14 (.in(_522));
  LED led_15 (.in(_532));
  LED led_16 (.in(_531));
  LED led_17 (.in(_542));
  LED led_18 (.in(_541));
  LED led_19 (.in(_552));
  LED led_20 (.in(_551));
  TTY #(.rows(2), .cols(73)) tty_3 ();  // open: data, clk, we, clr
  LED led_21 (.in(_911));
  LED led_22 (.in(_912));
  LED led_23 (.in(_921));
  LED led_24 (.in(_922));
  LED led_25 (.in(_932));
  LED led_26 (.in(_931));
  LED led_27 (.in(_942));
  LED led_28 (.in(_941));
  LED led_29 (.in(_951));
  LED led_30 (.in(_952));
  TTY #(.rows(2), .cols(73)) tty_4 ();  // open: data, clk, we, clr
  LED led_31 (.in(D12));
  LED led_32 (.in(D11));
  LED led_33 (.in(D22));
  LED led_34 (.in(D21));
  LED led_35 (.in(D31));
  LED led_36 (.in(D32));
  LED led_37 (.in(D42));
  LED led_38 (.in(D41));
  LED led_39 (.in(D51));
  LED led_40 (.in(D52));
  TTY #(.rows(37), .cols(4)) tty_5 ();  // open: data, clk, we, clr
  TTY #(.rows(2), .cols(73)) tty_6 ();  // open: data, clk, we, clr
  Button UP ();  // open: out
  Button DOWN ();  // open: out
  Button RIGHT ();  // open: out
  Button LEFT ();  // open: out
  Register #(.width(4)) register_1 (.Q(r1));  // open: D, en, clk, clr
  Register #(.width(4)) register_2 (.Q(r5));  // open: D, en, clk, clr
  Register #(.width(4)) register_3 (.Q(r9));  // open: D, en, clk, clr
  Register #(.width(4)) register_4 (.Q(rD));  // open: D, en, clk, clr
  LED led_41 (.in(_113));
  LED led_42 (.in(_114));
  LED led_43 (.in(_124));
  LED led_44 (.in(_123));
  LED led_45 (.in(_133));
  LED led_46 (.in(_134));
  LED led_47 (.in(_143));
  LED led_48 (.in(_144));
  LED led_49 (.in(_154));
  LED led_50 (.in(_153));
  LED led_51 (.in(_514));
  LED led_52 (.in(_513));
  LED led_53 (.in(_523));
  LED led_54 (.in(_524));
  LED led_55 (.in(_534));
  LED led_56 (.in(_533));
  LED led_57 (.in(_543));
  LED led_58 (.in(_544));
  LED led_59 (.in(_553));
  LED led_60 (.in(_554));
  LED led_61 (.in(_914));
  LED led_62 (.in(_913));
  LED led_63 (.in(_924));
  LED led_64 (.in(_923));
  LED led_65 (.in(_933));
  LED led_66 (.in(_934));
  LED led_67 (.in(_943));
  LED led_68 (.in(_944));
  LED led_69 (.in(_954));
  LED led_70 (.in(_953));
  LED led_71 (.in(D13));
  LED led_72 (.in(D14));
  LED led_73 (.in(D23));
  LED led_74 (.in(D24));
  LED led_75 (.in(D33));
  LED led_76 (.in(D34));
  LED led_77 (.in(D43));
  LED led_78 (.in(D44));
  LED led_79 (.in(D53));
  LED led_80 (.in(D54));
  TTY #(.rows(37), .cols(4)) tty_7 ();  // open: data, clk, we, clr
  Comparator comparator_1 ();  // open: a, b, gt, eq, lt
  Register #(.width(4)) register_5 (.Q(r2));  // open: D, en, clk, clr
  Register #(.width(4)) register_6 (.Q(r6));  // open: D, en, clk, clr
  Register #(.width(4)) register_7 (.Q(rA));  // open: D, en, clk, clr
  Register #(.width(4)) register_8 (.Q(rE));  // open: D, en, clk, clr
  LED led_81 (.in(_211));
  LED led_82 (.in(_214));
  LED led_83 (.in(_212));
  LED led_84 (.in(_213));
  LED led_85 (.in(_223));
  LED led_86 (.in(_221));
  LED led_87 (.in(_222));
  LED led_88 (.in(_231));
  LED led_89 (.in(_233));
  LED led_90 (.in(_232));
  LED led_91 (.in(_242));
  LED led_92 (.in(_243));
  LED led_93 (.in(_241));
  LED led_94 (.in(_252));
  LED led_95 (.in(_253));
  LED led_96 (.in(_251));
  LED led_97 (.in(_254));
  LED led_98 (.in(_611));
  LED led_99 (.in(_614));
  LED led_100 (.in(_612));
  LED led_101 (.in(_613));
  LED led_102 (.in(_623));
  LED led_103 (.in(_621));
  LED led_104 (.in(_622));
  LED led_105 (.in(_632));
  LED led_106 (.in(_631));
  LED led_107 (.in(_633));
  LED led_108 (.in(_641));
  LED led_109 (.in(_642));
  LED led_110 (.in(_643));
  LED led_111 (.in(_652));
  LED led_112 (.in(_654));
  LED led_113 (.in(_653));
  LED led_114 (.in(_651));
  LED led_115 (.in(A13));
  LED led_116 (.in(A14));
  LED led_117 (.in(A12));
  LED led_118 (.in(A11));
  LED led_119 (.in(A21));
  LED led_120 (.in(A23));
  LED led_121 (.in(A22));
  LED led_122 (.in(A33));
  LED led_123 (.in(A31));
  LED led_124 (.in(A32));
  LED led_125 (.in(A42));
  LED led_126 (.in(A41));
  LED led_127 (.in(A43));
  LED led_128 (.in(A52));
  LED led_129 (.in(A51));
  LED led_130 (.in(A53));
  LED led_131 (.in(A54));
  LED led_132 (.in(E13));
  LED led_133 (.in(E14));
  LED led_134 (.in(E11));
  LED led_135 (.in(E12));
  LED led_136 (.in(E21));
  LED led_137 (.in(E22));
  LED led_138 (.in(E23));
  LED led_139 (.in(E31));
  LED led_140 (.in(E33));
  LED led_141 (.in(E32));
  LED led_142 (.in(E43));
  LED led_143 (.in(E41));
  LED led_144 (.in(E42));
  LED led_145 (.in(E54));
  LED led_146 (.in(E52));
  LED led_147 (.in(E53));
  LED led_148 (.in(E51));
  Register #(.width(4)) register_9 (.Q(r3));  // open: D, en, clk, clr
  Register #(.width(4)) register_10 (.Q(r7));  // open: D, en, clk, clr
  Register #(.width(4)) register_11 (.Q(rB));  // open: D, en, clk, clr
  Register #(.width(4)) register_12 (.Q(rF));  // open: D, en, clk, clr
  LED led_149 (.in(_312));
  LED led_150 (.in(_311));
  LED led_151 (.in(_322));
  LED led_152 (.in(_321));
  LED led_153 (.in(_224));
  LED led_154 (.in(_332));
  LED led_155 (.in(_234));
  LED led_156 (.in(_331));
  LED led_157 (.in(_341));
  LED led_158 (.in(_342));
  LED led_159 (.in(_244));
  LED led_160 (.in(_351));
  LED led_161 (.in(_352));
  LED led_162 (.in(_711));
  LED led_163 (.in(_712));
  LED led_164 (.in(_721));
  LED led_165 (.in(_722));
  LED led_166 (.in(_624));
  LED led_167 (.in(_731));
  LED led_168 (.in(_732));
  LED led_169 (.in(_634));
  LED led_170 (.in(_742));
  LED led_171 (.in(_644));
  LED led_172 (.in(_741));
  LED led_173 (.in(_752));
  LED led_174 (.in(_751));
  LED led_175 (.in(B11));
  LED led_176 (.in(B12));
  LED led_177 (.in(B21));
  LED led_178 (.in(B22));
  LED led_179 (.in(A24));
  LED led_180 (.in(A34));
  LED led_181 (.in(B31));
  LED led_182 (.in(B32));
  LED led_183 (.in(B42));
  LED led_184 (.in(B41));
  LED led_185 (.in(A44));
  LED led_186 (.in(B52));
  LED led_187 (.in(B51));
  LED led_188 (.in(F12));
  LED led_189 (.in(F11));
  LED led_190 (.in(F21));
  LED led_191 (.in(F22));
  LED led_192 (.in(E24));
  LED led_193 (.in(F32));
  LED led_194 (.in(E34));
  LED led_195 (.in(F31));
  LED led_196 (.in(F41));
  LED led_197 (.in(F42));
  LED led_198 (.in(E44));
  LED led_199 (.in(F51));
  LED led_200 (.in(F52));
  TTY #(.rows(37), .cols(4)) tty_8 ();  // open: data, clk, we, clr
  RAM #(.dataWidth(4)) ram_1 ();  // open: addr, data, sel, clk, ld, clr
  Register #(.width(4)) register_13 (.Q(r4));  // open: D, en, clk, clr
  Register #(.width(4)) register_14 (.Q(r8));  // open: D, en, clk, clr
  Register #(.width(4)) register_15 (.Q(rC));  // open: D, en, clk, clr
  Register #(.width(4)) register_16 (.Q(r0));  // open: D, en, clk, clr
  LED led_201 (.in(_314));
  LED led_202 (.in(_313));
  LED led_203 (.in(_323));
  LED led_204 (.in(_324));
  LED led_205 (.in(_333));
  LED led_206 (.in(_334));
  LED led_207 (.in(_343));
  LED led_208 (.in(_344));
  LED led_209 (.in(_353));
  LED led_210 (.in(_354));
  LED led_211 (.in(_714));
  LED led_212 (.in(_713));
  LED led_213 (.in(_723));
  LED led_214 (.in(_724));
  LED led_215 (.in(_734));
  LED led_216 (.in(_733));
  LED led_217 (.in(_743));
  LED led_218 (.in(_744));
  LED led_219 (.in(_754));
  LED led_220 (.in(_753));
  LED led_221 (.in(B14));
  LED led_222 (.in(B13));
  LED led_223 (.in(B24));
  LED led_224 (.in(B23));
  LED led_225 (.in(B33));
  LED led_226 (.in(B34));
  LED led_227 (.in(B43));
  LED led_228 (.in(B44));
  LED led_229 (.in(B54));
  LED led_230 (.in(B53));
  LED led_231 (.in(F14));
  LED led_232 (.in(F13));
  LED led_233 (.in(F24));
  LED led_234 (.in(F23));
  LED led_235 (.in(F33));
  LED led_236 (.in(F34));
  LED led_237 (.in(F44));
  LED led_238 (.in(F43));
  LED led_239 (.in(F53));
  LED led_240 (.in(F54));
  TTY #(.rows(37), .cols(4)) tty_9 ();  // open: data, clk, we, clr
  LED led_241 (.in(_413));
  LED led_242 (.in(_412));
  LED led_243 (.in(_411));
  LED led_244 (.in(_414));
  LED led_245 (.in(_423));
  LED led_246 (.in(_421));
  LED led_247 (.in(_422));
  LED led_248 (.in(_433));
  LED led_249 (.in(_431));
  LED led_250 (.in(_432));
  LED led_251 (.in(_443));
  LED led_252 (.in(_442));
  LED led_253 (.in(_441));
  LED led_254 (.in(_454));
  LED led_255 (.in(_453));
  LED led_256 (.in(_452));
  LED led_257 (.in(_451));
  LED led_258 (.in(_812));
  LED led_259 (.in(_811));
  LED led_260 (.in(_813));
  LED led_261 (.in(_814));
  LED led_262 (.in(_823));
  LED led_263 (.in(_821));
  LED led_264 (.in(_822));
  LED led_265 (.in(_832));
  LED led_266 (.in(_831));
  LED led_267 (.in(_833));
  LED led_268 (.in(_842));
  LED led_269 (.in(_843));
  LED led_270 (.in(_841));
  LED led_271 (.in(_853));
  LED led_272 (.in(_852));
  LED led_273 (.in(_854));
  LED led_274 (.in(_851));
  LED led_275 (.in(C12));
  LED led_276 (.in(C13));
  LED led_277 (.in(C11));
  LED led_278 (.in(C14));
  LED led_279 (.in(C21));
  LED led_280 (.in(C22));
  LED led_281 (.in(C23));
  LED led_282 (.in(C33));
  LED led_283 (.in(C32));
  LED led_284 (.in(C31));
  LED led_285 (.in(C43));
  LED led_286 (.in(C41));
  LED led_287 (.in(C42));
  LED led_288 (.in(C53));
  LED led_289 (.in(C52));
  LED led_290 (.in(C51));
  LED led_291 (.in(C54));
  LED led_292 (.in(_011));
  LED led_293 (.in(_013));
  LED led_294 (.in(_014));
  LED led_295 (.in(_012));
  LED led_296 (.in(_023));
  LED led_297 (.in(_022));
  LED led_298 (.in(_021));
  LED led_299 (.in(_033));
  LED led_300 (.in(_031));
  LED led_301 (.in(_032));
  LED led_302 (.in(_043));
  LED led_303 (.in(_042));
  LED led_304 (.in(_041));
  LED led_305 (.in(_052));
  LED led_306 (.in(_054));
  LED led_307 (.in(_053));
  LED led_308 (.in(_051));
  LED led_309 ();  // open: in
  LED led_310 ();  // open: in
  LED led_311 ();  // open: in
  LED led_312 (.in(undriven_2));
  LED led_313 ();  // open: in
  LED led_314 (.in(undriven_3));
  LED led_315 (.in(undriven));
  LED led_316 ();  // open: in
  LED led_317 ();  // open: in
  LED led_318 ();  // open: in
  LED led_319 (.in(_424));
  LED led_320 (.in(_434));
  LED led_321 (.in(_444));
  LED led_322 (.in(_824));
  LED led_323 (.in(_834));
  LED led_324 (.in(_844));
  LED led_325 (.in(C24));
  LED led_326 (.in(C34));
  LED led_327 (.in(C44));
  LED led_328 (.in(_024));
  LED led_329 (.in(_034));
  LED led_330 (.in(_044));
  TTY #(.rows(37), .cols(4)) tty_10 ();  // open: data, clk, we, clr
  LED led_331 ();  // open: in
  LED led_332 ();  // open: in
  LED led_333 ();  // open: in
  LED led_334 (.in(undriven_4));
  LED led_335 (.in(undriven_5));
  LED led_336 ();  // open: in
  LED led_337 (.in(undriven_6));
  LED led_338 ();  // open: in
  LED led_339 ();  // open: in
  LED led_340 ();  // open: in
  ROM #(.addrWidth(4), .dataWidth(20)) rom_1 (
    .addr(r1),
    .data({_154, _153, _152, _151, _144, _143, _142, _141, _134, _133, _132, _131, _124, _123, _122, _121, _114, _113, _112, _111}));  // open: sel
  ROM #(.addrWidth(4), .dataWidth(20)) rom_2 (
    .addr(r5),
    .data({_554, _553, _552, _551, _544, _543, _542, _541, _534, _533, _532, _531, _524, _523, _522, _521, _514, _513, _512, _511}));  // open: sel
  ROM #(.addrWidth(4), .dataWidth(20)) rom_3 (
    .addr(r9),
    .data({_954, _953, _952, _951, _944, _943, _942, _941, _934, _933, _932, _931, _924, _923, _922, _921, _914, _913, _912, _911}));  // open: sel
  ROM #(.addrWidth(4), .dataWidth(20)) rom_4 (
    .addr(rD),
    .data({D54, D53, D52, D51, D44, D43, D42, D41, D34, D33, D32, D31, D24, D23, D22, D21, D14, D13, D12, D11}));  // open: sel
  ROM #(.addrWidth(4), .dataWidth(20)) rom_5 (
    .addr(r2),
    .data({_254, _253, _252, _251, _244, _243, _242, _241, _234, _233, _232, _231, _224, _223, _222, _221, _214, _213, _212, _211}));  // open: sel
  ROM #(.addrWidth(4), .dataWidth(20)) rom_6 (
    .addr(r6),
    .data({_654, _653, _652, _651, _644, _643, _642, _641, _634, _633, _632, _631, _624, _623, _622, _621, _614, _613, _612, _611}));  // open: sel
  ROM #(.addrWidth(4), .dataWidth(20)) rom_7 (
    .addr(rA),
    .data({A54, A53, A52, A51, A44, A43, A42, A41, A34, A33, A32, A31, A24, A23, A22, A21, A14, A13, A12, A11}));  // open: sel
  ROM #(.addrWidth(4), .dataWidth(20)) rom_8 (
    .addr(rE),
    .data({E54, E53, E52, E51, E44, E43, E42, E41, E34, E33, E32, E31, E24, E23, E22, E21, E14, E13, E12, E11}));  // open: sel
  ROM #(.addrWidth(4), .dataWidth(20)) rom_9 (
    .addr(r3),
    .data({_354, _353, _352, _351, _344, _343, _342, _341, _334, _333, _332, _331, _324, _323, _322, _321, _314, _313, _312, _311}));  // open: sel
  ROM #(.addrWidth(4), .dataWidth(20)) rom_10 (
    .addr(r7),
    .data({_754, _753, _752, _751, _744, _743, _742, _741, _734, _733, _732, _731, _724, _723, _722, _721, _714, _713, _712, _711}));  // open: sel
  ROM #(.addrWidth(4), .dataWidth(20)) rom_11 (
    .addr(rB),
    .data({B54, B53, B52, B51, B44, B43, B42, B41, B34, B33, B32, B31, B24, B23, B22, B21, B14, B13, B12, B11}));  // open: sel
  ROM #(.addrWidth(4), .dataWidth(20)) rom_12 (
    .addr(rF),
    .data({F54, F53, F52, F51, F44, F43, F42, F41, F34, F33, F32, F31, F24, F23, F22, F21, F14, F13, F12, F11}));  // open: sel
  ROM #(.addrWidth(4), .dataWidth(20)) rom_13 (
    .addr(r4),
    .data({_454, _453, _452, _451, _444, _443, _442, _441, _434, _433, _432, _431, _424, _423, _422, _421, _414, _413, _412, _411}));  // open: sel
  ROM #(.addrWidth(4), .dataWidth(20)) rom_14 (
    .addr(r8),
    .data({_854, _853, _852, _851, _844, _843, _842, _841, _834, _833, _832, _831, _824, _823, _822, _821, _814, _813, _812, _811}));  // open: sel
  ROM #(.addrWidth(4), .dataWidth(20)) rom_15 (
    .addr(rC),
    .data({C54, C53, C52, C51, C44, C43, C42, C41, C34, C33, C32, C31, C24, C23, C22, C21, C14, C13, C12, C11}));  // open: sel
  ROM #(.addrWidth(4), .dataWidth(20)) rom_16 (
    .addr(r0),
    .data({_054, _053, _052, _051, _044, _043, _042, _041, _034, _033, _032, _031, _024, _023, _022, _021, _014, _013, _012, _011}));  // open: sel
  LED led_341 ();  // open: in

  // Notes on the sheet:
  //   contents of rom_1 (hex, n*v repeats v):
  //   0 f4564 f1f8f f8f8f 88f99 f8f1f f9f1f 1248f f9f9f f8f9f 99f9f f9f11 f111f f9f88 f1f1f 11f1f
  //   contents of rom_2 (hex, n*v repeats v):
  //   0 f4564 f1f8f f8f8f 88f99 f8f1f f9f1f 1248f f9f9f f8f9f 99f9f f9f11 f111f f9f88 f1f1f 11f1f
  //   contents of rom_3 (hex, n*v repeats v):
  //   0 f4564 f1f8f f8f8f 88f99 f8f1f f9f1f 1248f f9f9f f8f9f 99f9f f9f11 f111f f9f88 f1f1f 11f1f
  //   contents of rom_4 (hex, n*v repeats v):
  //   0 f4564 f1f8f f8f8f 88f99 f8f1f f9f1f 1248f f9f9f f8f9f 99f9f f9f11 f111f f9f88 f1f1f 11f1f
  //   contents of rom_5 (hex, n*v repeats v):
  //   0 f4564 f1f8f f8f8f 88f99 f8f1f f9f1f 1248f f9f9f f8f9f 99f9f f9f11 f111f f9f88 f1f1f 11f1f
  //   contents of rom_6 (hex, n*v repeats v):
  //   0 f4564 f1f8f f8f8f 88f99 f8f1f f9f1f 1248f f9f9f f8f9f 99f9f f9f11 f111f f9f88 f1f1f 11f1f
  //   contents of rom_7 (hex, n*v repeats v):
  //   0 f4564 f1f8f f8f8f 88f99 f8f1f f9f1f 1248f f9f9f f8f9f 99f9f f9f11 f111f f9f88 f1f1f 11f1f
  //   contents of rom_8 (hex, n*v repeats v):
  //   0 f4564 f1f8f f8f8f 88f99 f8f1f f9f1f 1248f f9f9f f8f9f 99f9f f9f11 f111f f9f88 f1f1f 11f1f
  //   contents of rom_9 (hex, n*v repeats v):
  //   0 f4564 f1f8f f8f8f 88f99 f8f1f f9f1f 1248f f9f9f f8f9f 99f9f f9f11 f111f f9f88 f1f1f 11f1f
  //   contents of rom_10 (hex, n*v repeats v):
  //   0 f4564 f1f8f f8f8f 88f99 f8f1f f9f1f 1248f f9f9f f8f9f 99f9f f9f11 f111f f9f88 f1f1f 11f1f
  //   contents of rom_11 (hex, n*v repeats v):
  //   0 f4564 f1f8f f8f8f 88f99 f8f1f f9f1f 1248f f9f9f f8f9f 99f9f f9f11 f111f f9f88 f1f1f 11f1f
  //   contents of rom_12 (hex, n*v repeats v):
  //   0 f4564 f1f8f f8f8f 88f99 f8f1f f9f1f 1248f f9f9f f8f9f 99f9f f9f11 f111f f9f88 f1f1f 11f1f
  //   contents of rom_13 (hex, n*v repeats v):
  //   0 f4564 f1f8f f8f8f 88f99 f8f1f f9f1f 1248f f9f9f f8f9f 99f9f f9f11 f111f f9f88 f1f1f 11f1f
  //   contents of rom_14 (hex, n*v repeats v):
  //   0 f4564 f1f8f f8f8f 88f99 f8f1f f9f1f 1248f f9f9f f8f9f 99f9f f9f11 f111f f9f88 f1f1f 11f1f
  //   contents of rom_15 (hex, n*v repeats v):
  //   0 f4564 f1f8f f8f8f 88f99 f8f1f f9f1f 1248f f9f9f f8f9f 99f9f f9f11 f111f f9f88 f1f1f 11f1f
  //   contents of rom_16 (hex, n*v repeats v):
  //   0 f4564 f1f8f f8f8f 88f99 f8f1f f9f1f 1248f f9f9f f8f9f 99f9f f9f11 f111f f9f88 f1f1f 11f1f
endmodule

module Digit (
  input  [3:0] in_1
);

  wire _12345;
  wire [19:0] rom_1_data;

  ROM #(.addrWidth(4), .dataWidth(20)) rom_1 (
    .addr(in_1), .data({rom_1_data[19:4], _12345, rom_1_data[2:0]}));  // open: sel
  LED led_1 (.in(rom_1_data[0]));
  LED led_2 (.in(rom_1_data[1]));
  LED led_3 (.in(rom_1_data[5]));
  LED led_4 (.in(rom_1_data[4]));
  LED led_5 (.in(rom_1_data[8]));
  LED led_6 (.in(rom_1_data[9]));
  LED led_7 (.in(rom_1_data[12]));
  LED led_8 (.in(rom_1_data[13]));
  LED led_9 (.in(rom_1_data[17]));
  LED led_10 (.in(rom_1_data[16]));
  LED led_11 (.in(rom_1_data[2]));
  LED led_12 (.in(rom_1_data[7]));
  LED led_13 (.in(rom_1_data[6]));
  LED led_14 (.in(rom_1_data[11]));
  LED led_15 (.in(rom_1_data[10]));
  LED led_16 (.in(rom_1_data[14]));
  LED led_17 (.in(rom_1_data[15]));
  LED led_18 (.in(rom_1_data[18]));
  LED led_19 (.in(rom_1_data[19]));

  // Notes on the sheet:
  //   contents of rom_1 (hex, n*v repeats v):
  //   f999f f4564 f1f8f f8f8f 88f99 f8f1f f9f1f 1248f f9f9f f8f9f 99f9f f9f11 f111f f9f88 f1f1f 11f1f
endmodule
