// Logisim project 15puzzleV018.circ as structural Verilog: 2 circuits, main circuit Digit
module main (
);

  wire _011, _012, _013, _014, _021, _022, _023, _024, _031, _032, _033, _034, _041, _042, _043, _044, _051,
       _052, _053, _054, _111, _112, _113, _114, _121, _122, _123, _124, _131, _132, _133, _134, _141, _142,
       _143, _144, _151, _152, _153, _154, _211, _212, _213, _214, _221, _222, _223, _224, _231, _232, _233,
       _234, _241, _242, _243, _244, _251, _252, _253, _254, _311, _312, _313, _314, _321, _322, _323, _324,
       _331, _332, _333, _334, _341, _342, _343, _344, _351, _352, _353, _354, _411, _412, _413, _414, _421,
       _422, _423, _424, _431, _432, _433, _434, _441, _442, _443, _444, _451, _452, _453, _454, _511, _512,
       _513, _514, _521, _522, _523, _524, _531, _532, _533, _534, _541, _542, _543, _544, _551, _552, _553,
       _554, _611, _612, _613, _614, _621, _622, _623, _624, _631, _632, _633, _634, _641, _642, _643, _644,
       _651, _652, _653, _654, _711, _712, _713, _714, _721, _722, _723, _724, _731, _732, _733, _734, _741,
       _742, _743, _744, _751, _752, _753, _754, _811, _812, _813, _814, _821, _822, _823, _824, _831, _832,
       _833, _834, _841, _842, _843, _844, _851, _852, _853, _854, _911, _912, _913, _914, _921, _922, _923,
       _924, _931, _932, _933, _934, _941, _942, _943, _944, _951, _952, _953, _954, A11, A12, A13, A14, A21,
       A22, A23, A24, A31, A32, A33, A34, A41, A42, A43, A44, A51, A52, A53, A54, ad, adF1, adW, B11, B12,
       B13, B14, B21, B22, B23, B24, B31, B32, B33, B34, B41, B42, B43, B44, B51, B52, B53, B54,
       button_2_out, button_3_out, button_6_out, button_out, C11, C12, C13, C14, C21, C22, C23, C24, C31,
       C32, C33, C34, C41, C42, C43, C44, C51, C52, C53, C54, clock_1_out, D11, D12, D13, D14, D21, D22, D23,
       D24, D31, D32, D33, D34, D41, D42, D43, D44, D51, D52, D53, D54, decoder_1_out0, decoder_1_out1,
       decoder_1_out2, decoder_1_out3, DkR1, DkR2, DkR3, DkR4, DkR5, DkR6, DkR7, DkR8, DkR9, DkRA, DkRB,
       DkRC, DOWN, DOWN1, E11, E12, E13, E14, E21, E22, E23, E24, E31, E32, E33, E34, E41, E42, E43, E44,
       E51, E52, E53, E54, en, enF1, enW, F11, F12, F13, F14, F21, F22, F23, F24, F31, F32, F33, F34, F41,
       F42, F43, F44, F51, F52, F53, F54, kR0, kR1, kR2, kR3, kR4, kR5, kR6, kR7, kR8, kR9, kRA, kRB, kRC,
       kRD, kRE, kRF, LEFT, LEFT1, LkR0, LkR2, LkR3, LkR4, LkR6, LkR7, LkR8, LkRA, LkRB, LkRC, LkRE, LkRF,
       memory, not_1_out, not_2_out, not_3_out, or_1_out, or_2_out, or_3_out, or_4_out, or_5_out, or_6_out,
       or_7_out, or_8_out, or_9_out, or_10_out, or_11_out, or_12_out, or_13_out, or_14_out, or_15_out,
       or_16_out, or_17_out, or_18_out, or_19_out, or_20_out, or_21_out, or_22_out, or_23_out, or_24_out,
       or_25_out, or_26_out, or_27_out, or_28_out, or_29_out, or_30_out, or_31_out, or_32_out, or_33_out,
       or_34_out, or_35_out, or_36_out, or_37_out, or_38_out, or_39_out, or_40_out, or_41_out, or_42_out,
       or_43_out, or_44_out, or_45_out, or_46_out, or_47_out, or_48_out, or_49_out, or_50_out, R, read_write,
       Reset, RIGHT, RIGHT1, RkR1, RkR2, RkR3, RkR5, RkR6, RkR7, RkR9, RkRA, RkRB, RkRD, RkRE, RkRF, T,
       Tcdm8, TWin, undriven, undriven_2, undriven_3, undriven_4, undriven_5, undriven_6, UP, UP1, UpkR0,
       UpkR5, UpkR6, UpkR7, UpkR8, UpkR9, UpkRA, UpkRB, UpkRC, UpkRD, UpkRE, UpkRF, Win;
  wire [1:0] random_1_out;
  wire [3:0] multiplexer_18_out, multiplexer_20_out, multiplexer_22_out, multiplexer_23_out,
       multiplexer_25_out, multiplexer_26_out, multiplexer_28_out, multiplexer_40_out, multiplexer_41_out,
       multiplexer_42_out, multiplexer_43_out, multiplexer_44_out, multiplexer_46_out, multiplexer_47_out,
       multiplexer_48_out, multiplexer_50_out, multiplexer_51_out, multiplexer_68_out, multiplexer_69_out,
       multiplexer_70_out, multiplexer_71_out, multiplexer_72_out, multiplexer_74_out, multiplexer_75_out,
       multiplexer_76_out, multiplexer_78_out, multiplexer_79_out, multiplexer_96_out, multiplexer_98_out,
       multiplexer_99_out, multiplexer_101_out, multiplexer_102_out, multiplexer_104_out, r0, r0Res, r1,
       r1_r2, r1_r5, r1_r5_2, r1_r6, r1Res, r2, r2_r3, r2_r3_2, r2_r4, r2_r5, r2_r5_2, r2_r6, r2Res, r3,
       r3_r6, r3_r6_2, r3_r7, r3_r8, r3Res, r4, r4_r3, r4_r7, r4Res, r5, r5_r9, r5Res, r6, r6_r7, r6_r7_2,
       r6_r9, r6_r9_2, r6Res, r7, r7_r8, r7_r8_2, r7_rA, r7_rA_2, r7Res, r8, r8_rB, r8_rB_2, r8_rC, r8Res,
       r9, r9_rA, r9_rA_2, r9_rD, r9Res, rA, rA_rB, rA_rB_2, rA_rD, rA_rD_2, rARes, rB, rB_rC, rB_rC_2,
       rB_rE, rB_rE_2, rBRes, rC, rC_r0, rC_rF, rC_rF_2, rCRes, rD, rD_rE, rD_rE_2, rDRes, rE, rE_rF,
       rE_rF_2, register_18_q, rERes, rF, rF_r0, rF_r0_2, rFRes;
  wire [7:0] addr, cdm_8_mark5_1_r0, cdm_8_mark5_1_r1, cdm_8_mark5_1_r2, cdm_8_mark5_1_r3, CELL_BYTE, data,
       i1, i2, i3, i4, i5, multiplexer_7_out, multiplexer_17_out, n1, n2, n3, n4, n5, out, w1, w2, w3, w4, w5;
  wire [7:1] register_17_q;

  Register #(.width(4)) register_1 (.D(r1Res), .Q(r1), .clk(T));  // open: en, clr
  Register #(.width(4)) register_2 (.D(r5Res), .Q(r5), .clk(T));  // open: en, clr
  Register #(.width(4)) register_3 (.D(r9Res), .Q(r9), .clk(T));  // open: en, clr
  Register #(.width(4)) register_4 (.D(rDRes), .Q(rD), .clk(T));  // open: en, clr
  TTY #(.rows(1), .cols(73)) tty_1 ();  // open: data, clk, we, clr
  LED led_1 (.in(_111));
  LED led_2 (.in(_112));
  LED led_3 (.in(_122));
  LED led_4 (.in(_121));
  LED led_5 (.in(_132));
  LED led_6 (.in(_131));
  LED led_7 (.in(_141));
  LED led_8 (.in(_142));
  LED led_9 (.in(_151));
  LED led_10 (.in(_152));
  TTY #(.rows(2), .cols(73)) tty_2 ();  // open: data, clk, we, clr
  LED led_11 (.in(_511));
  LED led_12 (.in(_512));
  LED led_13 (.in(_521));
  LED led_14 (.in(_522));
  LED led_15 (.in(_532));
  LED led_16 (.in(_531));
  LED led_17 (.in(_541));
  LED led_18 (.in(_542));
  LED led_19 (.in(_551));
  LED led_20 (.in(_552));
  TTY #(.rows(2), .cols(73)) tty_3 ();  // open: data, clk, we, clr
  LED led_21 (.in(_912));
  LED led_22 (.in(_911));
  LED led_23 (.in(_921));
  LED led_24 (.in(_922));
  LED led_25 (.in(_931));
  LED led_26 (.in(_932));
  LED led_27 (.in(_942));
  LED led_28 (.in(_941));
  LED led_29 (.in(_951));
  LED led_30 (.in(_952));
  TTY #(.rows(2), .cols(73)) tty_4 ();  // open: data, clk, we, clr
  LED led_31 (.in(D12));
  LED led_32 (.in(D11));
  LED led_33 (.in(D22));
  LED led_34 (.in(D21));
  LED led_35 (.in(D32));
  LED led_36 (.in(D31));
  LED led_37 (.in(D42));
  LED led_38 (.in(D41));
  LED led_39 (.in(D52));
  LED led_40 (.in(D51));
  TTY #(.rows(37), .cols(4)) tty_5 ();  // open: data, clk, we, clr
  TTY #(.rows(2), .cols(73)) tty_6 ();  // open: data, clk, we, clr
  // Probe on cdm_8_mark5_1_r0
  Multiplexer #(.width(8)) multiplexer_1 (.in0({8{1'b0}}), .in1({8{1'b1}}), .out(w1), .sel(Win));  // open: en
  Multiplexer #(.width(8)) multiplexer_2 (.in0({8{1'b0}}), .in1(8'h81), .out(i1), .sel(Win));  // open: en
  Multiplexer #(.width(8)) multiplexer_3 (.in0({8{1'b0}}), .in1({8{1'b1}}), .out(n1), .sel(Win));  // open: en
  LED led_41 (.in(_113));
  LED led_42 (.in(_114));
  LED led_43 (.in(_124));
  LED led_44 (.in(_123));
  LED led_45 (.in(_133));
  LED led_46 (.in(_134));
  LED led_47 (.in(_144));
  LED led_48 (.in(_143));
  LED led_49 (.in(_153));
  LED led_50 (.in(_154));
  LED led_51 (.in(_514));
  LED led_52 (.in(_513));
  LED led_53 (.in(_523));
  LED led_54 (.in(_524));
  LED led_55 (.in(_533));
  LED led_56 (.in(_534));
  LED led_57 (.in(_544));
  LED led_58 (.in(_543));
  LED led_59 (.in(_553));
  LED led_60 (.in(_554));
  LED led_61 (.in(_913));
  LED led_62 (.in(_914));
  LED led_63 (.in(_923));
  LED led_64 (.in(_924));
  LED led_65 (.in(_934));
  LED led_66 (.in(_933));
  LED led_67 (.in(_944));
  LED led_68 (.in(_943));
  LED led_69 (.in(_953));
  LED led_70 (.in(_954));
  LED led_71 (.in(D14));
  LED led_72 (.in(D13));
  LED led_73 (.in(D24));
  LED led_74 (.in(D23));
  LED led_75 (.in(D34));
  LED led_76 (.in(D33));
  LED led_77 (.in(D44));
  LED led_78 (.in(D43));
  LED led_79 (.in(D53));
  LED led_80 (.in(D54));
  TTY #(.rows(37), .cols(4)) tty_7 ();  // open: data, clk, we, clr
  // Probe on cdm_8_mark5_1_r2
  // Probe on cdm_8_mark5_1_r1
  // Probe on cdm_8_mark5_1_r3
  and and_1 (en, memory, ad, not_1_out);
  not not_1 (not_1_out, read_write);
  Comparator comparator_1 (.a(addr), .b(8'hf0), .eq(ad));  // open: gt, lt
  Multiplexer #(.width(8)) multiplexer_4 (.in0({8{1'b0}}), .in1(8'h2), .out(w2), .sel(Win));  // open: en
  Multiplexer #(.width(8)) multiplexer_5 (.in0({8{1'b0}}), .in1(8'h81), .out(i2), .sel(Win));  // open: en
  Multiplexer #(.width(8)) multiplexer_6 (.in0({8{1'b0}}), .in1(8'h60), .out(n2), .sel(Win));  // open: en
  Register #(.width(4)) register_5 (.D(r2Res), .Q(r2), .clk(T));  // open: en, clr
  Register #(.width(4)) register_6 (.D(r6Res), .Q(r6), .clk(T));  // open: en, clr
  Register #(.width(4)) register_7 (.D(rARes), .Q(rA), .clk(T));  // open: en, clr
  Register #(.width(4)) register_8 (.D(rERes), .Q(rE), .clk(T));  // open: en, clr
  LED led_81 (.in(_212));
  LED led_82 (.in(_211));
  LED led_83 (.in(_214));
  LED led_84 (.in(_213));
  LED led_85 (.in(_223));
  LED led_86 (.in(_221));
  LED led_87 (.in(_222));
  LED led_88 (.in(_233));
  LED led_89 (.in(_232));
  LED led_90 (.in(_231));
  LED led_91 (.in(_241));
  LED led_92 (.in(_242));
  LED led_93 (.in(_243));
  LED led_94 (.in(_253));
  LED led_95 (.in(_254));
  LED led_96 (.in(_251));
  LED led_97 (.in(_252));
  LED led_98 (.in(_612));
  LED led_99 (.in(_613));
  LED led_100 (.in(_614));
  LED led_101 (.in(_611));
  LED led_102 (.in(_621));
  LED led_103 (.in(_622));
  LED led_104 (.in(_623));
  LED led_105 (.in(_631));
  LED led_106 (.in(_632));
  LED led_107 (.in(_633));
  LED led_108 (.in(_642));
  LED led_109 (.in(_643));
  LED led_110 (.in(_641));
  LED led_111 (.in(_652));
  LED led_112 (.in(_653));
  LED led_113 (.in(_651));
  LED led_114 (.in(_654));
  LED led_115 (.in(A14));
  LED led_116 (.in(A11));
  LED led_117 (.in(A13));
  LED led_118 (.in(A12));
  LED led_119 (.in(A22));
  LED led_120 (.in(A21));
  LED led_121 (.in(A23));
  LED led_122 (.in(A33));
  LED led_123 (.in(A31));
  LED led_124 (.in(A32));
  LED led_125 (.in(A41));
  LED led_126 (.in(A43));
  LED led_127 (.in(A42));
  LED led_128 (.in(A53));
  LED led_129 (.in(A54));
  LED led_130 (.in(A51));
  LED led_131 (.in(A52));
  LED led_132 (.in(E13));
  LED led_133 (.in(E14));
  LED led_134 (.in(E12));
  LED led_135 (.in(E11));
  LED led_136 (.in(E21));
  LED led_137 (.in(E23));
  LED led_138 (.in(E22));
  LED led_139 (.in(E31));
  LED led_140 (.in(E33));
  LED led_141 (.in(E32));
  LED led_142 (.in(E41));
  LED led_143 (.in(E42));
  LED led_144 (.in(E43));
  LED led_145 (.in(E51));
  LED led_146 (.in(E52));
  LED led_147 (.in(E54));
  LED led_148 (.in(E53));
  CdM_8_mark5 cdm_8_mark5_1 (
    .clock(Tcdm8), .addr(addr), .mem_read(read_write), .mem_cycle(memory), .data_out(out),
    .data_in(multiplexer_7_out), .r0(cdm_8_mark5_1_r0), .r1(cdm_8_mark5_1_r1), .r2(cdm_8_mark5_1_r2),
    .r3(cdm_8_mark5_1_r3));  // open: data_inst, PC, SP, PS, IAck, IRQ, vec
  Multiplexer #(.width(8)) multiplexer_7 (
    .in0(data), .in1(CELL_BYTE), .out(multiplexer_7_out), .sel(enF1));  // open: en
  ROM rom_1 (.addr(addr), .data(data));  // open: sel
  Multiplexer #(.width(8)) multiplexer_8 (.in0({8{1'b0}}), .in1(8'h1c), .out(w3), .sel(Win));  // open: en
  Multiplexer #(.width(8)) multiplexer_9 (.in0({8{1'b0}}), .in1({8{1'b1}}), .out(i3), .sel(Win));  // open: en
  Multiplexer #(.width(8)) multiplexer_10 (.in0({8{1'b0}}), .in1(8'h18), .out(n3), .sel(Win));  // open: en
  Register #(.width(4)) register_9 (.D(r3Res), .Q(r3), .clk(T));  // open: en, clr
  Register #(.width(4)) register_10 (.D(r7Res), .Q(r7), .clk(T));  // open: en, clr
  Register #(.width(4)) register_11 (.D(rBRes), .Q(rB), .clk(T));  // open: en, clr
  Register #(.width(4)) register_12 (.D(rFRes), .Q(rF), .clk(T));  // open: en, clr
  LED led_149 (.in(_312));
  LED led_150 (.in(_311));
  LED led_151 (.in(_322));
  LED led_152 (.in(_224));
  LED led_153 (.in(_321));
  LED led_154 (.in(_332));
  LED led_155 (.in(_234));
  LED led_156 (.in(_331));
  LED led_157 (.in(_342));
  LED led_158 (.in(_341));
  LED led_159 (.in(_244));
  LED led_160 (.in(_352));
  LED led_161 (.in(_351));
  LED led_162 (.in(_712));
  LED led_163 (.in(_711));
  LED led_164 (.in(_722));
  LED led_165 (.in(_721));
  LED led_166 (.in(_624));
  LED led_167 (.in(_731));
  LED led_168 (.in(_634));
  LED led_169 (.in(_732));
  LED led_170 (.in(_742));
  LED led_171 (.in(_644));
  LED led_172 (.in(_741));
  LED led_173 (.in(_751));
  LED led_174 (.in(_752));
  LED led_175 (.in(B12));
  LED led_176 (.in(B11));
  LED led_177 (.in(A24));
  LED led_178 (.in(B22));
  LED led_179 (.in(B21));
  LED led_180 (.in(A34));
  LED led_181 (.in(B31));
  LED led_182 (.in(B32));
  LED led_183 (.in(B42));
  LED led_184 (.in(B41));
  LED led_185 (.in(A44));
  LED led_186 (.in(B52));
  LED led_187 (.in(B51));
  LED led_188 (.in(F12));
  LED led_189 (.in(F11));
  LED led_190 (.in(F22));
  LED led_191 (.in(F21));
  LED led_192 (.in(E24));
  LED led_193 (.in(F32));
  LED led_194 (.in(F31));
  LED led_195 (.in(E34));
  LED led_196 (.in(E44));
  LED led_197 (.in(F42));
  LED led_198 (.in(F41));
  LED led_199 (.in(F51));
  LED led_200 (.in(F52));
  TTY #(.rows(37), .cols(4)) tty_8 ();  // open: data, clk, we, clr
  and and_2 (enF1, memory, adF1, read_write);
  Comparator comparator_2 (.a(addr), .b(8'hf1), .eq(adF1));  // open: gt, lt
  Multiplexer #(.width(8)) multiplexer_11 (.in0({8{1'b0}}), .in1(8'h2), .out(w4), .sel(Win));  // open: en
  Multiplexer #(.width(8)) multiplexer_12 (.in0({8{1'b0}}), .in1(8'h81), .out(i4), .sel(Win));  // open: en
  Multiplexer #(.width(8)) multiplexer_13 (.in0({8{1'b0}}), .in1(8'h6), .out(n4), .sel(Win));  // open: en
  LED led_201 (.in(_314));
  LED led_202 (.in(_313));
  LED led_203 (.in(_324));
  LED led_204 (.in(_323));
  LED led_205 (.in(_333));
  LED led_206 (.in(_334));
  LED led_207 (.in(_343));
  LED led_208 (.in(_344));
  LED led_209 (.in(_354));
  LED led_210 (.in(_353));
  LED led_211 (.in(_713));
  LED led_212 (.in(_714));
  LED led_213 (.in(_724));
  LED led_214 (.in(_723));
  LED led_215 (.in(_733));
  LED led_216 (.in(_734));
  LED led_217 (.in(_744));
  LED led_218 (.in(_743));
  LED led_219 (.in(_754));
  LED led_220 (.in(_753));
  LED led_221 (.in(B13));
  LED led_222 (.in(B14));
  LED led_223 (.in(B23));
  LED led_224 (.in(B24));
  LED led_225 (.in(B33));
  LED led_226 (.in(B34));
  LED led_227 (.in(B43));
  LED led_228 (.in(B44));
  LED led_229 (.in(B53));
  LED led_230 (.in(B54));
  LED led_231 (.in(F14));
  LED led_232 (.in(F13));
  LED led_233 (.in(F23));
  LED led_234 (.in(F24));
  LED led_235 (.in(F34));
  LED led_236 (.in(F33));
  LED led_237 (.in(F43));
  LED led_238 (.in(F44));
  LED led_239 (.in(F54));
  LED led_240 (.in(F53));
  TTY #(.rows(37), .cols(4)) tty_9 ();  // open: data, clk, we, clr
  Multiplexer #(.width(8)) multiplexer_14 (.in0({8{1'b0}}), .in1({8{1'b1}}), .out(w5), .sel(Win));  // open: en
  Multiplexer #(.width(8)) multiplexer_15 (.in0({8{1'b0}}), .in1(8'h81), .out(i5), .sel(Win));  // open: en
  Multiplexer #(.width(8)) multiplexer_16 (.in0({8{1'b0}}), .in1({8{1'b1}}), .out(n5), .sel(Win));  // open: en
  Register #(.width(4)) register_13 (.D(r4Res), .Q(r4), .clk(T));  // open: en, clr
  Register #(.width(4)) register_14 (.D(r8Res), .Q(r8), .clk(T));  // open: en, clr
  Register #(.width(4)) register_15 (.D(rCRes), .Q(rC), .clk(T));  // open: en, clr
  Register #(.width(4)) register_16 (.D(r0Res), .Q(r0), .clk(T));  // open: en, clr
  LED led_241 (.in(_413));
  LED led_242 (.in(_412));
  LED led_243 (.in(_414));
  LED led_244 (.in(_411));
  LED led_245 (.in(_423));
  LED led_246 (.in(_421));
  LED led_247 (.in(_422));
  LED led_248 (.in(_433));
  LED led_249 (.in(_431));
  LED led_250 (.in(_432));
  LED led_251 (.in(_443));
  LED led_252 (.in(_441));
  LED led_253 (.in(_442));
  LED led_254 (.in(_451));
  LED led_255 (.in(_454));
  LED led_256 (.in(_452));
  LED led_257 (.in(_453));
  LED led_258 (.in(_811));
  LED led_259 (.in(_813));
  LED led_260 (.in(_812));
  LED led_261 (.in(_814));
  LED led_262 (.in(_822));
  LED led_263 (.in(_821));
  LED led_264 (.in(_823));
  LED led_265 (.in(_832));
  LED led_266 (.in(_831));
  LED led_267 (.in(_833));
  LED led_268 (.in(_841));
  LED led_269 (.in(_843));
  LED led_270 (.in(_842));
  LED led_271 (.in(_854));
  LED led_272 (.in(_851));
  LED led_273 (.in(_852));
  LED led_274 (.in(_853));
  LED led_275 (.in(C13));
  LED led_276 (.in(C12));
  LED led_277 (.in(C11));
  LED led_278 (.in(C14));
  LED led_279 (.in(C22));
  LED led_280 (.in(C21));
  LED led_281 (.in(C23));
  LED led_282 (.in(C33));
  LED led_283 (.in(C31));
  LED led_284 (.in(C32));
  LED led_285 (.in(C43));
  LED led_286 (.in(C42));
  LED led_287 (.in(C41));
  LED led_288 (.in(C51));
  LED led_289 (.in(C54));
  LED led_290 (.in(C52));
  LED led_291 (.in(C53));
  LED led_292 (.in(_011));
  LED led_293 (.in(_014));
  LED led_294 (.in(_013));
  LED led_295 (.in(_012));
  LED led_296 (.in(_021));
  LED led_297 (.in(_022));
  LED led_298 (.in(_023));
  LED led_299 (.in(_031));
  LED led_300 (.in(_033));
  LED led_301 (.in(_032));
  LED led_302 (.in(_042));
  LED led_303 (.in(_041));
  LED led_304 (.in(_043));
  LED led_305 (.in(_051));
  LED led_306 (.in(_052));
  LED led_307 (.in(_053));
  LED led_308 (.in(_054));
  Multiplexer #(.width(8)) multiplexer_17 (
    .in0(out), .in1({8{1'b0}}), .out(multiplexer_17_out), .sel(Reset));  // open: en
  Register register_17 (.D(multiplexer_17_out), .en(or_1_out), .Q({register_17_q, Win}), .clk(TWin));  // open: clr
  or or_1 (or_1_out, Reset, enW);
  and and_3 (enW, memory, adW, not_2_out);
  not not_2 (not_2_out, read_write);
  Comparator comparator_3 (.a(addr), .b(8'hf2), .eq(adW));  // open: gt, lt
  Clock clock_1 (.out(clock_1_out));
  Random #(.width(2), .seed(4)) random_1 (.clk(clock_1_out), .next(R), .out(random_1_out));  // open: clr
  LED led_309 (.in(_424));
  LED led_310 (.in(_434));
  LED led_311 (.in(_444));
  LED led_312 (.in(_824));
  LED led_313 (.in(_834));
  LED led_314 (.in(_844));
  LED led_315 (.in(C24));
  LED led_316 (.in(C34));
  LED led_317 (.in(C44));
  LED led_318 (.in(_024));
  LED led_319 (.in(_034));
  LED led_320 (.in(_044));
  TTY #(.rows(37), .cols(4)) tty_10 ();  // open: data, clk, we, clr
  Decoder #(.select(2), .enable("false")) decoder_1 (
    .out0(decoder_1_out0), .out1(decoder_1_out1), .out2(decoder_1_out2), .out3(decoder_1_out3),
    .sel(random_1_out));
  DotMatrix #(.matrixrows(8)) dotmatrix_1 (.col0(w1), .col1(w2), .col2(w3), .col3(w4), .col4(w5));
  DotMatrix #(.matrixrows(8)) dotmatrix_2 (.col0(i1), .col1(i2), .col2(i3), .col3(i4), .col4(i5));
  and and_4 (LEFT, TWin, button_out);
  Multiplexer #(.select(4), .width(4)) multiplexer_18 (
    .in0(r0), .in1(r1), .in2(r2), .in3(r3), .in4(r4), .in5(r5), .in6(r6), .in7(r7), .in8(r8), .in9(r9),
    .in10(rA), .in11(rB), .in12(rC), .in13(rD), .in14(rE), .in15(rF), .out(multiplexer_18_out),
    .sel(register_18_q));  // open: en
  Register #(.width(4)) register_18 (.D(out[3:0]), .en(en), .Q(register_18_q), .clk(Tcdm8));  // open: clr
  and and_5 (UP1, R, decoder_1_out0);
  and and_6 (RIGHT1, R, decoder_1_out3);
  DotMatrix #(.matrixrows(8)) dotmatrix_3 (.col0(n1), .col1(n2), .col2(n3), .col3(n4), .col4(n5));
  Button button (.out(button_out));
  Clock #(.highDuration(150), .lowDuration(150)) clock_2 (.out(T));
  assign CELL_BYTE = {{4{1'b0}}, multiplexer_18_out};  // Bit_Extender bit_extender_1
  LED led_321 ();  // open: in
  and and_7 (DOWN1, R, decoder_1_out1);
  LED led_322 ();  // open: in
  LED led_323 ();  // open: in
  and and_8 (LEFT1, R, decoder_1_out2);
  and and_9 (UP, TWin, button_2_out);
  Button button_2 (.out(button_2_out));
  and and_10 (DOWN, TWin, button_3_out);
  Button button_3 (.out(button_3_out));
  Clock clock_3 (.out(Tcdm8));
  LED led_324 ();  // open: in
  LED led_325 ();  // open: in
  LED led_326 ();  // open: in
  LED led_327 ();  // open: in
  LED led_328 (.in(undriven_4));
  LED led_329 (.in(undriven));
  LED led_330 ();  // open: in
  LED led_331 (.in(undriven_2));
  LED led_332 (.in(undriven_5));
  LED led_333 ();  // open: in
  LED led_334 ();  // open: in
  LED led_335 (.in(undriven_3));
  LED led_336 (.in(undriven_6));
  LED led_337 ();  // open: in
  LED led_338 ();  // open: in
  LED led_339 ();  // open: in
  LED led_340 ();  // open: in
  Button button_4 (.out(Reset));
  and and_11 (RIGHT, TWin, button_6_out);
  and and_12 (TWin, Tcdm8, or_2_out);
  or or_2 (or_2_out, Reset, not_3_out);
  not not_3 (not_3_out, Win);
  Button button_5 (.out(R));
  Button button_6 (.out(button_6_out));
  ROM #(.addrWidth(4), .dataWidth(20)) rom_2 (
    .addr(r1),
    .data({_154, _153, _152, _151, _144, _143, _142, _141, _134, _133, _132, _131, _124, _123, _122, _121, _114, _113, _112, _111}));  // open: sel
  ROM #(.addrWidth(4), .dataWidth(20)) rom_3 (
    .addr(r5),
    .data({_554, _553, _552, _551, _544, _543, _542, _541, _534, _533, _532, _531, _524, _523, _522, _521, _514, _513, _512, _511}));  // open: sel
  ROM #(.addrWidth(4), .dataWidth(20)) rom_4 (
    .addr(r9),
    .data({_954, _953, _952, _951, _944, _943, _942, _941, _934, _933, _932, _931, _924, _923, _922, _921, _914, _913, _912, _911}));  // open: sel
  ROM #(.addrWidth(4), .dataWidth(20)) rom_5 (
    .addr(rD),
    .data({D54, D53, D52, D51, D44, D43, D42, D41, D34, D33, D32, D31, D24, D23, D22, D21, D14, D13, D12, D11}));  // open: sel
  ROM #(.addrWidth(4), .dataWidth(20)) rom_6 (
    .addr(r2),
    .data({_254, _253, _252, _251, _244, _243, _242, _241, _234, _233, _232, _231, _224, _223, _222, _221, _214, _213, _212, _211}));  // open: sel
  ROM #(.addrWidth(4), .dataWidth(20)) rom_7 (
    .addr(r6),
    .data({_654, _653, _652, _651, _644, _643, _642, _641, _634, _633, _632, _631, _624, _623, _622, _621, _614, _613, _612, _611}));  // open: sel
  ROM #(.addrWidth(4), .dataWidth(20)) rom_8 (
    .addr(rA),
    .data({A54, A53, A52, A51, A44, A43, A42, A41, A34, A33, A32, A31, A24, A23, A22, A21, A14, A13, A12, A11}));  // open: sel
  ROM #(.addrWidth(4), .dataWidth(20)) rom_9 (
    .addr(rE),
    .data({E54, E53, E52, E51, E44, E43, E42, E41, E34, E33, E32, E31, E24, E23, E22, E21, E14, E13, E12, E11}));  // open: sel
  ROM #(.addrWidth(4), .dataWidth(20)) rom_10 (
    .addr(r3),
    .data({_354, _353, _352, _351, _344, _343, _342, _341, _334, _333, _332, _331, _324, _323, _322, _321, _314, _313, _312, _311}));  // open: sel
  ROM #(.addrWidth(4), .dataWidth(20)) rom_11 (
    .addr(r7),
    .data({_754, _753, _752, _751, _744, _743, _742, _741, _734, _733, _732, _731, _724, _723, _722, _721, _714, _713, _712, _711}));  // open: sel
  ROM #(.addrWidth(4), .dataWidth(20)) rom_12 (
    .addr(rB),
    .data({B54, B53, B52, B51, B44, B43, B42, B41, B34, B33, B32, B31, B24, B23, B22, B21, B14, B13, B12, B11}));  // open: sel
  ROM #(.addrWidth(4), .dataWidth(20)) rom_13 (
    .addr(rF),
    .data({F54, F53, F52, F51, F44, F43, F42, F41, F34, F33, F32, F31, F24, F23, F22, F21, F14, F13, F12, F11}));  // open: sel
  ROM #(.addrWidth(4), .dataWidth(20)) rom_14 (
    .addr(r4),
    .data({_454, _453, _452, _451, _444, _443, _442, _441, _434, _433, _432, _431, _424, _423, _422, _421, _414, _413, _412, _411}));  // open: sel
  ROM #(.addrWidth(4), .dataWidth(20)) rom_15 (
    .addr(r8),
    .data({_854, _853, _852, _851, _844, _843, _842, _841, _834, _833, _832, _831, _824, _823, _822, _821, _814, _813, _812, _811}));  // open: sel
  ROM #(.addrWidth(4), .dataWidth(20)) rom_16 (
    .addr(rC),
    .data({C54, C53, C52, C51, C44, C43, C42, C41, C34, C33, C32, C31, C24, C23, C22, C21, C14, C13, C12, C11}));  // open: sel
  ROM #(.addrWidth(4), .dataWidth(20)) rom_17 (
    .addr(r0),
    .data({_054, _053, _052, _051, _044, _043, _042, _041, _034, _033, _032, _031, _024, _023, _022, _021, _014, _013, _012, _011}));  // open: sel
  and and_13 (LkR2, or_3_out, kR2);
  or or_3 (or_3_out, LEFT, LEFT1);
  and and_14 (LkR6, or_4_out, kR6);
  or or_4 (or_4_out, LEFT, LEFT1);
  and and_15 (LkRA, or_5_out, kRA);
  or or_5 (or_5_out, LEFT, LEFT1);
  and and_16 (LkRE, or_6_out, kRE);
  or or_6 (or_6_out, LEFT, LEFT1);
  and and_17 (LkR3, or_7_out, kR3);
  or or_7 (or_7_out, LEFT, LEFT1);
  and and_18 (LkR7, or_8_out, kR7);
  or or_8 (or_8_out, LEFT, LEFT1);
  and and_19 (LkRB, or_9_out, kRB);
  or or_9 (or_9_out, LEFT, LEFT1);
  and and_20 (LkRF, or_10_out, kRF);
  or or_10 (or_10_out, LEFT, LEFT1);
  Comparator #(.width(4)) comparator_4 (.a(r1), .b(4'b0000), .eq(kR1));  // open: gt, lt
  Comparator #(.width(4)) comparator_5 (.a(r5), .b(4'b0000), .eq(kR5));  // open: gt, lt
  Comparator #(.width(4)) comparator_6 (.a(r9), .b(4'b0000), .eq(kR9));  // open: gt, lt
  Comparator #(.width(4)) comparator_7 (.a(rD), .b(4'b0000), .eq(kRD));  // open: gt, lt
  and and_21 (LkR4, or_11_out, kR4);
  or or_11 (or_11_out, LEFT, LEFT1);
  and and_22 (LkR8, or_12_out, kR8);
  or or_12 (or_12_out, LEFT, LEFT1);
  and and_23 (LkRC, or_13_out, kRC);
  or or_13 (or_13_out, LEFT, LEFT1);
  and and_24 (LkR0, or_14_out, kR0);
  or or_14 (or_14_out, LEFT, LEFT1);
  and and_25 (UpkR5, or_15_out, kR5);
  or or_15 (or_15_out, UP, UP1);
  and and_26 (UpkR9, or_16_out, kR9);
  or or_16 (or_16_out, UP, UP1);
  and and_27 (UpkRD, or_17_out, kRD);
  or or_17 (or_17_out, UP, UP1);
  or or_18 (or_18_out, DOWN, DOWN1);
  or or_19 (or_19_out, DOWN, DOWN1);
  or or_20 (or_20_out, DOWN, DOWN1);
  Comparator #(.width(4)) comparator_8 (.a(r2), .b(4'b0000), .eq(kR2));  // open: gt, lt
  Comparator #(.width(4)) comparator_9 (.a(r6), .b(4'b0000), .eq(kR6));  // open: gt, lt
  Comparator #(.width(4)) comparator_10 (.a(rA), .b(4'b0000), .eq(kRA));  // open: gt, lt
  Comparator #(.width(4)) comparator_11 (.a(rE), .b(4'b0000), .eq(kRE));  // open: gt, lt
  and and_28 (UpkR6, or_21_out, kR6);
  or or_21 (or_21_out, UP, UP1);
  and and_29 (UpkRA, or_22_out, kRA);
  or or_22 (or_22_out, UP, UP1);
  and and_30 (UpkRE, or_23_out, kRE);
  or or_23 (or_23_out, UP, UP1);
  and and_31 (DkR1, or_18_out, kR1);
  or or_24 (or_24_out, DOWN, DOWN1);
  and and_32 (DkR5, or_19_out, kR5);
  or or_25 (or_25_out, DOWN, DOWN1);
  and and_33 (DkR9, or_20_out, kR9);
  or or_26 (or_26_out, DOWN, DOWN1);
  Comparator #(.width(4)) comparator_12 (.a(r3), .b(4'b0000), .eq(kR3));  // open: gt, lt
  Comparator #(.width(4)) comparator_13 (.a(r7), .b(4'b0000), .eq(kR7));  // open: gt, lt
  Comparator #(.width(4)) comparator_14 (.a(rB), .b(4'b0000), .eq(kRB));  // open: gt, lt
  Comparator #(.width(4)) comparator_15 (.a(rF), .b(4'b0000), .eq(kRF));  // open: gt, lt
  and and_34 (UpkR7, or_27_out, kR7);
  or or_27 (or_27_out, UP, UP1);
  and and_35 (UpkRB, or_28_out, kRB);
  or or_28 (or_28_out, UP, UP1);
  and and_36 (UpkRF, or_29_out, kRF);
  or or_29 (or_29_out, UP, UP1);
  and and_37 (DkR2, or_24_out, kR2);
  or or_30 (or_30_out, DOWN, DOWN1);
  and and_38 (DkR6, or_25_out, kR6);
  or or_31 (or_31_out, DOWN, DOWN1);
  and and_39 (DkRA, or_26_out, kRA);
  or or_32 (or_32_out, DOWN, DOWN1);
  and and_40 (UpkR8, or_33_out, kR8);
  or or_33 (or_33_out, UP, UP1);
  and and_41 (UpkRC, or_34_out, kRC);
  or or_34 (or_34_out, UP, UP1);
  and and_42 (UpkR0, or_35_out, kR0);
  or or_35 (or_35_out, UP, UP1);
  and and_43 (DkR3, or_30_out, kR3);
  or or_36 (or_36_out, DOWN, DOWN1);
  and and_44 (DkR7, or_31_out, kR7);
  or or_37 (or_37_out, DOWN, DOWN1);
  and and_45 (DkRB, or_32_out, kRB);
  or or_38 (or_38_out, DOWN, DOWN1);
  Comparator #(.width(4)) comparator_16 (.a(r4), .b(4'b0000), .eq(kR4));  // open: gt, lt
  Comparator #(.width(4)) comparator_17 (.a(r8), .b(4'b0000), .eq(kR8));  // open: gt, lt
  Comparator #(.width(4)) comparator_18 (.a(rC), .b(4'b0000), .eq(kRC));  // open: gt, lt
  Comparator #(.width(4)) comparator_19 (.a(r0), .b(4'b0000), .eq(kR0));  // open: gt, lt
  and and_46 (DkR4, or_36_out, kR4);
  and and_47 (DkR8, or_37_out, kR8);
  and and_48 (DkRC, or_38_out, kRC);
  and and_49 (RkR1, or_39_out, kR1);
  or or_39 (or_39_out, RIGHT, RIGHT1);
  and and_50 (RkR5, or_40_out, kR5);
  or or_40 (or_40_out, RIGHT, RIGHT1);
  and and_51 (RkR9, or_41_out, kR9);
  or or_41 (or_41_out, RIGHT, RIGHT1);
  and and_52 (RkRD, or_42_out, kRD);
  or or_42 (or_42_out, RIGHT, RIGHT1);
  and and_53 (RkR2, or_43_out, kR2);
  or or_43 (or_43_out, RIGHT, RIGHT1);
  and and_54 (RkR6, or_44_out, kR6);
  or or_44 (or_44_out, RIGHT, RIGHT1);
  and and_55 (RkRA, or_45_out, kRA);
  or or_45 (or_45_out, RIGHT, RIGHT1);
  and and_56 (RkRE, or_46_out, kRE);
  or or_46 (or_46_out, RIGHT, RIGHT1);
  and and_57 (RkR3, or_47_out, kR3);
  or or_47 (or_47_out, RIGHT, RIGHT1);
  and and_58 (RkR7, or_48_out, kR7);
  or or_48 (or_48_out, RIGHT, RIGHT1);
  and and_59 (RkRB, or_49_out, kRB);
  or or_49 (or_49_out, RIGHT, RIGHT1);
  and and_60 (RkRF, or_50_out, kRF);
  or or_50 (or_50_out, RIGHT, RIGHT1);
  Multiplexer #(.width(4), .enable("false")) multiplexer_19 (
    .in0(multiplexer_20_out), .in1(r2), .out(r1Res), .sel(RkR1));
  Multiplexer #(.width(4), .enable("false")) multiplexer_20 (
    .in0(r1_r5_2), .in1(r5), .out(multiplexer_20_out), .sel(DkR1));
  Multiplexer #(.width(4), .enable("false")) multiplexer_21 (
    .in0(multiplexer_23_out), .in1(r6), .out(r1_r5), .sel(RkR5));
  Multiplexer #(.width(4), .enable("false")) multiplexer_22 (.in0(r5), .in1(r1), .out(multiplexer_22_out), .sel(UpkR5));
  Multiplexer #(.width(4), .enable("false")) multiplexer_23 (
    .in0(multiplexer_22_out), .in1(r9), .out(multiplexer_23_out), .sel(DkR5));
  Multiplexer #(.width(4), .enable("false")) multiplexer_24 (
    .in0(multiplexer_26_out), .in1(rA), .out(r9_rA_2), .sel(RkR9));
  Multiplexer #(.width(4), .enable("false")) multiplexer_25 (
    .in0(r5_r9), .in1(r5), .out(multiplexer_25_out), .sel(UpkR9));
  Multiplexer #(.width(4), .enable("false")) multiplexer_26 (
    .in0(multiplexer_25_out), .in1(rD), .out(multiplexer_26_out), .sel(DkR9));
  Multiplexer #(.width(4), .enable("false")) multiplexer_27 (
    .in0(multiplexer_28_out), .in1(rE), .out(rD_rE_2), .sel(RkRD));
  Multiplexer #(.width(4), .enable("false")) multiplexer_28 (
    .in0(r9_rD), .in1(r9), .out(multiplexer_28_out), .sel(UpkRD));
  Multiplexer #(.width(4), .enable("false")) multiplexer_29 (.in0(r2), .in1(r1), .out(r1_r2), .sel(RkR1));
  Multiplexer #(.width(4), .enable("false")) multiplexer_30 (.in0(r1_r5), .in1(r1), .out(r1_r6), .sel(DkR1));
  Multiplexer #(.width(4), .enable("false")) multiplexer_31 (.in0(r6), .in1(r5), .out(r2_r5_2), .sel(RkR5));
  Multiplexer #(.width(4), .enable("false")) multiplexer_32 (.in0(r2_r5), .in1(r5), .out(r1_r5_2), .sel(UpkR5));
  Multiplexer #(.width(4), .enable("false")) multiplexer_33 (.in0(r9), .in1(r5), .out(r5_r9), .sel(DkR5));
  Multiplexer #(.width(4), .enable("false")) multiplexer_34 (.in0(r6_r9), .in1(r9), .out(r9_rA), .sel(RkR9));
  Multiplexer #(.width(4), .enable("false")) multiplexer_35 (.in0(r6_r9_2), .in1(r9), .out(r5Res), .sel(UpkR9));
  Multiplexer #(.width(4), .enable("false")) multiplexer_36 (.in0(rD), .in1(r9), .out(r9_rD), .sel(DkR9));
  Multiplexer #(.width(4), .enable("false")) multiplexer_37 (.in0(rA_rD_2), .in1(rD), .out(rD_rE), .sel(RkRD));
  Multiplexer #(.width(4), .enable("false")) multiplexer_38 (.in0(rA_rD), .in1(rD), .out(r9Res), .sel(UpkRD));
  Multiplexer #(.width(4), .enable("false")) multiplexer_39 (
    .in0(multiplexer_41_out), .in1(r3), .out(r2_r3_2), .sel(RkR2));
  Multiplexer #(.width(4), .enable("false")) multiplexer_40 (
    .in0(r1_r2), .in1(r1), .out(multiplexer_40_out), .sel(LkR2));
  Multiplexer #(.width(4), .enable("false")) multiplexer_41 (
    .in0(multiplexer_40_out), .in1(r6), .out(multiplexer_41_out), .sel(DkR2));
  Multiplexer #(.width(4), .enable("false")) multiplexer_42 (
    .in0(multiplexer_44_out), .in1(r7), .out(multiplexer_42_out), .sel(RkR6));
  Multiplexer #(.width(4), .enable("false")) multiplexer_43 (
    .in0(r2_r6), .in1(r5), .out(multiplexer_43_out), .sel(LkR6));
  Multiplexer #(.width(4), .enable("false")) multiplexer_44 (
    .in0(multiplexer_43_out), .in1(rA), .out(multiplexer_44_out), .sel(DkR6));
  Multiplexer #(.width(4), .enable("false")) multiplexer_45 (
    .in0(multiplexer_42_out), .in1(r2), .out(r6_r7_2), .sel(UpkR6));
  Multiplexer #(.width(4), .enable("false")) multiplexer_46 (
    .in0(multiplexer_48_out), .in1(rB), .out(multiplexer_46_out), .sel(RkRA));
  Multiplexer #(.width(4), .enable("false")) multiplexer_47 (
    .in0(r9_rA), .in1(r9), .out(multiplexer_47_out), .sel(LkRA));
  Multiplexer #(.width(4), .enable("false")) multiplexer_48 (
    .in0(multiplexer_47_out), .in1(rE), .out(multiplexer_48_out), .sel(DkRA));
  Multiplexer #(.width(4), .enable("false")) multiplexer_49 (
    .in0(multiplexer_46_out), .in1(r6), .out(rA_rB_2), .sel(UpkRA));
  Multiplexer #(.width(4), .enable("false")) multiplexer_50 (
    .in0(multiplexer_51_out), .in1(rF), .out(multiplexer_50_out), .sel(RkRE));
  Multiplexer #(.width(4), .enable("false")) multiplexer_51 (
    .in0(rD_rE), .in1(rD), .out(multiplexer_51_out), .sel(LkRE));
  Multiplexer #(.width(4), .enable("false")) multiplexer_52 (
    .in0(multiplexer_50_out), .in1(rA), .out(rE_rF_2), .sel(UpkRE));
  Multiplexer #(.width(4), .enable("false")) multiplexer_53 (.in0(r2_r4), .in1(r2), .out(r2_r3), .sel(RkR2));
  Multiplexer #(.width(4), .enable("false")) multiplexer_54 (.in0(r1), .in1(r2), .out(r2_r5), .sel(LkR2));
  Multiplexer #(.width(4), .enable("false")) multiplexer_55 (.in0(r2_r5_2), .in1(r2), .out(r2_r6), .sel(DkR2));
  Multiplexer #(.width(4), .enable("false")) multiplexer_56 (.in0(r3_r6_2), .in1(r6), .out(r6_r7), .sel(RkR6));
  Multiplexer #(.width(4), .enable("false")) multiplexer_57 (.in0(r1_r6), .in1(r6), .out(r6_r9_2), .sel(LkR6));
  Multiplexer #(.width(4), .enable("false")) multiplexer_58 (.in0(rA), .in1(r6), .out(r6_r9), .sel(DkR6));
  Multiplexer #(.width(4), .enable("false")) multiplexer_59 (.in0(r3_r6), .in1(r6), .out(r2Res), .sel(UpkR6));
  Multiplexer #(.width(4), .enable("false")) multiplexer_60 (.in0(r7_rA), .in1(rA), .out(rA_rB), .sel(RkRA));
  Multiplexer #(.width(4), .enable("false")) multiplexer_61 (.in0(r9_rA_2), .in1(rA), .out(rA_rD), .sel(LkRA));
  Multiplexer #(.width(4), .enable("false")) multiplexer_62 (.in0(rE), .in1(rA), .out(rA_rD_2), .sel(DkRA));
  Multiplexer #(.width(4), .enable("false")) multiplexer_63 (.in0(r7_rA_2), .in1(rA), .out(r6Res), .sel(UpkRA));
  Multiplexer #(.width(4), .enable("false")) multiplexer_64 (.in0(rB_rE), .in1(rE), .out(rE_rF), .sel(RkRE));
  Multiplexer #(.width(4), .enable("false")) multiplexer_65 (.in0(rD_rE_2), .in1(rE), .out(rDRes), .sel(LkRE));
  Multiplexer #(.width(4), .enable("false")) multiplexer_66 (.in0(rB_rE_2), .in1(rE), .out(rARes), .sel(UpkRE));
  Multiplexer #(.width(4), .enable("false")) multiplexer_67 (
    .in0(multiplexer_69_out), .in1(r4), .out(r3_r7), .sel(RkR3));
  Multiplexer #(.width(4), .enable("false")) multiplexer_68 (
    .in0(r2_r3), .in1(r2), .out(multiplexer_68_out), .sel(LkR3));
  Multiplexer #(.width(4), .enable("false")) multiplexer_69 (
    .in0(multiplexer_68_out), .in1(r7), .out(multiplexer_69_out), .sel(DkR3));
  Multiplexer #(.width(4), .enable("false")) multiplexer_70 (
    .in0(multiplexer_72_out), .in1(r8), .out(multiplexer_70_out), .sel(RkR7));
  Multiplexer #(.width(4), .enable("false")) multiplexer_71 (
    .in0(r6_r7), .in1(r6), .out(multiplexer_71_out), .sel(LkR7));
  Multiplexer #(.width(4), .enable("false")) multiplexer_72 (
    .in0(multiplexer_71_out), .in1(rB), .out(multiplexer_72_out), .sel(DkR7));
  Multiplexer #(.width(4), .enable("false")) multiplexer_73 (
    .in0(multiplexer_70_out), .in1(r3), .out(r7_r8), .sel(UpkR7));
  Multiplexer #(.width(4), .enable("false")) multiplexer_74 (
    .in0(multiplexer_76_out), .in1(rC), .out(multiplexer_74_out), .sel(RkRB));
  Multiplexer #(.width(4), .enable("false")) multiplexer_75 (
    .in0(rA_rB), .in1(rA), .out(multiplexer_75_out), .sel(LkRB));
  Multiplexer #(.width(4), .enable("false")) multiplexer_76 (
    .in0(multiplexer_75_out), .in1(rF), .out(multiplexer_76_out), .sel(DkRB));
  Multiplexer #(.width(4), .enable("false")) multiplexer_77 (
    .in0(multiplexer_74_out), .in1(r7), .out(rB_rC_2), .sel(UpkRB));
  Multiplexer #(.width(4), .enable("false")) multiplexer_78 (
    .in0(multiplexer_79_out), .in1(r0), .out(multiplexer_78_out), .sel(RkRF));
  Multiplexer #(.width(4), .enable("false")) multiplexer_79 (
    .in0(rE_rF), .in1(rE), .out(multiplexer_79_out), .sel(LkRF));
  Multiplexer #(.width(4), .enable("false")) multiplexer_80 (
    .in0(multiplexer_78_out), .in1(rB), .out(rF_r0), .sel(UpkRF));
  Multiplexer #(.width(4), .enable("false")) multiplexer_81 (.in0(r4_r3), .in1(r3), .out(r3_r8), .sel(RkR3));
  Multiplexer #(.width(4), .enable("false")) multiplexer_82 (.in0(r2_r3_2), .in1(r3), .out(r3_r6), .sel(LkR3));
  Multiplexer #(.width(4), .enable("false")) multiplexer_83 (.in0(r7), .in1(r3), .out(r3_r6_2), .sel(DkR3));
  Multiplexer #(.width(4), .enable("false")) multiplexer_84 (.in0(r4_r7), .in1(r7), .out(r7_r8_2), .sel(RkR7));
  Multiplexer #(.width(4), .enable("false")) multiplexer_85 (.in0(r6_r7_2), .in1(r7), .out(r7_rA_2), .sel(LkR7));
  Multiplexer #(.width(4), .enable("false")) multiplexer_86 (.in0(rB), .in1(r7), .out(r7_rA), .sel(DkR7));
  Multiplexer #(.width(4), .enable("false")) multiplexer_87 (.in0(r3_r7), .in1(r7), .out(r3Res), .sel(UpkR7));
  Multiplexer #(.width(4), .enable("false")) multiplexer_88 (.in0(r8_rB), .in1(rB), .out(rB_rC), .sel(RkRB));
  Multiplexer #(.width(4), .enable("false")) multiplexer_89 (.in0(rA_rB_2), .in1(rB), .out(rB_rE_2), .sel(LkRB));
  Multiplexer #(.width(4), .enable("false")) multiplexer_90 (.in0(rF), .in1(rB), .out(rB_rE), .sel(DkRB));
  Multiplexer #(.width(4), .enable("false")) multiplexer_91 (.in0(r8_rB_2), .in1(rB), .out(r7Res), .sel(UpkRB));
  Multiplexer #(.width(4), .enable("false")) multiplexer_92 (.in0(rC_rF_2), .in1(rF), .out(rF_r0_2), .sel(RkRF));
  Multiplexer #(.width(4), .enable("false")) multiplexer_93 (.in0(rE_rF_2), .in1(rF), .out(rERes), .sel(LkRF));
  Multiplexer #(.width(4), .enable("false")) multiplexer_94 (.in0(rC_rF), .in1(rF), .out(rBRes), .sel(UpkRF));
  Multiplexer #(.width(4), .enable("false")) multiplexer_95 (
    .in0(multiplexer_96_out), .in1(r3), .out(r4_r3), .sel(LkR4));
  Multiplexer #(.width(4), .enable("false")) multiplexer_96 (.in0(r4), .in1(r8), .out(multiplexer_96_out), .sel(DkR4));
  Multiplexer #(.width(4), .enable("false")) multiplexer_97 (
    .in0(multiplexer_99_out), .in1(r7), .out(r8_rC), .sel(LkR8));
  Multiplexer #(.width(4), .enable("false")) multiplexer_98 (
    .in0(r7_r8_2), .in1(r4), .out(multiplexer_98_out), .sel(UpkR8));
  Multiplexer #(.width(4), .enable("false")) multiplexer_99 (
    .in0(multiplexer_98_out), .in1(rC), .out(multiplexer_99_out), .sel(DkR8));
  Multiplexer #(.width(4), .enable("false")) multiplexer_100 (
    .in0(multiplexer_102_out), .in1(rB), .out(rC_r0), .sel(LkRC));
  Multiplexer #(.width(4), .enable("false")) multiplexer_101 (
    .in0(rB_rC), .in1(r8), .out(multiplexer_101_out), .sel(UpkRC));
  Multiplexer #(.width(4), .enable("false")) multiplexer_102 (
    .in0(multiplexer_101_out), .in1(r0), .out(multiplexer_102_out), .sel(DkRC));
  Multiplexer #(.width(4), .enable("false")) multiplexer_103 (
    .in0(multiplexer_104_out), .in1(rF), .out(r0Res), .sel(LkR0));
  Multiplexer #(.width(4), .enable("false")) multiplexer_104 (
    .in0(rF_r0_2), .in1(rC), .out(multiplexer_104_out), .sel(UpkR0));
  Multiplexer #(.width(4), .enable("false")) multiplexer_105 (.in0(r3), .in1(r4), .out(r2_r4), .sel(LkR4));
  Multiplexer #(.width(4), .enable("false")) multiplexer_106 (.in0(r8), .in1(r4), .out(r4_r7), .sel(DkR4));
  Multiplexer #(.width(4), .enable("false")) multiplexer_107 (.in0(r7_r8), .in1(r8), .out(r8_rB_2), .sel(LkR8));
  Multiplexer #(.width(4), .enable("false")) multiplexer_108 (.in0(r3_r8), .in1(r8), .out(r4Res), .sel(UpkR8));
  Multiplexer #(.width(4), .enable("false")) multiplexer_109 (.in0(rC), .in1(r8), .out(r8_rB), .sel(DkR8));
  Multiplexer #(.width(4), .enable("false")) multiplexer_110 (.in0(rB_rC_2), .in1(rC), .out(rC_rF), .sel(LkRC));
  Multiplexer #(.width(4), .enable("false")) multiplexer_111 (.in0(r8_rC), .in1(rC), .out(r8Res), .sel(UpkRC));
  Multiplexer #(.width(4), .enable("false")) multiplexer_112 (.in0(r0), .in1(rC), .out(rC_rF_2), .sel(DkRC));
  Multiplexer #(.width(4), .enable("false")) multiplexer_113 (.in0(rF_r0), .in1(r0), .out(rFRes), .sel(LkR0));
  Multiplexer #(.width(4), .enable("false")) multiplexer_114 (.in0(rC_r0), .in1(r0), .out(rCRes), .sel(UpkR0));
  LED led_341 ();  // open: in

  // Notes on the sheet:
  //   contents of rom_1 (hex, n*v repeats v):
  //   d3 f2 d0 0 ac d0 1 d1 1 d3 f0 ac d3 f1 be 79 e1 2d 8c 8d d3 10 77 e1 9 d0 0 d3 f0 ac d3 f1 be d1 0
  //   79 e1 2d d0 1 d3 f2 ac ee 0 d0 0 d3 f2 ac ee
  //   contents of rom_2 (hex, n*v repeats v):
  //   0 f4564 f1f8f f8f8f 88f99 f8f1f f9f1f 1248f f9f9f f8f9f 99f9f f9f11 f111f f9f88 f1f1f 11f1f
  //   contents of rom_3 (hex, n*v repeats v):
  //   0 f4564 f1f8f f8f8f 88f99 f8f1f f9f1f 1248f f9f9f f8f9f 99f9f f9f11 f111f f9f88 f1f1f 11f1f
  //   contents of rom_4 (hex, n*v repeats v):
  //   0 f4564 f1f8f f8f8f 88f99 f8f1f f9f1f 1248f f9f9f f8f9f 99f9f f9f11 f111f f9f88 f1f1f 11f1f
  //   contents of rom_5 (hex, n*v repeats v):
  //   0 f4564 f1f8f f8f8f 88f99 f8f1f f9f1f 1248f f9f9f f8f9f 99f9f f9f11 f111f f9f88 f1f1f 11f1f
  //   contents of rom_6 (hex, n*v repeats v):
  //   0 f4564 f1f8f f8f8f 88f99 f8f1f f9f1f 1248f f9f9f f8f9f 99f9f f9f11 f111f f9f88 f1f1f 11f1f
  //   contents of rom_7 (hex, n*v repeats v):
  //   0 f4564 f1f8f f8f8f 88f99 f8f1f f9f1f 1248f f9f9f f8f9f 99f9f f9f11 f111f f9f88 f1f1f 11f1f
  //   contents of rom_8 (hex, n*v repeats v):
  //   0 f4564 f1f8f f8f8f 88f99 f8f1f f9f1f 1248f f9f9f f8f9f 99f9f f9f11 f111f f9f88 f1f1f 11f1f
  //   contents of rom_9 (hex, n*v repeats v):
  //   0 f4564 f1f8f f8f8f 88f99 f8f1f f9f1f 1248f f9f9f f8f9f 99f9f f9f11 f111f f9f88 f1f1f 11f1f
  //   contents of rom_10 (hex, n*v repeats v):
  //   0 f4564 f1f8f f8f8f 88f99 f8f1f f9f1f 1248f f9f9f f8f9f 99f9f f9f11 f111f f9f88 f1f1f 11f1f
  //   contents of rom_11 (hex, n*v repeats v):
  //   0 f4564 f1f8f f8f8f 88f99 f8f1f f9f1f 1248f f9f9f f8f9f 99f9f f9f11 f111f f9f88 f1f1f 11f1f
  //   contents of rom_12 (hex, n*v repeats v):
  //   0 f4564 f1f8f f8f8f 88f99 f8f1f f9f1f 1248f f9f9f f8f9f 99f9f f9f11 f111f f9f88 f1f1f 11f1f
  //   contents of rom_13 (hex, n*v repeats v):
  //   0 f4564 f1f8f f8f8f 88f99 f8f1f f9f1f 1248f f9f9f f8f9f 99f9f f9f11 f111f f9f88 f1f1f 11f1f
  //   contents of rom_14 (hex, n*v repeats v):
  //   0 f4564 f1f8f f8f8f 88f99 f8f1f f9f1f 1248f f9f9f f8f9f 99f9f f9f11 f111f f9f88 f1f1f 11f1f
  //   contents of rom_15 (hex, n*v repeats v):
  //   0 f4564 f1f8f f8f8f 88f99 f8f1f f9f1f 1248f f9f9f f8f9f 99f9f f9f11 f111f f9f88 f1f1f 11f1f
  //   contents of rom_16 (hex, n*v repeats v):
  //   0 f4564 f1f8f f8f8f 88f99 f8f1f f9f1f 1248f f9f9f f8f9f 99f9f f9f11 f111f f9f88 f1f1f 11f1f
  //   contents of rom_17 (hex, n*v repeats v):
  //   0 f4564 f1f8f f8f8f 88f99 f8f1f f9f1f 1248f f9f9f f8f9f 99f9f f9f11 f111f f9f88 f1f1f 11f1f
  //   LEFT
  //   UP
  //   DOWN
  //   RIGHT
endmodule

module Digit (
  input  [3:0] in_1
);

  wire _12345;
  wire [19:0] rom_1_data;

  ROM #(.addrWidth(4), .dataWidth(20)) rom_1 (
    .addr(in_1), .data({rom_1_data[19:4], _12345, rom_1_data[2:0]}));  // open: sel
  LED led_1 (.in(rom_1_data[0]));
  LED led_2 (.in(rom_1_data[1]));
  LED led_3 (.in(rom_1_data[4]));
  LED led_4 (.in(rom_1_data[5]));
  LED led_5 (.in(rom_1_data[9]));
  LED led_6 (.in(rom_1_data[8]));
  LED led_7 (.in(rom_1_data[13]));
  LED led_8 (.in(rom_1_data[12]));
  LED led_9 (.in(rom_1_data[16]));
  LED led_10 (.in(rom_1_data[17]));
  LED led_11 (.in(rom_1_data[2]));
  LED led_12 (.in(rom_1_data[7]));
  LED led_13 (.in(rom_1_data[6]));
  LED led_14 (.in(rom_1_data[10]));
  LED led_15 (.in(rom_1_data[11]));
  LED led_16 (.in(rom_1_data[14]));
  LED led_17 (.in(rom_1_data[15]));
  LED led_18 (.in(rom_1_data[18]));
  LED led_19 (.in(rom_1_data[19]));

  // Notes on the sheet:
  //   contents of rom_1 (hex, n*v repeats v):
  //   f999f f4564 f1f8f f8f8f 88f99 f8f1f f9f1f 1248f f9f9f f8f9f 99f9f f9f11 f111f f9f88 f1f1f 11f1f
endmodule
