// Logisim project 15puzzleV1_08.circ as structural Verilog: 6 circuits, main circuit main
module main (
);

  wire ad, add, adF1, adW, clock_3_out, D, D_B, DkR1, DkR2, DkR3, DkR4, DkR5, DkR6, DkR7, DkR8, DkR9, DkRA,
       DkRB, DkRC, DOWN, DOWN1, en, enF1, enW, init, kR0, kR1, kR2, kR3, kR4, kR5, kR6, kR7, kR8, kR9, kRA,
       kRB, kRC, kRD, kRE, kRF, L, L_B, LEFT, LEFT1, LkR0, LkR2, LkR3, LkR4, LkR6, LkR7, LkR8, LkRA, LkRB,
       LkRC, LkRE, LkRF, memory, not_1_out, not_2_out, not_3_out, or_1_out, or_2_out, or_3_out, or_4_out,
       or_5_out, or_6_out, or_7_out, or_8_out, or_9_out, or_10_out, or_11_out, or_12_out, or_13_out,
       or_14_out, or_15_out, or_16_out, or_17_out, or_18_out, or_19_out, or_20_out, or_21_out, or_22_out,
       or_23_out, or_24_out, or_25_out, or_26_out, or_27_out, or_28_out, or_29_out, or_30_out, or_31_out,
       or_32_out, or_33_out, or_34_out, or_35_out, or_36_out, or_37_out, or_38_out, or_39_out, or_40_out,
       or_41_out, or_42_out, or_43_out, or_44_out, or_45_out, or_46_out, or_47_out, or_48_out, or_49_out,
       or_50_out, R, R_B, read_write, Reset, RIGHT, RIGHT1, RkR1, RkR2, RkR3, RkR5, RkR6, RkR7, RkR9, RkRA,
       RkRB, RkRD, RkRE, RkRF, Swap, T, Tcdm8, TWin, U, U_B, undriven, undriven_2, undriven_3, undriven_4,
       undriven_5, undriven_6, UP, UP1, UpkR0, UpkR5, UpkR6, UpkR7, UpkR8, UpkR9, UpkRA, UpkRB, UpkRC, UpkRD,
       UpkRE, UpkRF, Win;
  wire [1:0] random_1_out;
  wire [3:0] multiplexer_1_out, multiplexer_2_out, multiplexer_3_out, multiplexer_4_out, multiplexer_11_out,
       multiplexer_12_out, multiplexer_13_out, multiplexer_14_out, multiplexer_22_out, multiplexer_23_out,
       multiplexer_24_out, multiplexer_25_out, multiplexer_29_out, multiplexer_30_out, multiplexer_31_out,
       multiplexer_32_out, multiplexer_34_out, multiplexer_36_out, multiplexer_38_out, multiplexer_39_out,
       multiplexer_41_out, multiplexer_42_out, multiplexer_44_out, multiplexer_56_out, multiplexer_57_out,
       multiplexer_58_out, multiplexer_59_out, multiplexer_60_out, multiplexer_62_out, multiplexer_63_out,
       multiplexer_64_out, multiplexer_66_out, multiplexer_67_out, multiplexer_84_out, multiplexer_85_out,
       multiplexer_86_out, multiplexer_87_out, multiplexer_88_out, multiplexer_90_out, multiplexer_91_out,
       multiplexer_92_out, multiplexer_94_out, multiplexer_95_out, multiplexer_112_out, multiplexer_114_out,
       multiplexer_115_out, multiplexer_117_out, multiplexer_118_out, multiplexer_120_out, r0, r0Res, r1,
       r1_r2, r1_r5, r1_r5_2, r1_r6, r1Res, r2, r2_r3, r2_r3_2, r2_r4, r2_r5, r2_r5_2, r2_r6, r2Res, r3,
       r3_r6, r3_r6_2, r3_r7, r3_r8, r3Res, r4, r4_r3, r4_r7, r4Res, r5, r5_r9, r5Res, r6, r6_r7, r6_r7_2,
       r6_r9, r6_r9_2, r6Res, r7, r7_r8, r7_r8_2, r7_rA, r7_rA_2, r7Res, r8, r8_rB, r8_rB_2, r8_rC, r8Res,
       r9, r9_rA, r9_rA_2, r9_rD, r9Res, rA, rA_rB, rA_rB_2, rA_rD, rA_rD_2, rARes, rB, rB_rC, rB_rC_2,
       rB_rE, rB_rE_2, rBRes, rC, rC_r0, rC_rF, rC_rF_2, rCRes, rD, rD_rE, rD_rE_2, rDRes, rE, rE_rF,
       rE_rF_2, register_18_q, rERes, rF, rF_r0, rF_r0_2, rFRes;
  wire [6:0] Keyboard;
  wire [7:0] addr, cdm_8_mark5_1_r0, cdm_8_mark5_1_r1, cdm_8_mark5_1_r2, cdm_8_mark5_1_r3, CELL_BYTE, data,
       i1, i2, i3, i4, i5, multiplexer_15_out, multiplexer_33_out, n1, n2, n3, n4, n5, out, RAM, w1, w2, w3,
       w4, w5;
  wire [7:1] register_17_q;
  wire [9:0] _01, _02, _03, _04, _05, _06, _07, _08, _11, _12, _13, _14, _15, _16, _17, _18, _21, _22, _23,
       _24, _25, _26, _27, _28, _31, _32, _33, _34, _35, _36, _37, _38, _41, _42, _43, _44, _45, _46, _47,
       _48, _51, _52, _53, _54, _55, _56, _57, _58, _61, _62, _63, _64, _65, _66, _67, _68, _71, _72, _73,
       _74, _75, _76, _77, _78, _81, _82, _83, _84, _85, _86, _87, _88, _91, _92, _93, _94, _95, _96, _97,
       _98, A1, A2, A3, A4, A5, A6, A7, A8, B1, B2, B3, B4, B5, B6, B7, B8, C1, C2, C3, C4, C5, C6, C7, C8,
       D1, D2, D3, D4, D5, D6, D7, D8, E1, E2, E3, E4, E5, E6, E7, E8, F1, F2, F3, F4, F5, F6, F7, F8;

  TTY #(.rows(3), .cols(54)) tty_1 ();  // open: data, clk, we, clr
  TTY #(.rows(3), .cols(54)) tty_2 ();  // open: data, clk, we, clr
  TTY #(.rows(3), .cols(54)) tty_3 ();  // open: data, clk, we, clr
  TTY #(.rows(3), .cols(54)) tty_4 ();  // open: data, clk, we, clr
  DotMatrix #(.matrixcols(8), .matrixrows(10)) dotmatrix_1 (
    .col0(_12), .col1(_11), .col2(_14), .col3(_13), .col4(_16), .col5(_15), .col6(_18), .col7(_17));
  DotMatrix #(.matrixcols(8), .matrixrows(10)) dotmatrix_2 (
    .col0(_52), .col1(_51), .col2(_54), .col3(_53), .col4(_56), .col5(_55), .col6(_58), .col7(_57));
  DotMatrix #(.matrixcols(8), .matrixrows(10)) dotmatrix_3 (
    .col0(_92), .col1(_91), .col2(_94), .col3(_93), .col4(_96), .col5(_95), .col6(_98), .col7(_97));
  DotMatrix #(.matrixcols(8), .matrixrows(10)) dotmatrix_4 (
    .col0(D2), .col1(D1), .col2(D4), .col3(D3), .col4(D6), .col5(D5), .col6(D8), .col7(D7));
  Multiplexer #(.width(4), .enable("false")) multiplexer_1 (
    .in0(r1Res), .in1(4'b0001), .out(multiplexer_1_out), .sel(init));
  Register #(.width(4)) register_1 (.D(multiplexer_1_out), .Q(r1), .clk(T));  // open: en, clr
  Multiplexer #(.width(4), .enable("false")) multiplexer_2 (
    .in0(r5Res), .in1(4'b0101), .out(multiplexer_2_out), .sel(init));
  Register #(.width(4)) register_2 (.D(multiplexer_2_out), .Q(r5), .clk(T));  // open: en, clr
  Multiplexer #(.width(4), .enable("false")) multiplexer_3 (
    .in0(r9Res), .in1(4'b1001), .out(multiplexer_3_out), .sel(init));
  Register #(.width(4)) register_3 (.D(multiplexer_3_out), .Q(r9), .clk(T));  // open: en, clr
  Multiplexer #(.width(4), .enable("false")) multiplexer_4 (
    .in0(rDRes), .in1(4'b1101), .out(multiplexer_4_out), .sel(init));
  Register #(.width(4)) register_4 (.D(multiplexer_4_out), .Q(rD), .clk(T));  // open: en, clr
  // Probe on cdm_8_mark5_1_r0
  and and_1 (en, memory, add, not_1_out);
  not not_1 (not_1_out, read_write);
  Comparator comparator_1 (.a(addr), .b(8'hf0), .eq(ad));  // open: gt, lt
  Multiplexer #(.width(8), .enable("false")) multiplexer_5 (.in0({8{1'b0}}), .in1({8{1'b1}}), .out(w1), .sel(Win));
  Multiplexer #(.width(8), .enable("false")) multiplexer_6 (.in0({8{1'b0}}), .in1(8'h81), .out(i1), .sel(Win));
  Multiplexer #(.width(8), .enable("false")) multiplexer_7 (.in0({8{1'b0}}), .in1({8{1'b1}}), .out(n1), .sel(Win));
  LED led_1 ();  // open: in
  LED led_2 ();  // open: in
  LED led_3 ();  // open: in
  LED led_4 (.in(undriven_2));
  LED led_5 ();  // open: in
  LED led_6 ();  // open: in
  LED led_7 (.in(undriven_3));
  LED led_8 ();  // open: in
  LED led_9 (.in(undriven));
  LED led_10 ();  // open: in
  LED led_11 ();  // open: in
  LED led_12 ();  // open: in
  DotMatrix #(.matrixcols(8), .matrixrows(10)) dotmatrix_5 (
    .col0(_22), .col1(_21), .col2(_24), .col3(_23), .col4(_26), .col5(_25), .col6(_28), .col7(_27));
  DotMatrix #(.matrixcols(8), .matrixrows(10)) dotmatrix_6 (
    .col0(_62), .col1(_61), .col2(_64), .col3(_63), .col4(_66), .col5(_65), .col6(_68), .col7(_67));
  DotMatrix #(.matrixcols(8), .matrixrows(10)) dotmatrix_7 (
    .col0(A2), .col1(A1), .col2(A4), .col3(A3), .col4(A6), .col5(A5), .col6(A8), .col7(A7));
  DotMatrix #(.matrixcols(8), .matrixrows(10)) dotmatrix_8 (
    .col0(E2), .col1(E1), .col2(E4), .col3(E3), .col4(E6), .col5(E5), .col6(E8), .col7(E7));
  // Probe on cdm_8_mark5_1_r1
  // Probe on cdm_8_mark5_1_r2
  // Probe on cdm_8_mark5_1_r3
  ROM rom_1 (.addr(addr), .data(data));  // open: sel
  Multiplexer #(.width(8), .enable("false")) multiplexer_8 (.in0({8{1'b0}}), .in1(8'h2), .out(w2), .sel(Win));
  Multiplexer #(.width(8), .enable("false")) multiplexer_9 (.in0({8{1'b0}}), .in1(8'h81), .out(i2), .sel(Win));
  Multiplexer #(.width(8), .enable("false")) multiplexer_10 (.in0({8{1'b0}}), .in1(8'h60), .out(n2), .sel(Win));
  LED led_13 ();  // open: in
  LED led_14 ();  // open: in
  LED led_15 (.in(undriven_4));
  LED led_16 (.in(undriven_5));
  LED led_17 ();  // open: in
  LED led_18 ();  // open: in
  LED led_19 (.in(undriven_6));
  LED led_20 ();  // open: in
  DotMatrix #(.matrixcols(8), .matrixrows(10)) dotmatrix_9 (
    .col0(_32), .col1(_31), .col2(_34), .col3(_33), .col4(_36), .col5(_35), .col6(_38), .col7(_37));
  DotMatrix #(.matrixcols(8), .matrixrows(10)) dotmatrix_10 (
    .col0(_72), .col1(_71), .col2(_74), .col3(_73), .col4(_76), .col5(_75), .col6(_78), .col7(_77));
  DotMatrix #(.matrixcols(8), .matrixrows(10)) dotmatrix_11 (
    .col0(B2), .col1(B1), .col2(B4), .col3(B3), .col4(B6), .col5(B5), .col6(B8), .col7(B7));
  DotMatrix #(.matrixcols(8), .matrixrows(10)) dotmatrix_12 (
    .col0(F2), .col1(F1), .col2(F4), .col3(F3), .col4(F6), .col5(F5), .col6(F8), .col7(F7));
  Register #(.width(4)) register_5 (.D(multiplexer_11_out), .Q(r2), .clk(T));  // open: en, clr
  Multiplexer #(.width(4), .enable("false")) multiplexer_11 (
    .in0(r2Res), .in1(4'b0010), .out(multiplexer_11_out), .sel(init));
  Multiplexer #(.width(4), .enable("false")) multiplexer_12 (
    .in0(r6Res), .in1(4'b0110), .out(multiplexer_12_out), .sel(init));
  Register #(.width(4)) register_6 (.D(multiplexer_12_out), .Q(r6), .clk(T));  // open: en, clr
  Multiplexer #(.width(4), .enable("false")) multiplexer_13 (
    .in0(rARes), .in1(4'b1010), .out(multiplexer_13_out), .sel(init));
  Register #(.width(4)) register_7 (.D(multiplexer_13_out), .Q(rA), .clk(T));  // open: en, clr
  Register #(.width(4)) register_8 (.D(multiplexer_14_out), .Q(rE), .clk(T));  // open: en, clr
  Multiplexer #(.width(4), .enable("false")) multiplexer_14 (
    .in0(rERes), .in1(4'b1110), .out(multiplexer_14_out), .sel(init));
  CdM_8_mark5 cdm_8_mark5_1 (
    .clock(Tcdm8), .addr(addr), .mem_read(read_write), .mem_cycle(memory), .data_out(out),
    .data_in(multiplexer_15_out), .r0(cdm_8_mark5_1_r0), .r1(cdm_8_mark5_1_r1), .r2(cdm_8_mark5_1_r2),
    .r3(cdm_8_mark5_1_r3));  // open: data_inst, PC, SP, PS, IAck, IRQ, vec
  Multiplexer #(.width(8), .enable("false")) multiplexer_15 (
    .in0(data), .in1(CELL_BYTE), .out(multiplexer_15_out), .sel(enF1));
  and and_2 (enF1, memory, adF1, read_write);
  Comparator comparator_2 (.a(addr), .b(8'hf1), .eq(adF1));  // open: gt, lt
  Multiplexer #(.width(8), .enable("false")) multiplexer_16 (.in0({8{1'b0}}), .in1(8'h1c), .out(w3), .sel(Win));
  Multiplexer #(.width(8), .enable("false")) multiplexer_17 (.in0({8{1'b0}}), .in1({8{1'b1}}), .out(i3), .sel(Win));
  Multiplexer #(.width(8), .enable("false")) multiplexer_18 (.in0({8{1'b0}}), .in1(8'h18), .out(n3), .sel(Win));
  DotMatrix #(.matrixcols(8), .matrixrows(10)) dotmatrix_13 (
    .col0(_42), .col1(_41), .col2(_44), .col3(_43), .col4(_46), .col5(_45), .col6(_48), .col7(_47));
  DotMatrix #(.matrixcols(8), .matrixrows(10)) dotmatrix_14 (
    .col0(_82), .col1(_81), .col2(_84), .col3(_83), .col4(_86), .col5(_85), .col6(_88), .col7(_87));
  DotMatrix #(.matrixcols(8), .matrixrows(10)) dotmatrix_15 (
    .col0(C2), .col1(C1), .col2(C4), .col3(C3), .col4(C6), .col5(C5), .col6(C8), .col7(C7));
  DotMatrix #(.matrixcols(8), .matrixrows(10)) dotmatrix_16 (
    .col0(_02), .col1(_01), .col2(_04), .col3(_03), .col4(_06), .col5(_05), .col6(_08), .col7(_07));
  Multiplexer #(.width(8), .enable("false")) multiplexer_19 (.in0({8{1'b0}}), .in1(8'h2), .out(w4), .sel(Win));
  Multiplexer #(.width(8), .enable("false")) multiplexer_20 (.in0({8{1'b0}}), .in1(8'h81), .out(i4), .sel(Win));
  Multiplexer #(.width(8), .enable("false")) multiplexer_21 (.in0({8{1'b0}}), .in1(8'h6), .out(n4), .sel(Win));
  Register #(.width(4)) register_9 (.D(multiplexer_22_out), .Q(r3), .clk(T));  // open: en, clr
  Multiplexer #(.width(4), .enable("false")) multiplexer_22 (
    .in0(r3Res), .in1(4'b0011), .out(multiplexer_22_out), .sel(init));
  Register #(.width(4)) register_10 (.D(multiplexer_23_out), .Q(r7), .clk(T));  // open: en, clr
  Multiplexer #(.width(4), .enable("false")) multiplexer_23 (
    .in0(r7Res), .in1(4'b0111), .out(multiplexer_23_out), .sel(init));
  Multiplexer #(.width(4), .enable("false")) multiplexer_24 (
    .in0(rBRes), .in1(4'b1011), .out(multiplexer_24_out), .sel(init));
  Register #(.width(4)) register_11 (.D(multiplexer_24_out), .Q(rB), .clk(T));  // open: en, clr
  Multiplexer #(.width(4), .enable("false")) multiplexer_25 (
    .in0(rFRes), .in1(4'b1111), .out(multiplexer_25_out), .sel(init));
  Register #(.width(4)) register_12 (.D(multiplexer_25_out), .Q(rF), .clk(T));  // open: en, clr
  and and_3 (enW, memory, adW, not_2_out);
  not not_2 (not_2_out, read_write);
  Comparator comparator_3 (.a(addr), .b(8'hf2), .eq(adW));  // open: gt, lt
  Multiplexer #(.width(8), .enable("false")) multiplexer_26 (.in0({8{1'b0}}), .in1({8{1'b1}}), .out(w5), .sel(Win));
  Multiplexer #(.width(8), .enable("false")) multiplexer_27 (.in0({8{1'b0}}), .in1(8'h81), .out(i5), .sel(Win));
  Multiplexer #(.width(8), .enable("false")) multiplexer_28 (.in0({8{1'b0}}), .in1({8{1'b1}}), .out(n5), .sel(Win));
  DotMatrix #(.matrixcols(17), .matrixrows(8)) dotmatrix_17 (
    .col0(w1), .col1(w2), .col2(w3), .col3(w4), .col4(w5), .col5({8{1'b0}}), .col6(i1), .col7(i2), .col8(i3),
    .col9(i4), .col10(i5), .col11({8{1'b0}}), .col12(n1), .col13(n2), .col14(n3), .col15(n4), .col16(n5));
  Button button (.out(U_B));
  Button button_2 (.out(L_B));
  Button button_3 (.out(R_B));
  Button button_4 (.out(D_B));
  Keyboard #(.buflen(1)) keyboard_1 (.clk(T), .data(Keyboard));  // open: re, clr, avail
  RAM ram_1 (.addr(addr), .data(RAM), .sel(memory), .clk(Tcdm8), .ld(read_write), .clr(Reset));
  Button button_5 (.out(Reset));
  Button button_6 (.out(Swap));
  Register #(.width(4)) register_13 (.D(multiplexer_29_out), .Q(r4), .clk(T));  // open: en, clr
  Multiplexer #(.width(4), .enable("false")) multiplexer_29 (
    .in0(r4Res), .in1(4'b0100), .out(multiplexer_29_out), .sel(init));
  Multiplexer #(.width(4), .enable("false")) multiplexer_30 (
    .in0(r8Res), .in1(4'b1000), .out(multiplexer_30_out), .sel(init));
  Register #(.width(4)) register_14 (.D(multiplexer_30_out), .Q(r8), .clk(T));  // open: en, clr
  Multiplexer #(.width(4), .enable("false")) multiplexer_31 (
    .in0(rCRes), .in1(4'b1100), .out(multiplexer_31_out), .sel(init));
  Register #(.width(4)) register_15 (.D(multiplexer_31_out), .Q(rC), .clk(T));  // open: en, clr
  Register #(.width(4)) register_16 (.D(multiplexer_32_out), .Q(r0), .clk(T));  // open: en, clr
  Multiplexer #(.width(4), .enable("false")) multiplexer_32 (
    .in0(r0Res), .in1(4'b0000), .out(multiplexer_32_out), .sel(init));
  Multiplexer #(.width(8), .enable("false")) multiplexer_33 (
    .in0(out), .in1({8{1'b0}}), .out(multiplexer_33_out), .sel(Reset));
  or or_1 (or_1_out, Reset, enW);
  and and_4 (LEFT, TWin, L);
  Register register_17 (.D(multiplexer_33_out), .en(or_1_out), .Q({register_17_q, Win}), .clk(TWin));  // open: clr
  and and_5 (UP, TWin, U);
  and and_6 (DOWN, TWin, D);
  \Авто_инициализация  \u_авто_инициализация_1  (.clk(T), .init(init));
  Clock #(.highDuration(150), .lowDuration(150)) clock_1 (.out(T));
  and and_7 (RIGHT, TWin, R);
  Multiplexer #(.select(4), .width(4)) multiplexer_34 (
    .in0(r0), .in1(r1), .in2(r2), .in3(r3), .in4(r4), .in5(r5), .in6(r6), .in7(r7), .in8(r8), .in9(r9),
    .in10(rA), .in11(rB), .in12(rC), .in13(rD), .in14(rE), .in15(rF), .out(multiplexer_34_out),
    .sel(register_18_q));  // open: en
  Register #(.width(4)) register_18 (.D(out[3:0]), .en(en), .Q(register_18_q), .clk(Tcdm8));  // open: clr
  Clock clock_2 (.out(Tcdm8));
  and and_8 (TWin, Tcdm8, or_2_out);
  or or_2 (or_2_out, Reset, not_3_out);
  not not_3 (not_3_out, Win);
  assign CELL_BYTE = {{4{1'b0}}, multiplexer_34_out};  // Bit_Extender bit_extender_1
  Clock clock_3 (.out(clock_3_out));
  Random #(.width(2), .seed(4)) random_1 (.clk(clock_3_out), .next(Swap), .out(random_1_out));  // open: clr
  \Перемешивание  \u_перемешивание_1  (
    .in_1(Swap), .in_2(Swap), .in_3(Swap), .in_5(Swap), .out_6(UP1), .out_7(DOWN1), .out_8(LEFT1),
    .out_9(RIGHT1), .in_4(random_1_out));
  \Управление  \u_управление_1  (
    .out_6(U), .out_7(D), .out_8(R), .out_9(L), .in_1(Keyboard), .in_2(U_B), .in_3(D_B), .in_4(R_B),
    .in_5(L_B));
  \Отображение_матриц  \u_отображение_матриц_1  (
    .in_1(r1), .out_2(_11), .out_3(_12), .out_4(_13), .out_5(_14), .out_6(_15), .out_7(_16), .out_8(_17),
    .out_9(_18));
  \Отображение_матриц  \u_отображение_матриц_2  (
    .in_1(r5), .out_2(_51), .out_3(_52), .out_4(_53), .out_5(_54), .out_6(_55), .out_7(_56), .out_8(_57),
    .out_9(_58));
  \Отображение_матриц  \u_отображение_матриц_3  (
    .in_1(r9), .out_2(_91), .out_3(_92), .out_4(_93), .out_5(_94), .out_6(_95), .out_7(_96), .out_8(_97),
    .out_9(_98));
  \Отображение_матриц  \u_отображение_матриц_4  (
    .in_1(rD), .out_2(D1), .out_3(D2), .out_4(D3), .out_5(D4), .out_6(D5), .out_7(D6), .out_8(D7), .out_9(D8));
  \Проверка_на_0  \u_проверка_на_0_1  (.in_1(r1), .out_2(kR1));
  \Проверка_на_0  \u_проверка_на_0_2  (.in_1(r5), .out_2(kR5));
  \Проверка_на_0  \u_проверка_на_0_3  (.in_1(r9), .out_2(kR9));
  \Проверка_на_0  \u_проверка_на_0_4  (.in_1(rD), .out_2(kRD));
  \Отображение_матриц  \u_отображение_матриц_5  (
    .in_1(r2), .out_2(_21), .out_3(_22), .out_4(_23), .out_5(_24), .out_6(_25), .out_7(_26), .out_8(_27),
    .out_9(_28));
  \Отображение_матриц  \u_отображение_матриц_6  (
    .in_1(r6), .out_2(_61), .out_3(_62), .out_4(_63), .out_5(_64), .out_6(_65), .out_7(_66), .out_8(_67),
    .out_9(_68));
  \Отображение_матриц  \u_отображение_матриц_7  (
    .in_1(rA), .out_2(A1), .out_3(A2), .out_4(A3), .out_5(A4), .out_6(A5), .out_7(A6), .out_8(A7), .out_9(A8));
  \Отображение_матриц  \u_отображение_матриц_8  (
    .in_1(rE), .out_2(E1), .out_3(E2), .out_4(E3), .out_5(E4), .out_6(E5), .out_7(E6), .out_8(E7), .out_9(E8));
  \Проверка_на_0  \u_проверка_на_0_5  (.in_1(r2), .out_2(kR2));
  \Проверка_на_0  \u_проверка_на_0_6  (.in_1(r6), .out_2(kR6));
  \Проверка_на_0  \u_проверка_на_0_7  (.in_1(rA), .out_2(kRA));
  \Проверка_на_0  \u_проверка_на_0_8  (.in_1(rE), .out_2(kRE));
  \Отображение_матриц  \u_отображение_матриц_9  (
    .in_1(r3), .out_2(_31), .out_3(_32), .out_4(_33), .out_5(_34), .out_6(_35), .out_7(_36), .out_8(_37),
    .out_9(_38));
  \Отображение_матриц  \u_отображение_матриц_10  (
    .in_1(r7), .out_2(_71), .out_3(_72), .out_4(_73), .out_5(_74), .out_6(_75), .out_7(_76), .out_8(_77),
    .out_9(_78));
  \Отображение_матриц  \u_отображение_матриц_11  (
    .in_1(rB), .out_2(B1), .out_3(B2), .out_4(B3), .out_5(B4), .out_6(B5), .out_7(B6), .out_8(B7), .out_9(B8));
  \Отображение_матриц  \u_отображение_матриц_12  (
    .in_1(rF), .out_2(F1), .out_3(F2), .out_4(F3), .out_5(F4), .out_6(F5), .out_7(F6), .out_8(F7), .out_9(F8));
  \Проверка_на_0  \u_проверка_на_0_9  (.in_1(r3), .out_2(kR3));
  \Проверка_на_0  \u_проверка_на_0_10  (.in_1(r7), .out_2(kR7));
  \Проверка_на_0  \u_проверка_на_0_11  (.in_1(rB), .out_2(kRB));
  \Проверка_на_0  \u_проверка_на_0_12  (.in_1(rF), .out_2(kRF));
  \Отображение_матриц  \u_отображение_матриц_13  (
    .in_1(r4), .out_2(_41), .out_3(_42), .out_4(_43), .out_5(_44), .out_6(_45), .out_7(_46), .out_8(_47),
    .out_9(_48));
  \Отображение_матриц  \u_отображение_матриц_14  (
    .in_1(r8), .out_2(_81), .out_3(_82), .out_4(_83), .out_5(_84), .out_6(_85), .out_7(_86), .out_8(_87),
    .out_9(_88));
  \Отображение_матриц  \u_отображение_матриц_15  (
    .in_1(rC), .out_2(C1), .out_3(C2), .out_4(C3), .out_5(C4), .out_6(C5), .out_7(C6), .out_8(C7), .out_9(C8));
  \Отображение_матриц  \u_отображение_матриц_16  (
    .in_1(r0), .out_2(_01), .out_3(_02), .out_4(_03), .out_5(_04), .out_6(_05), .out_7(_06), .out_8(_07),
    .out_9(_08));
  \Проверка_на_0  \u_проверка_на_0_13  (.in_1(r4), .out_2(kR4));
  \Проверка_на_0  \u_проверка_на_0_14  (.in_1(r8), .out_2(kR8));
  \Проверка_на_0  \u_проверка_на_0_15  (.in_1(rC), .out_2(kRC));
  \Проверка_на_0  \u_проверка_на_0_16  (.in_1(r0), .out_2(kR0));
  and and_9 (LkR2, or_3_out, kR2);
  or or_3 (or_3_out, LEFT, LEFT1);
  and and_10 (LkR6, or_4_out, kR6);
  or or_4 (or_4_out, LEFT, LEFT1);
  and and_11 (LkRA, or_5_out, kRA);
  or or_5 (or_5_out, LEFT, LEFT1);
  and and_12 (LkRE, or_6_out, kRE);
  or or_6 (or_6_out, LEFT, LEFT1);
  and and_13 (LkR3, or_7_out, kR3);
  or or_7 (or_7_out, LEFT, LEFT1);
  and and_14 (LkR7, or_8_out, kR7);
  or or_8 (or_8_out, LEFT, LEFT1);
  and and_15 (LkRB, or_9_out, kRB);
  or or_9 (or_9_out, LEFT, LEFT1);
  and and_16 (LkRF, or_10_out, kRF);
  or or_10 (or_10_out, LEFT, LEFT1);
  and and_17 (LkR4, or_11_out, kR4);
  or or_11 (or_11_out, LEFT, LEFT1);
  and and_18 (LkR8, or_12_out, kR8);
  or or_12 (or_12_out, LEFT, LEFT1);
  and and_19 (LkRC, or_13_out, kRC);
  or or_13 (or_13_out, LEFT, LEFT1);
  and and_20 (LkR0, or_14_out, kR0);
  or or_14 (or_14_out, LEFT, LEFT1);
  and and_21 (UpkR5, or_15_out, kR5);
  or or_15 (or_15_out, UP, UP1);
  and and_22 (UpkR9, or_16_out, kR9);
  or or_16 (or_16_out, UP, UP1);
  and and_23 (UpkRD, or_17_out, kRD);
  or or_17 (or_17_out, UP, UP1);
  and and_24 (DkR1, or_18_out, kR1);
  or or_18 (or_18_out, DOWN, DOWN1);
  and and_25 (DkR5, or_19_out, kR5);
  or or_19 (or_19_out, DOWN, DOWN1);
  and and_26 (DkR9, or_20_out, kR9);
  or or_20 (or_20_out, DOWN, DOWN1);
  and and_27 (UpkR6, or_21_out, kR6);
  or or_21 (or_21_out, UP, UP1);
  and and_28 (UpkRA, or_22_out, kRA);
  or or_22 (or_22_out, UP, UP1);
  and and_29 (UpkRE, or_23_out, kRE);
  or or_23 (or_23_out, UP, UP1);
  and and_30 (DkR2, or_24_out, kR2);
  or or_24 (or_24_out, DOWN, DOWN1);
  and and_31 (DkR6, or_25_out, kR6);
  or or_25 (or_25_out, DOWN, DOWN1);
  and and_32 (DkRA, or_26_out, kRA);
  or or_26 (or_26_out, DOWN, DOWN1);
  and and_33 (UpkR7, or_27_out, kR7);
  or or_27 (or_27_out, UP, UP1);
  and and_34 (UpkRB, or_28_out, kRB);
  or or_28 (or_28_out, UP, UP1);
  and and_35 (UpkRF, or_29_out, kRF);
  or or_29 (or_29_out, UP, UP1);
  and and_36 (DkR3, or_30_out, kR3);
  or or_30 (or_30_out, DOWN, DOWN1);
  and and_37 (DkR7, or_31_out, kR7);
  or or_31 (or_31_out, DOWN, DOWN1);
  and and_38 (DkRB, or_32_out, kRB);
  or or_32 (or_32_out, DOWN, DOWN1);
  and and_39 (UpkR8, or_33_out, kR8);
  or or_33 (or_33_out, UP, UP1);
  and and_40 (UpkRC, or_34_out, kRC);
  or or_34 (or_34_out, UP, UP1);
  and and_41 (UpkR0, or_35_out, kR0);
  or or_35 (or_35_out, UP, UP1);
  and and_42 (DkR4, or_36_out, kR4);
  or or_36 (or_36_out, DOWN, DOWN1);
  and and_43 (DkR8, or_37_out, kR8);
  or or_37 (or_37_out, DOWN, DOWN1);
  and and_44 (DkRC, or_38_out, kRC);
  or or_38 (or_38_out, DOWN, DOWN1);
  or or_39 (or_39_out, RIGHT, RIGHT1);
  or or_40 (or_40_out, RIGHT, RIGHT1);
  or or_41 (or_41_out, RIGHT, RIGHT1);
  or or_42 (or_42_out, RIGHT, RIGHT1);
  and and_45 (RkR1, or_39_out, kR1);
  or or_43 (or_43_out, RIGHT, RIGHT1);
  and and_46 (RkR5, or_40_out, kR5);
  or or_44 (or_44_out, RIGHT, RIGHT1);
  and and_47 (RkR9, or_41_out, kR9);
  or or_45 (or_45_out, RIGHT, RIGHT1);
  and and_48 (RkRD, or_42_out, kRD);
  or or_46 (or_46_out, RIGHT, RIGHT1);
  and and_49 (RkR2, or_43_out, kR2);
  or or_47 (or_47_out, RIGHT, RIGHT1);
  and and_50 (RkR6, or_44_out, kR6);
  or or_48 (or_48_out, RIGHT, RIGHT1);
  and and_51 (RkRA, or_45_out, kRA);
  or or_49 (or_49_out, RIGHT, RIGHT1);
  and and_52 (RkRE, or_46_out, kRE);
  or or_50 (or_50_out, RIGHT, RIGHT1);
  and and_53 (RkR3, or_47_out, kR3);
  and and_54 (RkR7, or_48_out, kR7);
  and and_55 (RkRB, or_49_out, kRB);
  and and_56 (RkRF, or_50_out, kRF);
  Multiplexer #(.width(4), .enable("false")) multiplexer_35 (
    .in0(multiplexer_36_out), .in1(r2), .out(r1Res), .sel(RkR1));
  Multiplexer #(.width(4), .enable("false")) multiplexer_36 (
    .in0(r1_r5_2), .in1(r5), .out(multiplexer_36_out), .sel(DkR1));
  Multiplexer #(.width(4), .enable("false")) multiplexer_37 (
    .in0(multiplexer_39_out), .in1(r6), .out(r1_r5), .sel(RkR5));
  Multiplexer #(.width(4), .enable("false")) multiplexer_38 (.in0(r5), .in1(r1), .out(multiplexer_38_out), .sel(UpkR5));
  Multiplexer #(.width(4), .enable("false")) multiplexer_39 (
    .in0(multiplexer_38_out), .in1(r9), .out(multiplexer_39_out), .sel(DkR5));
  Multiplexer #(.width(4), .enable("false")) multiplexer_40 (
    .in0(multiplexer_42_out), .in1(rA), .out(r9_rA_2), .sel(RkR9));
  Multiplexer #(.width(4), .enable("false")) multiplexer_41 (
    .in0(r5_r9), .in1(r5), .out(multiplexer_41_out), .sel(UpkR9));
  Multiplexer #(.width(4), .enable("false")) multiplexer_42 (
    .in0(multiplexer_41_out), .in1(rD), .out(multiplexer_42_out), .sel(DkR9));
  Multiplexer #(.width(4), .enable("false")) multiplexer_43 (
    .in0(multiplexer_44_out), .in1(rE), .out(rD_rE_2), .sel(RkRD));
  Multiplexer #(.width(4), .enable("false")) multiplexer_44 (
    .in0(r9_rD), .in1(r9), .out(multiplexer_44_out), .sel(UpkRD));
  Multiplexer #(.width(4), .enable("false")) multiplexer_45 (.in0(r2), .in1(r1), .out(r1_r2), .sel(RkR1));
  Multiplexer #(.width(4), .enable("false")) multiplexer_46 (.in0(r1_r5), .in1(r1), .out(r1_r6), .sel(DkR1));
  Multiplexer #(.width(4), .enable("false")) multiplexer_47 (.in0(r6), .in1(r5), .out(r2_r5_2), .sel(RkR5));
  Multiplexer #(.width(4), .enable("false")) multiplexer_48 (.in0(r2_r5), .in1(r5), .out(r1_r5_2), .sel(UpkR5));
  Multiplexer #(.width(4), .enable("false")) multiplexer_49 (.in0(r9), .in1(r5), .out(r5_r9), .sel(DkR5));
  Multiplexer #(.width(4), .enable("false")) multiplexer_50 (.in0(r6_r9), .in1(r9), .out(r9_rA), .sel(RkR9));
  Multiplexer #(.width(4), .enable("false")) multiplexer_51 (.in0(r6_r9_2), .in1(r9), .out(r5Res), .sel(UpkR9));
  Multiplexer #(.width(4), .enable("false")) multiplexer_52 (.in0(rD), .in1(r9), .out(r9_rD), .sel(DkR9));
  Multiplexer #(.width(4), .enable("false")) multiplexer_53 (.in0(rA_rD_2), .in1(rD), .out(rD_rE), .sel(RkRD));
  Multiplexer #(.width(4), .enable("false")) multiplexer_54 (.in0(rA_rD), .in1(rD), .out(r9Res), .sel(UpkRD));
  Multiplexer #(.width(4), .enable("false")) multiplexer_55 (
    .in0(multiplexer_57_out), .in1(r3), .out(r2_r3_2), .sel(RkR2));
  Multiplexer #(.width(4), .enable("false")) multiplexer_56 (
    .in0(r1_r2), .in1(r1), .out(multiplexer_56_out), .sel(LkR2));
  Multiplexer #(.width(4), .enable("false")) multiplexer_57 (
    .in0(multiplexer_56_out), .in1(r6), .out(multiplexer_57_out), .sel(DkR2));
  Multiplexer #(.width(4), .enable("false")) multiplexer_58 (
    .in0(multiplexer_60_out), .in1(r7), .out(multiplexer_58_out), .sel(RkR6));
  Multiplexer #(.width(4), .enable("false")) multiplexer_59 (
    .in0(r2_r6), .in1(r5), .out(multiplexer_59_out), .sel(LkR6));
  Multiplexer #(.width(4), .enable("false")) multiplexer_60 (
    .in0(multiplexer_59_out), .in1(rA), .out(multiplexer_60_out), .sel(DkR6));
  Multiplexer #(.width(4), .enable("false")) multiplexer_61 (
    .in0(multiplexer_58_out), .in1(r2), .out(r6_r7_2), .sel(UpkR6));
  Multiplexer #(.width(4), .enable("false")) multiplexer_62 (
    .in0(multiplexer_64_out), .in1(rB), .out(multiplexer_62_out), .sel(RkRA));
  Multiplexer #(.width(4), .enable("false")) multiplexer_63 (
    .in0(r9_rA), .in1(r9), .out(multiplexer_63_out), .sel(LkRA));
  Multiplexer #(.width(4), .enable("false")) multiplexer_64 (
    .in0(multiplexer_63_out), .in1(rE), .out(multiplexer_64_out), .sel(DkRA));
  Multiplexer #(.width(4), .enable("false")) multiplexer_65 (
    .in0(multiplexer_62_out), .in1(r6), .out(rA_rB_2), .sel(UpkRA));
  Multiplexer #(.width(4), .enable("false")) multiplexer_66 (
    .in0(multiplexer_67_out), .in1(rF), .out(multiplexer_66_out), .sel(RkRE));
  Multiplexer #(.width(4), .enable("false")) multiplexer_67 (
    .in0(rD_rE), .in1(rD), .out(multiplexer_67_out), .sel(LkRE));
  Multiplexer #(.width(4), .enable("false")) multiplexer_68 (
    .in0(multiplexer_66_out), .in1(rA), .out(rE_rF_2), .sel(UpkRE));
  Multiplexer #(.width(4), .enable("false")) multiplexer_69 (.in0(r2_r4), .in1(r2), .out(r2_r3), .sel(RkR2));
  Multiplexer #(.width(4), .enable("false")) multiplexer_70 (.in0(r1), .in1(r2), .out(r2_r5), .sel(LkR2));
  Multiplexer #(.width(4), .enable("false")) multiplexer_71 (.in0(r2_r5_2), .in1(r2), .out(r2_r6), .sel(DkR2));
  Multiplexer #(.width(4), .enable("false")) multiplexer_72 (.in0(r3_r6_2), .in1(r6), .out(r6_r7), .sel(RkR6));
  Multiplexer #(.width(4), .enable("false")) multiplexer_73 (.in0(r1_r6), .in1(r6), .out(r6_r9_2), .sel(LkR6));
  Multiplexer #(.width(4), .enable("false")) multiplexer_74 (.in0(rA), .in1(r6), .out(r6_r9), .sel(DkR6));
  Multiplexer #(.width(4), .enable("false")) multiplexer_75 (.in0(r3_r6), .in1(r6), .out(r2Res), .sel(UpkR6));
  Multiplexer #(.width(4), .enable("false")) multiplexer_76 (.in0(r7_rA), .in1(rA), .out(rA_rB), .sel(RkRA));
  Multiplexer #(.width(4), .enable("false")) multiplexer_77 (.in0(r9_rA_2), .in1(rA), .out(rA_rD), .sel(LkRA));
  Multiplexer #(.width(4), .enable("false")) multiplexer_78 (.in0(rE), .in1(rA), .out(rA_rD_2), .sel(DkRA));
  Multiplexer #(.width(4), .enable("false")) multiplexer_79 (.in0(r7_rA_2), .in1(rA), .out(r6Res), .sel(UpkRA));
  Multiplexer #(.width(4), .enable("false")) multiplexer_80 (.in0(rB_rE), .in1(rE), .out(rE_rF), .sel(RkRE));
  Multiplexer #(.width(4), .enable("false")) multiplexer_81 (.in0(rD_rE_2), .in1(rE), .out(rDRes), .sel(LkRE));
  Multiplexer #(.width(4), .enable("false")) multiplexer_82 (.in0(rB_rE_2), .in1(rE), .out(rARes), .sel(UpkRE));
  Multiplexer #(.width(4), .enable("false")) multiplexer_83 (
    .in0(multiplexer_85_out), .in1(r4), .out(r3_r7), .sel(RkR3));
  Multiplexer #(.width(4), .enable("false")) multiplexer_84 (
    .in0(r2_r3), .in1(r2), .out(multiplexer_84_out), .sel(LkR3));
  Multiplexer #(.width(4), .enable("false")) multiplexer_85 (
    .in0(multiplexer_84_out), .in1(r7), .out(multiplexer_85_out), .sel(DkR3));
  Multiplexer #(.width(4), .enable("false")) multiplexer_86 (
    .in0(multiplexer_88_out), .in1(r8), .out(multiplexer_86_out), .sel(RkR7));
  Multiplexer #(.width(4), .enable("false")) multiplexer_87 (
    .in0(r6_r7), .in1(r6), .out(multiplexer_87_out), .sel(LkR7));
  Multiplexer #(.width(4), .enable("false")) multiplexer_88 (
    .in0(multiplexer_87_out), .in1(rB), .out(multiplexer_88_out), .sel(DkR7));
  Multiplexer #(.width(4), .enable("false")) multiplexer_89 (
    .in0(multiplexer_86_out), .in1(r3), .out(r7_r8), .sel(UpkR7));
  Multiplexer #(.width(4), .enable("false")) multiplexer_90 (
    .in0(multiplexer_92_out), .in1(rC), .out(multiplexer_90_out), .sel(RkRB));
  Multiplexer #(.width(4), .enable("false")) multiplexer_91 (
    .in0(rA_rB), .in1(rA), .out(multiplexer_91_out), .sel(LkRB));
  Multiplexer #(.width(4), .enable("false")) multiplexer_92 (
    .in0(multiplexer_91_out), .in1(rF), .out(multiplexer_92_out), .sel(DkRB));
  Multiplexer #(.width(4), .enable("false")) multiplexer_93 (
    .in0(multiplexer_90_out), .in1(r7), .out(rB_rC_2), .sel(UpkRB));
  Multiplexer #(.width(4), .enable("false")) multiplexer_94 (
    .in0(multiplexer_95_out), .in1(r0), .out(multiplexer_94_out), .sel(RkRF));
  Multiplexer #(.width(4), .enable("false")) multiplexer_95 (
    .in0(rE_rF), .in1(rE), .out(multiplexer_95_out), .sel(LkRF));
  Multiplexer #(.width(4), .enable("false")) multiplexer_96 (
    .in0(multiplexer_94_out), .in1(rB), .out(rF_r0), .sel(UpkRF));
  Multiplexer #(.width(4), .enable("false")) multiplexer_97 (.in0(r4_r3), .in1(r3), .out(r3_r8), .sel(RkR3));
  Multiplexer #(.width(4), .enable("false")) multiplexer_98 (.in0(r2_r3_2), .in1(r3), .out(r3_r6), .sel(LkR3));
  Multiplexer #(.width(4), .enable("false")) multiplexer_99 (.in0(r7), .in1(r3), .out(r3_r6_2), .sel(DkR3));
  Multiplexer #(.width(4), .enable("false")) multiplexer_100 (.in0(r4_r7), .in1(r7), .out(r7_r8_2), .sel(RkR7));
  Multiplexer #(.width(4), .enable("false")) multiplexer_101 (.in0(r6_r7_2), .in1(r7), .out(r7_rA_2), .sel(LkR7));
  Multiplexer #(.width(4), .enable("false")) multiplexer_102 (.in0(rB), .in1(r7), .out(r7_rA), .sel(DkR7));
  Multiplexer #(.width(4), .enable("false")) multiplexer_103 (.in0(r3_r7), .in1(r7), .out(r3Res), .sel(UpkR7));
  Multiplexer #(.width(4), .enable("false")) multiplexer_104 (.in0(r8_rB), .in1(rB), .out(rB_rC), .sel(RkRB));
  Multiplexer #(.width(4), .enable("false")) multiplexer_105 (.in0(rA_rB_2), .in1(rB), .out(rB_rE_2), .sel(LkRB));
  Multiplexer #(.width(4), .enable("false")) multiplexer_106 (.in0(rF), .in1(rB), .out(rB_rE), .sel(DkRB));
  Multiplexer #(.width(4), .enable("false")) multiplexer_107 (.in0(r8_rB_2), .in1(rB), .out(r7Res), .sel(UpkRB));
  Multiplexer #(.width(4), .enable("false")) multiplexer_108 (.in0(rC_rF_2), .in1(rF), .out(rF_r0_2), .sel(RkRF));
  Multiplexer #(.width(4), .enable("false")) multiplexer_109 (.in0(rE_rF_2), .in1(rF), .out(rERes), .sel(LkRF));
  Multiplexer #(.width(4), .enable("false")) multiplexer_110 (.in0(rC_rF), .in1(rF), .out(rBRes), .sel(UpkRF));
  Multiplexer #(.width(4), .enable("false")) multiplexer_111 (
    .in0(multiplexer_112_out), .in1(r3), .out(r4_r3), .sel(LkR4));
  Multiplexer #(.width(4), .enable("false")) multiplexer_112 (
    .in0(r4), .in1(r8), .out(multiplexer_112_out), .sel(DkR4));
  Multiplexer #(.width(4), .enable("false")) multiplexer_113 (
    .in0(multiplexer_115_out), .in1(r7), .out(r8_rC), .sel(LkR8));
  Multiplexer #(.width(4), .enable("false")) multiplexer_114 (
    .in0(r7_r8_2), .in1(r4), .out(multiplexer_114_out), .sel(UpkR8));
  Multiplexer #(.width(4), .enable("false")) multiplexer_115 (
    .in0(multiplexer_114_out), .in1(rC), .out(multiplexer_115_out), .sel(DkR8));
  Multiplexer #(.width(4), .enable("false")) multiplexer_116 (
    .in0(multiplexer_118_out), .in1(rB), .out(rC_r0), .sel(LkRC));
  Multiplexer #(.width(4), .enable("false")) multiplexer_117 (
    .in0(rB_rC), .in1(r8), .out(multiplexer_117_out), .sel(UpkRC));
  Multiplexer #(.width(4), .enable("false")) multiplexer_118 (
    .in0(multiplexer_117_out), .in1(r0), .out(multiplexer_118_out), .sel(DkRC));
  Multiplexer #(.width(4), .enable("false")) multiplexer_119 (
    .in0(multiplexer_120_out), .in1(rF), .out(r0Res), .sel(LkR0));
  Multiplexer #(.width(4), .enable("false")) multiplexer_120 (
    .in0(rF_r0_2), .in1(rC), .out(multiplexer_120_out), .sel(UpkR0));
  Multiplexer #(.width(4), .enable("false")) multiplexer_121 (.in0(r3), .in1(r4), .out(r2_r4), .sel(LkR4));
  Multiplexer #(.width(4), .enable("false")) multiplexer_122 (.in0(r8), .in1(r4), .out(r4_r7), .sel(DkR4));
  Multiplexer #(.width(4), .enable("false")) multiplexer_123 (.in0(r7_r8), .in1(r8), .out(r8_rB_2), .sel(LkR8));
  Multiplexer #(.width(4), .enable("false")) multiplexer_124 (.in0(r3_r8), .in1(r8), .out(r4Res), .sel(UpkR8));
  Multiplexer #(.width(4), .enable("false")) multiplexer_125 (.in0(rC), .in1(r8), .out(r8_rB), .sel(DkR8));
  Multiplexer #(.width(4), .enable("false")) multiplexer_126 (.in0(rB_rC_2), .in1(rC), .out(rC_rF), .sel(LkRC));
  Multiplexer #(.width(4), .enable("false")) multiplexer_127 (.in0(r8_rC), .in1(rC), .out(r8Res), .sel(UpkRC));
  Multiplexer #(.width(4), .enable("false")) multiplexer_128 (.in0(r0), .in1(rC), .out(rC_rF_2), .sel(DkRC));
  Multiplexer #(.width(4), .enable("false")) multiplexer_129 (.in0(rF_r0), .in1(r0), .out(rFRes), .sel(LkR0));
  Multiplexer #(.width(4), .enable("false")) multiplexer_130 (.in0(rC_r0), .in1(r0), .out(rCRes), .sel(UpkR0));
  LED led_21 ();  // open: in

  // Notes on the sheet:
  //   contents of rom_1 (hex, n*v repeats v):
  //   d3 f2 d0 0 ac d0 1 d1 1 d3 f0 ac d3 f1 be 79 e1 2d 8c 8d d3 10 77 e1 9 d0 0 d3 f0 ac d3 f1 be d1 0
  //   79 e1 2d d0 1 d3 f2 ac ee 0 d0 0 d3 f2 ac ee
  //   МАТРИЦА WIN
  //   РЕГИСТРЫ ЯЧЕЕК
  //   МИКРОПРОЦЕССОР
  //   ПРОВЕРКА ПОБЕДЫ
  //   ТАКТЫ И РАНДОМНОЕ ПЕРЕМЕШИВАНИЕ
  //   ОТОБРАЖЕНИЯ МАТРИЦ
  //   ПРОВЕРКА НА 0
  //   ВЛЕВО
  //   ВВЕРХ
  //   ВНИЗ
  //   ВПРАВО
  //   Блок на возможность движения
endmodule

module \Отображение_матриц  (
  input  [3:0] in_1,
  output [9:0] out_2,
  output [9:0] out_3,
  output [9:0] out_4,
  output [9:0] out_5,
  output [9:0] out_6,
  output [9:0] out_7,
  output [9:0] out_8,
  output [9:0] out_9
);

  ROM #(.addrWidth(4), .dataWidth(20)) rom_1 (.addr(in_1), .data({out_3, out_2}));  // open: sel
  ROM #(.addrWidth(4), .dataWidth(20)) rom_2 (.addr(in_1), .data({out_5, out_4}));  // open: sel
  ROM #(.addrWidth(4), .dataWidth(20)) rom_3 (.addr(in_1), .data({out_7, out_6}));  // open: sel
  ROM #(.addrWidth(4), .dataWidth(20)) rom_4 (.addr(in_1), .data({out_9, out_8}));  // open: sel

  // Notes on the sheet:
  //   contents of rom_1 (hex, n*v repeats v):
  //   0 81 40603 41a01 4030 f1a41 3f921 80207 77a21 78211 6*407ff
  //   contents of rom_2 (hex, n*v repeats v):
  //   0 407ff 81609 80601 14090 90641 88621 82210 88621 84611 6*400
  //   contents of rom_3 (hex, n*v repeats v):
  //   0 ffc01 84621 98661 44210 90641 88621 88240 88621 84611 ffe01 407ff 8fe21 80621 f8020 f8621
  //   contents of rom_4 (hex, n*v repeats v):
  //   0 400 90581 9859e ffc10 9063e 8841e a0300 885de 849fc 807ff 400 887e1 887ff 83ff 8863f
endmodule

module \Проверка_на_0  (
  input  [3:0] in_1,
  output out_2
);

  Comparator #(.width(4)) comparator_1 (.a(in_1), .b(4'b0000), .eq(out_2));  // open: gt, lt
endmodule

module \Управление  (
  input  [6:0] in_1,
  input  in_2,
  input  in_3,
  input  in_4,
  input  in_5,
  output out_6,
  output out_7,
  output out_8,
  output out_9
);

  wire comparator_1_eq, comparator_2_eq, comparator_3_eq, comparator_4_eq, comparator_5_eq, comparator_6_eq,
       comparator_7_eq, comparator_8_eq;

  Comparator #(.width(7)) comparator_1 (.a(in_1), .b(7'b1110111), .eq(comparator_1_eq));  // open: gt, lt
  Comparator #(.width(7)) comparator_2 (.a(in_1), .b(7'b1000110), .eq(comparator_2_eq));  // open: gt, lt
  Comparator #(.width(7)) comparator_3 (.a(in_1), .b(7'b1110011), .eq(comparator_3_eq));  // open: gt, lt
  Comparator #(.width(7)) comparator_4 (.a(in_1), .b(7'b1001011), .eq(comparator_4_eq));  // open: gt, lt
  Comparator #(.width(7)) comparator_5 (.a(in_1), .b(7'b1100100), .eq(comparator_5_eq));  // open: gt, lt
  Comparator #(.width(7)) comparator_6 (.a(in_1), .b(7'b0110010), .eq(comparator_6_eq));  // open: gt, lt
  Comparator #(.width(7)) comparator_7 (.a(in_1), .b(7'b1100001), .eq(comparator_7_eq));  // open: gt, lt
  Comparator #(.width(7)) comparator_8 (.a(in_1), .b(7'b1000100), .eq(comparator_8_eq));  // open: gt, lt
  or or_1 (out_6, in_2, comparator_1_eq, comparator_2_eq);
  or or_2 (out_7, in_3, comparator_3_eq, comparator_4_eq);
  or or_3 (out_8, in_4, comparator_5_eq, comparator_6_eq);
  or or_4 (out_9, in_5, comparator_7_eq, comparator_8_eq);
endmodule

module \Перемешивание  (
  input  in_1,
  input  in_2,
  input  in_3,
  input  [1:0] in_4,
  input  in_5,
  output out_6,
  output out_7,
  output out_8,
  output out_9
);

  wire decoder_1_out0, decoder_1_out1, decoder_1_out2, decoder_1_out3;

  Decoder #(.select(2), .enable("false")) decoder_1 (
    .out0(decoder_1_out0), .out1(decoder_1_out1), .out2(decoder_1_out2), .out3(decoder_1_out3), .sel(in_4));
  and and_1 (out_6, in_1, decoder_1_out0);
  and and_2 (out_7, in_2, decoder_1_out1);
  and and_3 (out_8, in_3, decoder_1_out2);
  and and_4 (out_9, in_5, decoder_1_out3);
endmodule

module \Авто_инициализация  (
  input  clk,
  output init
);

  wire register_1_q;

  Register #(.width(1)) register_1 (.D(1'b1), .Q(register_1_q), .clk(clk));  // open: en, clr
  not not_1 (init, register_1_q);
endmodule
