// Logisim project 15puzzleV1_REPACK_BY_XATAB.circ as structural Verilog: 2 circuits, main circuit Digit
module main (
);

  wire ad, adF1, adW, clock_3_out, D_B, decoder_1_out0, decoder_1_out1, decoder_1_out2, decoder_1_out3, DkR1,
       DkR2, DkR3, DkR4, DkR5, DkR6, DkR7, DkR8, DkR9, DkRA, DkRB, DkRC, DOWN, DOWN1, en, enF1, enW, kR0,
       kR1, kR2, kR3, kR4, kR5, kR6, kR7, kR8, kR9, kRA, kRB, kRC, kRD, kRE, kRF, L_B, LEFT, LEFT1, LkR0,
       LkR2, LkR3, LkR4, LkR6, LkR7, LkR8, LkRA, LkRB, LkRC, LkRE, LkRF, memory, not_1_out, not_2_out,
       not_3_out, or_1_out, or_2_out, or_3_out, or_4_out, or_5_out, or_6_out, or_7_out, or_8_out, or_9_out,
       or_10_out, or_11_out, or_12_out, or_13_out, or_14_out, or_15_out, or_16_out, or_17_out, or_18_out,
       or_19_out, or_20_out, or_21_out, or_22_out, or_23_out, or_24_out, or_25_out, or_26_out, or_27_out,
       or_28_out, or_29_out, or_30_out, or_31_out, or_32_out, or_33_out, or_34_out, or_35_out, or_36_out,
       or_37_out, or_38_out, or_39_out, or_40_out, or_41_out, or_42_out, or_43_out, or_44_out, or_45_out,
       or_46_out, or_47_out, or_48_out, or_49_out, or_50_out, R, R_B, read_write, Reset, RIGHT, RIGHT1, RkR1,
       RkR2, RkR3, RkR5, RkR6, RkR7, RkR9, RkRA, RkRB, RkRD, RkRE, RkRF, T, Tcdm8, TWin, U_B, undriven,
       undriven_2, undriven_3, undriven_4, undriven_5, undriven_6, UP, UP1, UpkR0, UpkR5, UpkR6, UpkR7,
       UpkR8, UpkR9, UpkRA, UpkRB, UpkRC, UpkRD, UpkRE, UpkRF, Win;
  wire [1:0] random_1_out;
  wire [3:0] multiplexer_18_out, multiplexer_20_out, multiplexer_22_out, multiplexer_23_out,
       multiplexer_25_out, multiplexer_26_out, multiplexer_28_out, multiplexer_40_out, multiplexer_41_out,
       multiplexer_42_out, multiplexer_43_out, multiplexer_44_out, multiplexer_46_out, multiplexer_47_out,
       multiplexer_48_out, multiplexer_50_out, multiplexer_51_out, multiplexer_68_out, multiplexer_69_out,
       multiplexer_70_out, multiplexer_71_out, multiplexer_72_out, multiplexer_74_out, multiplexer_75_out,
       multiplexer_76_out, multiplexer_78_out, multiplexer_79_out, multiplexer_96_out, multiplexer_98_out,
       multiplexer_99_out, multiplexer_101_out, multiplexer_102_out, multiplexer_104_out, r0, r0Res, r1,
       r1_r2, r1_r5, r1_r5_2, r1_r6, r1Res, r2, r2_r3, r2_r3_2, r2_r4, r2_r5, r2_r5_2, r2_r6, r2Res, r3,
       r3_r6, r3_r6_2, r3_r7, r3_r8, r3Res, r4, r4_r3, r4_r7, r4Res, r5, r5_r9, r5Res, r6, r6_r7, r6_r7_2,
       r6_r9, r6_r9_2, r6Res, r7, r7_r8, r7_r8_2, r7_rA, r7_rA_2, r7Res, r8, r8_rB, r8_rB_2, r8_rC, r8Res,
       r9, r9_rA, r9_rA_2, r9_rD, r9Res, rA, rA_rB, rA_rB_2, rA_rD, rA_rD_2, rARes, rB, rB_rC, rB_rC_2,
       rB_rE, rB_rE_2, rBRes, rC, rC_r0, rC_rF, rC_rF_2, rCRes, rD, rD_rE, rD_rE_2, rDRes, rE, rE_rF,
       rE_rF_2, register_18_q, rERes, rF, rF_r0, rF_r0_2, rFRes;
  wire [7:0] addr, cdm_8_mark5_1_r0, cdm_8_mark5_1_r1, cdm_8_mark5_1_r2, cdm_8_mark5_1_r3, CELL_BYTE, data,
       i1, i2, i3, i4, i5, multiplexer_7_out, multiplexer_17_out, n1, n2, n3, n4, n5, out, w1, w2, w3, w4, w5;
  wire [7:1] register_17_q;
  wire [9:0] _01, _02, _03, _04, _05, _06, _07, _08, _11, _12, _13, _14, _15, _16, _17, _18, _21, _22, _23,
       _24, _25, _26, _27, _28, _31, _32, _33, _34, _35, _36, _37, _38, _41, _42, _43, _44, _45, _46, _47,
       _48, _51, _52, _53, _54, _55, _56, _57, _58, _61, _62, _63, _64, _65, _66, _67, _68, _71, _72, _73,
       _74, _75, _76, _77, _78, _81, _82, _83, _84, _85, _86, _87, _88, _91, _92, _93, _94, _95, _96, _97,
       _98, A1, A2, A3, A4, A5, A6, A7, A8, B1, B2, B3, B4, B5, B6, B7, B8, C1, C2, C3, C4, C5, C6, C7, C8,
       D1, D2, D3, D4, D5, D6, D7, D8, E1, E2, E3, E4, E5, E6, E7, E8, F1, F2, F3, F4, F5, F6, F7, F8;

  LED led_1 ();  // open: in
  LED led_2 ();  // open: in
  LED led_3 (.in(undriven));
  LED led_4 ();  // open: in
  LED led_5 (.in(undriven_2));
  LED led_6 ();  // open: in
  LED led_7 ();  // open: in
  LED led_8 (.in(undriven_3));
  LED led_9 ();  // open: in
  LED led_10 ();  // open: in
  Register #(.width(4)) register_1 (.D(r1Res), .Q(r1), .clk(T));  // open: en, clr
  Register #(.width(4)) register_2 (.D(r5Res), .Q(r5), .clk(T));  // open: en, clr
  Register #(.width(4)) register_3 (.D(r9Res), .Q(r9), .clk(T));  // open: en, clr
  Register #(.width(4)) register_4 (.D(rDRes), .Q(rD), .clk(T));  // open: en, clr
  DotMatrix #(.matrixcols(8), .matrixrows(10)) dotmatrix_1 (
    .col0(_12), .col1(_11), .col2(_14), .col3(_13), .col4(_16), .col5(_15), .col6(_18), .col7(_17));
  TTY #(.rows(3), .cols(54)) tty_1 ();  // open: data, clk, we, clr
  DotMatrix #(.matrixcols(8), .matrixrows(10)) dotmatrix_2 (
    .col0(_52), .col1(_51), .col2(_54), .col3(_53), .col4(_56), .col5(_55), .col6(_58), .col7(_57));
  TTY #(.rows(3), .cols(54)) tty_2 ();  // open: data, clk, we, clr
  DotMatrix #(.matrixcols(8), .matrixrows(10)) dotmatrix_3 (
    .col0(_92), .col1(_91), .col2(_94), .col3(_93), .col4(_96), .col5(_95), .col6(_98), .col7(_97));
  TTY #(.rows(3), .cols(54)) tty_3 ();  // open: data, clk, we, clr
  DotMatrix #(.matrixcols(8), .matrixrows(10)) dotmatrix_4 (
    .col0(D2), .col1(D1), .col2(D4), .col3(D3), .col4(D6), .col5(D5), .col6(D8), .col7(D7));
  TTY #(.rows(3), .cols(54)) tty_4 ();  // open: data, clk, we, clr
  // Probe on cdm_8_mark5_1_r0
  Multiplexer #(.width(8)) multiplexer_1 (.in0({8{1'b0}}), .in1({8{1'b1}}), .out(w1), .sel(Win));  // open: en
  Multiplexer #(.width(8)) multiplexer_2 (.in0({8{1'b0}}), .in1(8'h81), .out(i1), .sel(Win));  // open: en
  Multiplexer #(.width(8)) multiplexer_3 (.in0({8{1'b0}}), .in1({8{1'b1}}), .out(n1), .sel(Win));  // open: en
  LED led_11 ();  // open: in
  LED led_12 ();  // open: in
  LED led_13 ();  // open: in
  LED led_14 (.in(undriven_4));
  LED led_15 (.in(undriven_5));
  LED led_16 ();  // open: in
  LED led_17 (.in(undriven_6));
  LED led_18 ();  // open: in
  LED led_19 ();  // open: in
  LED led_20 ();  // open: in
  DotMatrix #(.matrixcols(8), .matrixrows(10)) dotmatrix_5 (
    .col0(_22), .col1(_21), .col2(_24), .col3(_23), .col4(_26), .col5(_25), .col6(_28), .col7(_27));
  DotMatrix #(.matrixcols(8), .matrixrows(10)) dotmatrix_6 (
    .col0(_62), .col1(_61), .col2(_64), .col3(_63), .col4(_66), .col5(_65), .col6(_68), .col7(_67));
  DotMatrix #(.matrixcols(8), .matrixrows(10)) dotmatrix_7 (
    .col0(A2), .col1(A1), .col2(A4), .col3(A3), .col4(A6), .col5(A5), .col6(A8), .col7(A7));
  DotMatrix #(.matrixcols(8), .matrixrows(10)) dotmatrix_8 (
    .col0(E2), .col1(E1), .col2(E4), .col3(E3), .col4(E6), .col5(E5), .col6(E8), .col7(E7));
  // Probe on cdm_8_mark5_1_r2
  // Probe on cdm_8_mark5_1_r1
  // Probe on cdm_8_mark5_1_r3
  and and_1 (en, memory, ad, not_1_out);
  not not_1 (not_1_out, read_write);
  Comparator comparator_1 (.a(addr), .b(8'hf0), .eq(ad));  // open: gt, lt
  Multiplexer #(.width(8)) multiplexer_4 (.in0({8{1'b0}}), .in1(8'h2), .out(w2), .sel(Win));  // open: en
  Multiplexer #(.width(8)) multiplexer_5 (.in0({8{1'b0}}), .in1(8'h81), .out(i2), .sel(Win));  // open: en
  Multiplexer #(.width(8)) multiplexer_6 (.in0({8{1'b0}}), .in1(8'h60), .out(n2), .sel(Win));  // open: en
  Register #(.width(4)) register_5 (.D(r2Res), .Q(r2), .clk(T));  // open: en, clr
  Register #(.width(4)) register_6 (.D(r6Res), .Q(r6), .clk(T));  // open: en, clr
  Register #(.width(4)) register_7 (.D(rARes), .Q(rA), .clk(T));  // open: en, clr
  Register #(.width(4)) register_8 (.D(rERes), .Q(rE), .clk(T));  // open: en, clr
  DotMatrix #(.matrixcols(8), .matrixrows(10)) dotmatrix_9 (
    .col0(_32), .col1(_31), .col2(_34), .col3(_33), .col4(_36), .col5(_35), .col6(_38), .col7(_37));
  DotMatrix #(.matrixcols(8), .matrixrows(10)) dotmatrix_10 (
    .col0(_72), .col1(_71), .col2(_74), .col3(_73), .col4(_76), .col5(_75), .col6(_78), .col7(_77));
  DotMatrix #(.matrixcols(8), .matrixrows(10)) dotmatrix_11 (
    .col0(B2), .col1(B1), .col2(B4), .col3(B3), .col4(B6), .col5(B5), .col6(B8), .col7(B7));
  DotMatrix #(.matrixcols(8), .matrixrows(10)) dotmatrix_12 (
    .col0(F2), .col1(F1), .col2(F4), .col3(F3), .col4(F6), .col5(F5), .col6(F8), .col7(F7));
  CdM_8_mark5 cdm_8_mark5_1 (
    .clock(Tcdm8), .addr(addr), .mem_read(read_write), .mem_cycle(memory), .data_out(out),
    .data_in(multiplexer_7_out), .r0(cdm_8_mark5_1_r0), .r1(cdm_8_mark5_1_r1), .r2(cdm_8_mark5_1_r2),
    .r3(cdm_8_mark5_1_r3));  // open: data_inst, PC, SP, PS, IAck, IRQ, vec
  Multiplexer #(.width(8)) multiplexer_7 (
    .in0(data), .in1(CELL_BYTE), .out(multiplexer_7_out), .sel(enF1));  // open: en
  ROM rom_1 (.addr(addr), .data(data));  // open: sel
  Multiplexer #(.width(8)) multiplexer_8 (.in0({8{1'b0}}), .in1(8'h1c), .out(w3), .sel(Win));  // open: en
  Multiplexer #(.width(8)) multiplexer_9 (.in0({8{1'b0}}), .in1({8{1'b1}}), .out(i3), .sel(Win));  // open: en
  Multiplexer #(.width(8)) multiplexer_10 (.in0({8{1'b0}}), .in1(8'h18), .out(n3), .sel(Win));  // open: en
  Register #(.width(4)) register_9 (.D(r3Res), .Q(r3), .clk(T));  // open: en, clr
  Register #(.width(4)) register_10 (.D(r7Res), .Q(r7), .clk(T));  // open: en, clr
  Register #(.width(4)) register_11 (.D(rBRes), .Q(rB), .clk(T));  // open: en, clr
  Register #(.width(4)) register_12 (.D(rFRes), .Q(rF), .clk(T));  // open: en, clr
  and and_2 (enF1, memory, adF1, read_write);
  Comparator comparator_2 (.a(addr), .b(8'hf1), .eq(adF1));  // open: gt, lt
  Multiplexer #(.width(8)) multiplexer_11 (.in0({8{1'b0}}), .in1(8'h2), .out(w4), .sel(Win));  // open: en
  Multiplexer #(.width(8)) multiplexer_12 (.in0({8{1'b0}}), .in1(8'h81), .out(i4), .sel(Win));  // open: en
  Multiplexer #(.width(8)) multiplexer_13 (.in0({8{1'b0}}), .in1(8'h6), .out(n4), .sel(Win));  // open: en
  DotMatrix #(.matrixcols(8), .matrixrows(10)) dotmatrix_13 (
    .col0(_42), .col1(_41), .col2(_44), .col3(_43), .col4(_46), .col5(_45), .col6(_48), .col7(_47));
  DotMatrix #(.matrixcols(8), .matrixrows(10)) dotmatrix_14 (
    .col0(_82), .col1(_81), .col2(_84), .col3(_83), .col4(_86), .col5(_85), .col6(_88), .col7(_87));
  DotMatrix #(.matrixcols(8), .matrixrows(10)) dotmatrix_15 (
    .col0(C2), .col1(C1), .col2(C4), .col3(C3), .col4(C6), .col5(C5), .col6(C8), .col7(C7));
  DotMatrix #(.matrixcols(8), .matrixrows(10)) dotmatrix_16 (
    .col0(_02), .col1(_01), .col2(_04), .col3(_03), .col4(_06), .col5(_05), .col6(_08), .col7(_07));
  Multiplexer #(.width(8)) multiplexer_14 (.in0({8{1'b0}}), .in1({8{1'b1}}), .out(w5), .sel(Win));  // open: en
  Multiplexer #(.width(8)) multiplexer_15 (.in0({8{1'b0}}), .in1(8'h81), .out(i5), .sel(Win));  // open: en
  Multiplexer #(.width(8)) multiplexer_16 (.in0({8{1'b0}}), .in1({8{1'b1}}), .out(n5), .sel(Win));  // open: en
  Register #(.width(4)) register_13 (.D(r4Res), .Q(r4), .clk(T));  // open: en, clr
  Register #(.width(4)) register_14 (.D(r8Res), .Q(r8), .clk(T));  // open: en, clr
  Register #(.width(4)) register_15 (.D(rCRes), .Q(rC), .clk(T));  // open: en, clr
  Register #(.width(4)) register_16 (.D(r0Res), .Q(r0), .clk(T));  // open: en, clr
  Multiplexer #(.width(8)) multiplexer_17 (
    .in0(out), .in1({8{1'b0}}), .out(multiplexer_17_out), .sel(Reset));  // open: en
  Register register_17 (.D(multiplexer_17_out), .en(or_1_out), .Q({register_17_q, Win}), .clk(TWin));  // open: clr
  or or_1 (or_1_out, Reset, enW);
  and and_3 (enW, memory, adW, not_2_out);
  not not_2 (not_2_out, read_write);
  Comparator comparator_3 (.a(addr), .b(8'hf2), .eq(adW));  // open: gt, lt
  DotMatrix #(.matrixcols(17), .matrixrows(8)) dotmatrix_17 (
    .col0(w1), .col1(w2), .col2(w3), .col3(w4), .col4(w5), .col5({8{1'b0}}), .col6(i1), .col7(i2), .col8(i3),
    .col9(i4), .col10(i5), .col11({8{1'b0}}), .col12(n1), .col13(n2), .col14(n3), .col15(n4), .col16(n5));
  Button button (.out(U_B));
  Button button_2 (.out(D_B));
  Button button_3 (.out(L_B));
  Button button_4 (.out(Reset));
  Button button_5 (.out(R_B));
  Multiplexer #(.select(4), .width(4)) multiplexer_18 (
    .in0(r0), .in1(r1), .in2(r2), .in3(r3), .in4(r4), .in5(r5), .in6(r6), .in7(r7), .in8(r8), .in9(r9),
    .in10(rA), .in11(rB), .in12(rC), .in13(rD), .in14(rE), .in15(rF), .out(multiplexer_18_out),
    .sel(register_18_q));  // open: en
  Register #(.width(4)) register_18 (.D(out[3:0]), .en(en), .Q(register_18_q), .clk(Tcdm8));  // open: clr
  and and_4 (LEFT, TWin, L_B);
  Button button_6 (.out(R));
  assign CELL_BYTE = {{4{1'b0}}, multiplexer_18_out};  // Bit_Extender bit_extender_1
  Clock #(.highDuration(150), .lowDuration(150)) clock_1 (.out(T));
  and and_5 (UP, TWin, U_B);
  and and_6 (DOWN, TWin, D_B);
  Clock clock_2 (.out(Tcdm8));
  and and_7 (RIGHT, TWin, R_B);
  Clock clock_3 (.out(clock_3_out));
  Random #(.width(2), .seed(4)) random_1 (.clk(clock_3_out), .next(R), .out(random_1_out));  // open: clr
  Decoder #(.select(2), .enable("false")) decoder_1 (
    .out0(decoder_1_out0), .out1(decoder_1_out1), .out2(decoder_1_out2), .out3(decoder_1_out3),
    .sel(random_1_out));
  and and_8 (UP1, R, decoder_1_out0);
  and and_9 (RIGHT1, R, decoder_1_out3);
  and and_10 (DOWN1, R, decoder_1_out1);
  and and_11 (LEFT1, R, decoder_1_out2);
  ROM #(.addrWidth(4), .dataWidth(20)) rom_2 (.addr(r1), .data({_12, _11}));  // open: sel
  ROM #(.addrWidth(4), .dataWidth(20)) rom_3 (.addr(r1), .data({_14, _13}));  // open: sel
  ROM #(.addrWidth(4), .dataWidth(20)) rom_4 (.addr(r1), .data({_16, _15}));  // open: sel
  ROM #(.addrWidth(4), .dataWidth(20)) rom_5 (.addr(r1), .data({_18, _17}));  // open: sel
  ROM #(.addrWidth(4), .dataWidth(20)) rom_6 (.addr(r5), .data({_52, _51}));  // open: sel
  ROM #(.addrWidth(4), .dataWidth(20)) rom_7 (.addr(r5), .data({_54, _53}));  // open: sel
  ROM #(.addrWidth(4), .dataWidth(20)) rom_8 (.addr(r5), .data({_56, _55}));  // open: sel
  ROM #(.addrWidth(4), .dataWidth(20)) rom_9 (.addr(r5), .data({_58, _57}));  // open: sel
  ROM #(.addrWidth(4), .dataWidth(20)) rom_10 (.addr(r9), .data({_92, _91}));  // open: sel
  ROM #(.addrWidth(4), .dataWidth(20)) rom_11 (.addr(r9), .data({_94, _93}));  // open: sel
  ROM #(.addrWidth(4), .dataWidth(20)) rom_12 (.addr(r9), .data({_96, _95}));  // open: sel
  ROM #(.addrWidth(4), .dataWidth(20)) rom_13 (.addr(r9), .data({_98, _97}));  // open: sel
  ROM #(.addrWidth(4), .dataWidth(20)) rom_14 (.addr(rD), .data({D2, D1}));  // open: sel
  ROM #(.addrWidth(4), .dataWidth(20)) rom_15 (.addr(rD), .data({D4, D3}));  // open: sel
  ROM #(.addrWidth(4), .dataWidth(20)) rom_16 (.addr(rD), .data({D6, D5}));  // open: sel
  ROM #(.addrWidth(4), .dataWidth(20)) rom_17 (.addr(rD), .data({D8, D7}));  // open: sel
  and and_12 (TWin, Tcdm8, or_2_out);
  or or_2 (or_2_out, Reset, not_3_out);
  not not_3 (not_3_out, Win);
  ROM #(.addrWidth(4), .dataWidth(20)) rom_18 (.addr(r2), .data({_22, _21}));  // open: sel
  ROM #(.addrWidth(4), .dataWidth(20)) rom_19 (.addr(r2), .data({_24, _23}));  // open: sel
  ROM #(.addrWidth(4), .dataWidth(20)) rom_20 (.addr(r2), .data({_26, _25}));  // open: sel
  ROM #(.addrWidth(4), .dataWidth(20)) rom_21 (.addr(r2), .data({_28, _27}));  // open: sel
  ROM #(.addrWidth(4), .dataWidth(20)) rom_22 (.addr(r6), .data({_62, _61}));  // open: sel
  ROM #(.addrWidth(4), .dataWidth(20)) rom_23 (.addr(r6), .data({_64, _63}));  // open: sel
  ROM #(.addrWidth(4), .dataWidth(20)) rom_24 (.addr(r6), .data({_66, _65}));  // open: sel
  ROM #(.addrWidth(4), .dataWidth(20)) rom_25 (.addr(r6), .data({_68, _67}));  // open: sel
  ROM #(.addrWidth(4), .dataWidth(20)) rom_26 (.addr(rA), .data({A2, A1}));  // open: sel
  ROM #(.addrWidth(4), .dataWidth(20)) rom_27 (.addr(rA), .data({A4, A3}));  // open: sel
  ROM #(.addrWidth(4), .dataWidth(20)) rom_28 (.addr(rA), .data({A6, A5}));  // open: sel
  ROM #(.addrWidth(4), .dataWidth(20)) rom_29 (.addr(rA), .data({A8, A7}));  // open: sel
  ROM #(.addrWidth(4), .dataWidth(20)) rom_30 (.addr(rE), .data({E2, E1}));  // open: sel
  ROM #(.addrWidth(4), .dataWidth(20)) rom_31 (.addr(rE), .data({E4, E3}));  // open: sel
  ROM #(.addrWidth(4), .dataWidth(20)) rom_32 (.addr(rE), .data({E6, E5}));  // open: sel
  ROM #(.addrWidth(4), .dataWidth(20)) rom_33 (.addr(rE), .data({E8, E7}));  // open: sel
  ROM #(.addrWidth(4), .dataWidth(20)) rom_34 (.addr(r3), .data({_32, _31}));  // open: sel
  ROM #(.addrWidth(4), .dataWidth(20)) rom_35 (.addr(r3), .data({_34, _33}));  // open: sel
  ROM #(.addrWidth(4), .dataWidth(20)) rom_36 (.addr(r3), .data({_36, _35}));  // open: sel
  ROM #(.addrWidth(4), .dataWidth(20)) rom_37 (.addr(r3), .data({_38, _37}));  // open: sel
  ROM #(.addrWidth(4), .dataWidth(20)) rom_38 (.addr(r7), .data({_72, _71}));  // open: sel
  ROM #(.addrWidth(4), .dataWidth(20)) rom_39 (.addr(r7), .data({_74, _73}));  // open: sel
  ROM #(.addrWidth(4), .dataWidth(20)) rom_40 (.addr(r7), .data({_76, _75}));  // open: sel
  ROM #(.addrWidth(4), .dataWidth(20)) rom_41 (.addr(r7), .data({_78, _77}));  // open: sel
  ROM #(.addrWidth(4), .dataWidth(20)) rom_42 (.addr(rB), .data({B2, B1}));  // open: sel
  ROM #(.addrWidth(4), .dataWidth(20)) rom_43 (.addr(rB), .data({B4, B3}));  // open: sel
  ROM #(.addrWidth(4), .dataWidth(20)) rom_44 (.addr(rB), .data({B6, B5}));  // open: sel
  ROM #(.addrWidth(4), .dataWidth(20)) rom_45 (.addr(rB), .data({B8, B7}));  // open: sel
  ROM #(.addrWidth(4), .dataWidth(20)) rom_46 (.addr(rF), .data({F2, F1}));  // open: sel
  ROM #(.addrWidth(4), .dataWidth(20)) rom_47 (.addr(rF), .data({F4, F3}));  // open: sel
  ROM #(.addrWidth(4), .dataWidth(20)) rom_48 (.addr(rF), .data({F6, F5}));  // open: sel
  ROM #(.addrWidth(4), .dataWidth(20)) rom_49 (.addr(rF), .data({F8, F7}));  // open: sel
  ROM #(.addrWidth(4), .dataWidth(20)) rom_50 (.addr(r4), .data({_42, _41}));  // open: sel
  ROM #(.addrWidth(4), .dataWidth(20)) rom_51 (.addr(r4), .data({_44, _43}));  // open: sel
  ROM #(.addrWidth(4), .dataWidth(20)) rom_52 (.addr(r4), .data({_46, _45}));  // open: sel
  ROM #(.addrWidth(4), .dataWidth(20)) rom_53 (.addr(r4), .data({_48, _47}));  // open: sel
  ROM #(.addrWidth(4), .dataWidth(20)) rom_54 (.addr(r8), .data({_82, _81}));  // open: sel
  ROM #(.addrWidth(4), .dataWidth(20)) rom_55 (.addr(r8), .data({_84, _83}));  // open: sel
  ROM #(.addrWidth(4), .dataWidth(20)) rom_56 (.addr(r8), .data({_86, _85}));  // open: sel
  ROM #(.addrWidth(4), .dataWidth(20)) rom_57 (.addr(r8), .data({_88, _87}));  // open: sel
  ROM #(.addrWidth(4), .dataWidth(20)) rom_58 (.addr(rC), .data({C2, C1}));  // open: sel
  ROM #(.addrWidth(4), .dataWidth(20)) rom_59 (.addr(rC), .data({C4, C3}));  // open: sel
  ROM #(.addrWidth(4), .dataWidth(20)) rom_60 (.addr(rC), .data({C6, C5}));  // open: sel
  ROM #(.addrWidth(4), .dataWidth(20)) rom_61 (.addr(rC), .data({C8, C7}));  // open: sel
  ROM #(.addrWidth(4), .dataWidth(20)) rom_62 (.addr(r0), .data({_02, _01}));  // open: sel
  ROM #(.addrWidth(4), .dataWidth(20)) rom_63 (.addr(r0), .data({_04, _03}));  // open: sel
  ROM #(.addrWidth(4), .dataWidth(20)) rom_64 (.addr(r0), .data({_06, _05}));  // open: sel
  ROM #(.addrWidth(4), .dataWidth(20)) rom_65 (.addr(r0), .data({_08, _07}));  // open: sel
  and and_13 (LkR2, or_3_out, kR2);
  or or_3 (or_3_out, LEFT, LEFT1);
  and and_14 (LkR6, or_4_out, kR6);
  or or_4 (or_4_out, LEFT, LEFT1);
  and and_15 (LkRA, or_5_out, kRA);
  or or_5 (or_5_out, LEFT, LEFT1);
  and and_16 (LkRE, or_6_out, kRE);
  or or_6 (or_6_out, LEFT, LEFT1);
  and and_17 (LkR3, or_7_out, kR3);
  or or_7 (or_7_out, LEFT, LEFT1);
  and and_18 (LkR7, or_8_out, kR7);
  or or_8 (or_8_out, LEFT, LEFT1);
  and and_19 (LkRB, or_9_out, kRB);
  or or_9 (or_9_out, LEFT, LEFT1);
  and and_20 (LkRF, or_10_out, kRF);
  or or_10 (or_10_out, LEFT, LEFT1);
  Comparator #(.width(4)) comparator_4 (.a(r1), .b(4'b0000), .eq(kR1));  // open: gt, lt
  Comparator #(.width(4)) comparator_5 (.a(r5), .b(4'b0000), .eq(kR5));  // open: gt, lt
  Comparator #(.width(4)) comparator_6 (.a(r9), .b(4'b0000), .eq(kR9));  // open: gt, lt
  Comparator #(.width(4)) comparator_7 (.a(rD), .b(4'b0000), .eq(kRD));  // open: gt, lt
  and and_21 (LkR4, or_11_out, kR4);
  or or_11 (or_11_out, LEFT, LEFT1);
  and and_22 (LkR8, or_12_out, kR8);
  or or_12 (or_12_out, LEFT, LEFT1);
  and and_23 (LkRC, or_13_out, kRC);
  or or_13 (or_13_out, LEFT, LEFT1);
  and and_24 (LkR0, or_14_out, kR0);
  or or_14 (or_14_out, LEFT, LEFT1);
  and and_25 (UpkR5, or_15_out, kR5);
  or or_15 (or_15_out, UP, UP1);
  and and_26 (UpkR9, or_16_out, kR9);
  or or_16 (or_16_out, UP, UP1);
  and and_27 (UpkRD, or_17_out, kRD);
  or or_17 (or_17_out, UP, UP1);
  or or_18 (or_18_out, DOWN, DOWN1);
  or or_19 (or_19_out, DOWN, DOWN1);
  or or_20 (or_20_out, DOWN, DOWN1);
  Comparator #(.width(4)) comparator_8 (.a(r2), .b(4'b0000), .eq(kR2));  // open: gt, lt
  Comparator #(.width(4)) comparator_9 (.a(r6), .b(4'b0000), .eq(kR6));  // open: gt, lt
  Comparator #(.width(4)) comparator_10 (.a(rA), .b(4'b0000), .eq(kRA));  // open: gt, lt
  Comparator #(.width(4)) comparator_11 (.a(rE), .b(4'b0000), .eq(kRE));  // open: gt, lt
  and and_28 (UpkR6, or_21_out, kR6);
  or or_21 (or_21_out, UP, UP1);
  and and_29 (UpkRA, or_22_out, kRA);
  or or_22 (or_22_out, UP, UP1);
  and and_30 (UpkRE, or_23_out, kRE);
  or or_23 (or_23_out, UP, UP1);
  and and_31 (DkR1, or_18_out, kR1);
  or or_24 (or_24_out, DOWN, DOWN1);
  and and_32 (DkR5, or_19_out, kR5);
  or or_25 (or_25_out, DOWN, DOWN1);
  and and_33 (DkR9, or_20_out, kR9);
  or or_26 (or_26_out, DOWN, DOWN1);
  Comparator #(.width(4)) comparator_12 (.a(r3), .b(4'b0000), .eq(kR3));  // open: gt, lt
  Comparator #(.width(4)) comparator_13 (.a(r7), .b(4'b0000), .eq(kR7));  // open: gt, lt
  Comparator #(.width(4)) comparator_14 (.a(rB), .b(4'b0000), .eq(kRB));  // open: gt, lt
  Comparator #(.width(4)) comparator_15 (.a(rF), .b(4'b0000), .eq(kRF));  // open: gt, lt
  and and_34 (UpkR7, or_27_out, kR7);
  or or_27 (or_27_out, UP, UP1);
  and and_35 (UpkRB, or_28_out, kRB);
  or or_28 (or_28_out, UP, UP1);
  and and_36 (UpkRF, or_29_out, kRF);
  or or_29 (or_29_out, UP, UP1);
  and and_37 (DkR2, or_24_out, kR2);
  or or_30 (or_30_out, DOWN, DOWN1);
  and and_38 (DkR6, or_25_out, kR6);
  or or_31 (or_31_out, DOWN, DOWN1);
  and and_39 (DkRA, or_26_out, kRA);
  or or_32 (or_32_out, DOWN, DOWN1);
  and and_40 (UpkR8, or_33_out, kR8);
  or or_33 (or_33_out, UP, UP1);
  and and_41 (UpkRC, or_34_out, kRC);
  or or_34 (or_34_out, UP, UP1);
  and and_42 (UpkR0, or_35_out, kR0);
  or or_35 (or_35_out, UP, UP1);
  and and_43 (DkR3, or_30_out, kR3);
  or or_36 (or_36_out, DOWN, DOWN1);
  and and_44 (DkR7, or_31_out, kR7);
  or or_37 (or_37_out, DOWN, DOWN1);
  and and_45 (DkRB, or_32_out, kRB);
  or or_38 (or_38_out, DOWN, DOWN1);
  Comparator #(.width(4)) comparator_16 (.a(r4), .b(4'b0000), .eq(kR4));  // open: gt, lt
  Comparator #(.width(4)) comparator_17 (.a(r8), .b(4'b0000), .eq(kR8));  // open: gt, lt
  Comparator #(.width(4)) comparator_18 (.a(rC), .b(4'b0000), .eq(kRC));  // open: gt, lt
  Comparator #(.width(4)) comparator_19 (.a(r0), .b(4'b0000), .eq(kR0));  // open: gt, lt
  and and_46 (DkR4, or_36_out, kR4);
  and and_47 (DkR8, or_37_out, kR8);
  and and_48 (DkRC, or_38_out, kRC);
  and and_49 (RkR1, or_39_out, kR1);
  or or_39 (or_39_out, RIGHT, RIGHT1);
  and and_50 (RkR5, or_40_out, kR5);
  or or_40 (or_40_out, RIGHT, RIGHT1);
  and and_51 (RkR9, or_41_out, kR9);
  or or_41 (or_41_out, RIGHT, RIGHT1);
  and and_52 (RkRD, or_42_out, kRD);
  or or_42 (or_42_out, RIGHT, RIGHT1);
  and and_53 (RkR2, or_43_out, kR2);
  or or_43 (or_43_out, RIGHT, RIGHT1);
  and and_54 (RkR6, or_44_out, kR6);
  or or_44 (or_44_out, RIGHT, RIGHT1);
  and and_55 (RkRA, or_45_out, kRA);
  or or_45 (or_45_out, RIGHT, RIGHT1);
  and and_56 (RkRE, or_46_out, kRE);
  or or_46 (or_46_out, RIGHT, RIGHT1);
  and and_57 (RkR3, or_47_out, kR3);
  or or_47 (or_47_out, RIGHT, RIGHT1);
  and and_58 (RkR7, or_48_out, kR7);
  or or_48 (or_48_out, RIGHT, RIGHT1);
  and and_59 (RkRB, or_49_out, kRB);
  or or_49 (or_49_out, RIGHT, RIGHT1);
  and and_60 (RkRF, or_50_out, kRF);
  or or_50 (or_50_out, RIGHT, RIGHT1);
  Multiplexer #(.width(4), .enable("false")) multiplexer_19 (
    .in0(multiplexer_20_out), .in1(r2), .out(r1Res), .sel(RkR1));
  Multiplexer #(.width(4), .enable("false")) multiplexer_20 (
    .in0(r1_r5_2), .in1(r5), .out(multiplexer_20_out), .sel(DkR1));
  Multiplexer #(.width(4), .enable("false")) multiplexer_21 (
    .in0(multiplexer_23_out), .in1(r6), .out(r1_r5), .sel(RkR5));
  Multiplexer #(.width(4), .enable("false")) multiplexer_22 (.in0(r5), .in1(r1), .out(multiplexer_22_out), .sel(UpkR5));
  Multiplexer #(.width(4), .enable("false")) multiplexer_23 (
    .in0(multiplexer_22_out), .in1(r9), .out(multiplexer_23_out), .sel(DkR5));
  Multiplexer #(.width(4), .enable("false")) multiplexer_24 (
    .in0(multiplexer_26_out), .in1(rA), .out(r9_rA_2), .sel(RkR9));
  Multiplexer #(.width(4), .enable("false")) multiplexer_25 (
    .in0(r5_r9), .in1(r5), .out(multiplexer_25_out), .sel(UpkR9));
  Multiplexer #(.width(4), .enable("false")) multiplexer_26 (
    .in0(multiplexer_25_out), .in1(rD), .out(multiplexer_26_out), .sel(DkR9));
  Multiplexer #(.width(4), .enable("false")) multiplexer_27 (
    .in0(multiplexer_28_out), .in1(rE), .out(rD_rE_2), .sel(RkRD));
  Multiplexer #(.width(4), .enable("false")) multiplexer_28 (
    .in0(r9_rD), .in1(r9), .out(multiplexer_28_out), .sel(UpkRD));
  Multiplexer #(.width(4), .enable("false")) multiplexer_29 (.in0(r2), .in1(r1), .out(r1_r2), .sel(RkR1));
  Multiplexer #(.width(4), .enable("false")) multiplexer_30 (.in0(r1_r5), .in1(r1), .out(r1_r6), .sel(DkR1));
  Multiplexer #(.width(4), .enable("false")) multiplexer_31 (.in0(r6), .in1(r5), .out(r2_r5_2), .sel(RkR5));
  Multiplexer #(.width(4), .enable("false")) multiplexer_32 (.in0(r2_r5), .in1(r5), .out(r1_r5_2), .sel(UpkR5));
  Multiplexer #(.width(4), .enable("false")) multiplexer_33 (.in0(r9), .in1(r5), .out(r5_r9), .sel(DkR5));
  Multiplexer #(.width(4), .enable("false")) multiplexer_34 (.in0(r6_r9), .in1(r9), .out(r9_rA), .sel(RkR9));
  Multiplexer #(.width(4), .enable("false")) multiplexer_35 (.in0(r6_r9_2), .in1(r9), .out(r5Res), .sel(UpkR9));
  Multiplexer #(.width(4), .enable("false")) multiplexer_36 (.in0(rD), .in1(r9), .out(r9_rD), .sel(DkR9));
  Multiplexer #(.width(4), .enable("false")) multiplexer_37 (.in0(rA_rD_2), .in1(rD), .out(rD_rE), .sel(RkRD));
  Multiplexer #(.width(4), .enable("false")) multiplexer_38 (.in0(rA_rD), .in1(rD), .out(r9Res), .sel(UpkRD));
  Multiplexer #(.width(4), .enable("false")) multiplexer_39 (
    .in0(multiplexer_41_out), .in1(r3), .out(r2_r3_2), .sel(RkR2));
  Multiplexer #(.width(4), .enable("false")) multiplexer_40 (
    .in0(r1_r2), .in1(r1), .out(multiplexer_40_out), .sel(LkR2));
  Multiplexer #(.width(4), .enable("false")) multiplexer_41 (
    .in0(multiplexer_40_out), .in1(r6), .out(multiplexer_41_out), .sel(DkR2));
  Multiplexer #(.width(4), .enable("false")) multiplexer_42 (
    .in0(multiplexer_44_out), .in1(r7), .out(multiplexer_42_out), .sel(RkR6));
  Multiplexer #(.width(4), .enable("false")) multiplexer_43 (
    .in0(r2_r6), .in1(r5), .out(multiplexer_43_out), .sel(LkR6));
  Multiplexer #(.width(4), .enable("false")) multiplexer_44 (
    .in0(multiplexer_43_out), .in1(rA), .out(multiplexer_44_out), .sel(DkR6));
  Multiplexer #(.width(4), .enable("false")) multiplexer_45 (
    .in0(multiplexer_42_out), .in1(r2), .out(r6_r7_2), .sel(UpkR6));
  Multiplexer #(.width(4), .enable("false")) multiplexer_46 (
    .in0(multiplexer_48_out), .in1(rB), .out(multiplexer_46_out), .sel(RkRA));
  Multiplexer #(.width(4), .enable("false")) multiplexer_47 (
    .in0(r9_rA), .in1(r9), .out(multiplexer_47_out), .sel(LkRA));
  Multiplexer #(.width(4), .enable("false")) multiplexer_48 (
    .in0(multiplexer_47_out), .in1(rE), .out(multiplexer_48_out), .sel(DkRA));
  Multiplexer #(.width(4), .enable("false")) multiplexer_49 (
    .in0(multiplexer_46_out), .in1(r6), .out(rA_rB_2), .sel(UpkRA));
  Multiplexer #(.width(4), .enable("false")) multiplexer_50 (
    .in0(multiplexer_51_out), .in1(rF), .out(multiplexer_50_out), .sel(RkRE));
  Multiplexer #(.width(4), .enable("false")) multiplexer_51 (
    .in0(rD_rE), .in1(rD), .out(multiplexer_51_out), .sel(LkRE));
  Multiplexer #(.width(4), .enable("false")) multiplexer_52 (
    .in0(multiplexer_50_out), .in1(rA), .out(rE_rF_2), .sel(UpkRE));
  Multiplexer #(.width(4), .enable("false")) multiplexer_53 (.in0(r2_r4), .in1(r2), .out(r2_r3), .sel(RkR2));
  Multiplexer #(.width(4), .enable("false")) multiplexer_54 (.in0(r1), .in1(r2), .out(r2_r5), .sel(LkR2));
  Multiplexer #(.width(4), .enable("false")) multiplexer_55 (.in0(r2_r5_2), .in1(r2), .out(r2_r6), .sel(DkR2));
  Multiplexer #(.width(4), .enable("false")) multiplexer_56 (.in0(r3_r6_2), .in1(r6), .out(r6_r7), .sel(RkR6));
  Multiplexer #(.width(4), .enable("false")) multiplexer_57 (.in0(r1_r6), .in1(r6), .out(r6_r9_2), .sel(LkR6));
  Multiplexer #(.width(4), .enable("false")) multiplexer_58 (.in0(rA), .in1(r6), .out(r6_r9), .sel(DkR6));
  Multiplexer #(.width(4), .enable("false")) multiplexer_59 (.in0(r3_r6), .in1(r6), .out(r2Res), .sel(UpkR6));
  Multiplexer #(.width(4), .enable("false")) multiplexer_60 (.in0(r7_rA), .in1(rA), .out(rA_rB), .sel(RkRA));
  Multiplexer #(.width(4), .enable("false")) multiplexer_61 (.in0(r9_rA_2), .in1(rA), .out(rA_rD), .sel(LkRA));
  Multiplexer #(.width(4), .enable("false")) multiplexer_62 (.in0(rE), .in1(rA), .out(rA_rD_2), .sel(DkRA));
  Multiplexer #(.width(4), .enable("false")) multiplexer_63 (.in0(r7_rA_2), .in1(rA), .out(r6Res), .sel(UpkRA));
  Multiplexer #(.width(4), .enable("false")) multiplexer_64 (.in0(rB_rE), .in1(rE), .out(rE_rF), .sel(RkRE));
  Multiplexer #(.width(4), .enable("false")) multiplexer_65 (.in0(rD_rE_2), .in1(rE), .out(rDRes), .sel(LkRE));
  Multiplexer #(.width(4), .enable("false")) multiplexer_66 (.in0(rB_rE_2), .in1(rE), .out(rARes), .sel(UpkRE));
  Multiplexer #(.width(4), .enable("false")) multiplexer_67 (
    .in0(multiplexer_69_out), .in1(r4), .out(r3_r7), .sel(RkR3));
  Multiplexer #(.width(4), .enable("false")) multiplexer_68 (
    .in0(r2_r3), .in1(r2), .out(multiplexer_68_out), .sel(LkR3));
  Multiplexer #(.width(4), .enable("false")) multiplexer_69 (
    .in0(multiplexer_68_out), .in1(r7), .out(multiplexer_69_out), .sel(DkR3));
  Multiplexer #(.width(4), .enable("false")) multiplexer_70 (
    .in0(multiplexer_72_out), .in1(r8), .out(multiplexer_70_out), .sel(RkR7));
  Multiplexer #(.width(4), .enable("false")) multiplexer_71 (
    .in0(r6_r7), .in1(r6), .out(multiplexer_71_out), .sel(LkR7));
  Multiplexer #(.width(4), .enable("false")) multiplexer_72 (
    .in0(multiplexer_71_out), .in1(rB), .out(multiplexer_72_out), .sel(DkR7));
  Multiplexer #(.width(4), .enable("false")) multiplexer_73 (
    .in0(multiplexer_70_out), .in1(r3), .out(r7_r8), .sel(UpkR7));
  Multiplexer #(.width(4), .enable("false")) multiplexer_74 (
    .in0(multiplexer_76_out), .in1(rC), .out(multiplexer_74_out), .sel(RkRB));
  Multiplexer #(.width(4), .enable("false")) multiplexer_75 (
    .in0(rA_rB), .in1(rA), .out(multiplexer_75_out), .sel(LkRB));
  Multiplexer #(.width(4), .enable("false")) multiplexer_76 (
    .in0(multiplexer_75_out), .in1(rF), .out(multiplexer_76_out), .sel(DkRB));
  Multiplexer #(.width(4), .enable("false")) multiplexer_77 (
    .in0(multiplexer_74_out), .in1(r7), .out(rB_rC_2), .sel(UpkRB));
  Multiplexer #(.width(4), .enable("false")) multiplexer_78 (
    .in0(multiplexer_79_out), .in1(r0), .out(multiplexer_78_out), .sel(RkRF));
  Multiplexer #(.width(4), .enable("false")) multiplexer_79 (
    .in0(rE_rF), .in1(rE), .out(multiplexer_79_out), .sel(LkRF));
  Multiplexer #(.width(4), .enable("false")) multiplexer_80 (
    .in0(multiplexer_78_out), .in1(rB), .out(rF_r0), .sel(UpkRF));
  Multiplexer #(.width(4), .enable("false")) multiplexer_81 (.in0(r4_r3), .in1(r3), .out(r3_r8), .sel(RkR3));
  Multiplexer #(.width(4), .enable("false")) multiplexer_82 (.in0(r2_r3_2), .in1(r3), .out(r3_r6), .sel(LkR3));
  Multiplexer #(.width(4), .enable("false")) multiplexer_83 (.in0(r7), .in1(r3), .out(r3_r6_2), .sel(DkR3));
  Multiplexer #(.width(4), .enable("false")) multiplexer_84 (.in0(r4_r7), .in1(r7), .out(r7_r8_2), .sel(RkR7));
  Multiplexer #(.width(4), .enable("false")) multiplexer_85 (.in0(r6_r7_2), .in1(r7), .out(r7_rA_2), .sel(LkR7));
  Multiplexer #(.width(4), .enable("false")) multiplexer_86 (.in0(rB), .in1(r7), .out(r7_rA), .sel(DkR7));
  Multiplexer #(.width(4), .enable("false")) multiplexer_87 (.in0(r3_r7), .in1(r7), .out(r3Res), .sel(UpkR7));
  Multiplexer #(.width(4), .enable("false")) multiplexer_88 (.in0(r8_rB), .in1(rB), .out(rB_rC), .sel(RkRB));
  Multiplexer #(.width(4), .enable("false")) multiplexer_89 (.in0(rA_rB_2), .in1(rB), .out(rB_rE_2), .sel(LkRB));
  Multiplexer #(.width(4), .enable("false")) multiplexer_90 (.in0(rF), .in1(rB), .out(rB_rE), .sel(DkRB));
  Multiplexer #(.width(4), .enable("false")) multiplexer_91 (.in0(r8_rB_2), .in1(rB), .out(r7Res), .sel(UpkRB));
  Multiplexer #(.width(4), .enable("false")) multiplexer_92 (.in0(rC_rF_2), .in1(rF), .out(rF_r0_2), .sel(RkRF));
  Multiplexer #(.width(4), .enable("false")) multiplexer_93 (.in0(rE_rF_2), .in1(rF), .out(rERes), .sel(LkRF));
  Multiplexer #(.width(4), .enable("false")) multiplexer_94 (.in0(rC_rF), .in1(rF), .out(rBRes), .sel(UpkRF));
  Multiplexer #(.width(4), .enable("false")) multiplexer_95 (
    .in0(multiplexer_96_out), .in1(r3), .out(r4_r3), .sel(LkR4));
  Multiplexer #(.width(4), .enable("false")) multiplexer_96 (.in0(r4), .in1(r8), .out(multiplexer_96_out), .sel(DkR4));
  Multiplexer #(.width(4), .enable("false")) multiplexer_97 (
    .in0(multiplexer_99_out), .in1(r7), .out(r8_rC), .sel(LkR8));
  Multiplexer #(.width(4), .enable("false")) multiplexer_98 (
    .in0(r7_r8_2), .in1(r4), .out(multiplexer_98_out), .sel(UpkR8));
  Multiplexer #(.width(4), .enable("false")) multiplexer_99 (
    .in0(multiplexer_98_out), .in1(rC), .out(multiplexer_99_out), .sel(DkR8));
  Multiplexer #(.width(4), .enable("false")) multiplexer_100 (
    .in0(multiplexer_102_out), .in1(rB), .out(rC_r0), .sel(LkRC));
  Multiplexer #(.width(4), .enable("false")) multiplexer_101 (
    .in0(rB_rC), .in1(r8), .out(multiplexer_101_out), .sel(UpkRC));
  Multiplexer #(.width(4), .enable("false")) multiplexer_102 (
    .in0(multiplexer_101_out), .in1(r0), .out(multiplexer_102_out), .sel(DkRC));
  Multiplexer #(.width(4), .enable("false")) multiplexer_103 (
    .in0(multiplexer_104_out), .in1(rF), .out(r0Res), .sel(LkR0));
  Multiplexer #(.width(4), .enable("false")) multiplexer_104 (
    .in0(rF_r0_2), .in1(rC), .out(multiplexer_104_out), .sel(UpkR0));
  Multiplexer #(.width(4), .enable("false")) multiplexer_105 (.in0(r3), .in1(r4), .out(r2_r4), .sel(LkR4));
  Multiplexer #(.width(4), .enable("false")) multiplexer_106 (.in0(r8), .in1(r4), .out(r4_r7), .sel(DkR4));
  Multiplexer #(.width(4), .enable("false")) multiplexer_107 (.in0(r7_r8), .in1(r8), .out(r8_rB_2), .sel(LkR8));
  Multiplexer #(.width(4), .enable("false")) multiplexer_108 (.in0(r3_r8), .in1(r8), .out(r4Res), .sel(UpkR8));
  Multiplexer #(.width(4), .enable("false")) multiplexer_109 (.in0(rC), .in1(r8), .out(r8_rB), .sel(DkR8));
  Multiplexer #(.width(4), .enable("false")) multiplexer_110 (.in0(rB_rC_2), .in1(rC), .out(rC_rF), .sel(LkRC));
  Multiplexer #(.width(4), .enable("false")) multiplexer_111 (.in0(r8_rC), .in1(rC), .out(r8Res), .sel(UpkRC));
  Multiplexer #(.width(4), .enable("false")) multiplexer_112 (.in0(r0), .in1(rC), .out(rC_rF_2), .sel(DkRC));
  Multiplexer #(.width(4), .enable("false")) multiplexer_113 (.in0(rF_r0), .in1(r0), .out(rFRes), .sel(LkR0));
  Multiplexer #(.width(4), .enable("false")) multiplexer_114 (.in0(rC_r0), .in1(r0), .out(rCRes), .sel(UpkR0));
  LED led_21 ();  // open: in

  // Notes on the sheet:
  //   contents of rom_1 (hex, n*v repeats v):
  //   d3 f2 d0 0 ac d0 1 d1 1 d3 f0 ac d3 f1 be 79 e1 2d 8c 8d d3 10 77 e1 9 d0 0 d3 f0 ac d3 f1 be d1 0
  //   79 e1 2d d0 1 d3 f2 ac ee 0 d0 0 d3 f2 ac ee
  //   contents of rom_2 (hex, n*v repeats v):
  //   0 81 40603 41a01 4030 f1a41 3f921 80207 77a21 78211 3f920 ffa22 7f202 ffa02 ffa22 ffa20
  //   contents of rom_3 (hex, n*v repeats v):
  //   0 407ff 81609 80601 14090 90641 88621 82210 88621 84611 88220 88a22 80a02 80a02 88a22 88220
  //   contents of rom_4 (hex, n*v repeats v):
  //   0 ffc01 84621 98661 44210 90641 88621 88240 88621 84611 88220 88a22 80a02 80a02 88a22 88220
  //   contents of rom_5 (hex, n*v repeats v):
  //   0 400 90581 9859e ffc10 9063e 8841e a0300 885de 849fc 480fe 889dc 80904 410f8 88a02 88200
  //   contents of rom_6 (hex, n*v repeats v):
  //   0 81 40603 41a01 4030 f1a41 3f921 80207 77a21 78211 3f920 ffa22 7f202 ffa02 ffa22 ffa20
  //   contents of rom_7 (hex, n*v repeats v):
  //   0 407ff 81609 80601 14090 90641 88621 82210 88621 84611 88220 88a22 80a02 80a02 88a22 88220
  //   contents of rom_8 (hex, n*v repeats v):
  //   0 ffc01 84621 98661 44210 90641 88621 88240 88621 84611 88220 88a22 80a02 80a02 88a22 88220
  //   contents of rom_9 (hex, n*v repeats v):
  //   0 400 90581 9859e ffc10 9063e 8841e a0300 885de 849fc 480fe 889dc 80904 410f8 88a02 88200
  //   contents of rom_10 (hex, n*v repeats v):
  //   0 81 40603 41a01 4030 f1a41 3f921 80207 77a21 78211 3f920 ffa22 7f202 ffa02 ffa22 ffa20
  //   contents of rom_11 (hex, n*v repeats v):
  //   0 407ff 81609 80601 14090 90641 88621 82210 88621 84611 88220 88a22 80a02 80a02 88a22 88220
  //   contents of rom_12 (hex, n*v repeats v):
  //   0 ffc01 84621 98661 44210 90641 88621 88240 88621 84611 88220 88a22 80a02 80a02 88a22 88220
  //   contents of rom_13 (hex, n*v repeats v):
  //   0 400 90581 9859e ffc10 9063e 8841e a0300 885de 849fc 480fe 889dc 80904 410f8 88a02 88200
  //   contents of rom_14 (hex, n*v repeats v):
  //   0 81 40603 41a01 4030 f1a41 3f921 80207 77a21 78211 3f920 ffa22 7f202 ffa02 ffa22 ffa20
  //   contents of rom_15 (hex, n*v repeats v):
  //   0 407ff 81609 80601 14090 90641 88621 82210 88621 84611 88220 88a22 80a02 80a02 88a22 88220
  //   contents of rom_16 (hex, n*v repeats v):
  //   0 ffc01 84621 98661 44210 90641 88621 88240 88621 84611 88220 88a22 80a02 80a02 88a22 88220
  //   contents of rom_17 (hex, n*v repeats v):
  //   0 400 90581 9859e ffc10 9063e 8841e a0300 885de 849fc 480fe 889dc 80904 410f8 88a02 88200
  //   contents of rom_18 (hex, n*v repeats v):
  //   0 81 40603 41a01 4030 f1a41 3f921 80207 77a21 78211 3f920 ffa22 7f202 ffa02 ffa22 ffa20
  //   contents of rom_19 (hex, n*v repeats v):
  //   0 407ff 81609 80601 14090 90641 88621 82210 88621 84611 88220 88a22 80a02 80a02 88a22 88220
  //   contents of rom_20 (hex, n*v repeats v):
  //   0 ffc01 84621 98661 44210 90641 88621 88240 88621 84611 88220 88a22 80a02 80a02 88a22 88220
  //   contents of rom_21 (hex, n*v repeats v):
  //   0 400 90581 9859e ffc10 9063e 8841e a0300 885de 849fc 480fe 889dc 80904 410f8 88a02 88200
  //   contents of rom_22 (hex, n*v repeats v):
  //   0 81 40603 41a01 4030 f1a41 3f921 80207 77a21 78211 3f920 ffa22 7f202 ffa02 ffa22 ffa20
  //   contents of rom_23 (hex, n*v repeats v):
  //   0 407ff 81609 80601 14090 90641 88621 82210 88621 84611 88220 88a22 80a02 80a02 88a22 88220
  //   contents of rom_24 (hex, n*v repeats v):
  //   0 ffc01 84621 98661 44210 90641 88621 88240 88621 84611 88220 88a22 80a02 80a02 88a22 88220
  //   contents of rom_25 (hex, n*v repeats v):
  //   0 400 90581 9859e ffc10 9063e 8841e a0300 885de 849fc 480fe 889dc 80904 410f8 88a02 88200
  //   contents of rom_26 (hex, n*v repeats v):
  //   0 81 40603 41a01 4030 f1a41 3f921 80207 77a21 78211 3f920 ffa22 7f202 ffa02 ffa22 ffa20
  //   contents of rom_27 (hex, n*v repeats v):
  //   0 407ff 81609 80601 14090 90641 88621 82210 88621 84611 88220 88a22 80a02 80a02 88a22 88220
  //   contents of rom_28 (hex, n*v repeats v):
  //   0 ffc01 84621 98661 44210 90641 88621 88240 88621 84611 88220 88a22 80a02 80a02 88a22 88220
  //   contents of rom_29 (hex, n*v repeats v):
  //   0 400 90581 9859e ffc10 9063e 8841e a0300 885de 849fc 480fe 889dc 80904 410f8 88a02 88200
  //   contents of rom_30 (hex, n*v repeats v):
  //   0 81 40603 41a01 4030 f1a41 3f921 80207 77a21 78211 3f920 ffa22 7f202 ffa02 ffa22 ffa20
  //   contents of rom_31 (hex, n*v repeats v):
  //   0 407ff 81609 80601 14090 90641 88621 82210 88621 84611 88220 88a22 80a02 80a02 88a22 88220
  //   contents of rom_32 (hex, n*v repeats v):
  //   0 ffc01 84621 98661 44210 90641 88621 88240 88621 84611 88220 88a22 80a02 80a02 88a22 88220
  //   contents of rom_33 (hex, n*v repeats v):
  //   0 400 90581 9859e ffc10 9063e 8841e a0300 885de 849fc 480fe 889dc 80904 410f8 88a02 88200
  //   contents of rom_34 (hex, n*v repeats v):
  //   0 81 40603 41a01 4030 f1a41 3f921 80207 77a21 78211 3f920 ffa22 7f202 ffa02 ffa22 ffa20
  //   contents of rom_35 (hex, n*v repeats v):
  //   0 407ff 81609 80601 14090 90641 88621 82210 88621 84611 88220 88a22 80a02 80a02 88a22 88220
  //   contents of rom_36 (hex, n*v repeats v):
  //   0 ffc01 84621 98661 44210 90641 88621 88240 88621 84611 88220 88a22 80a02 80a02 88a22 88220
  //   contents of rom_37 (hex, n*v repeats v):
  //   0 400 90581 9859e ffc10 9063e 8841e a0300 885de 849fc 480fe 889dc 80904 410f8 88a02 88200
  //   contents of rom_38 (hex, n*v repeats v):
  //   0 81 40603 41a01 4030 f1a41 3f921 80207 77a21 78211 3f920 ffa22 7f202 ffa02 ffa22 ffa20
  //   contents of rom_39 (hex, n*v repeats v):
  //   0 407ff 81609 80601 14090 90641 88621 82210 88621 84611 88220 88a22 80a02 80a02 88a22 88220
  //   contents of rom_40 (hex, n*v repeats v):
  //   0 ffc01 84621 98661 44210 90641 88621 88240 88621 84611 88220 88a22 80a02 80a02 88a22 88220
  //   contents of rom_41 (hex, n*v repeats v):
  //   0 400 90581 9859e ffc10 9063e 8841e a0300 885de 849fc 480fe 889dc 80904 410f8 88a02 88200
  //   contents of rom_42 (hex, n*v repeats v):
  //   0 81 40603 41a01 4030 f1a41 3f921 80207 77a21 78211 3f920 ffa22 7f202 ffa02 ffa22 ffa20
  //   contents of rom_43 (hex, n*v repeats v):
  //   0 407ff 81609 80601 14090 90641 88621 82210 88621 84611 88220 88a22 80a02 80a02 88a22 88220
  //   contents of rom_44 (hex, n*v repeats v):
  //   0 ffc01 84621 98661 44210 90641 88621 88240 88621 84611 88220 88a22 80a02 80a02 88a22 88220
  //   contents of rom_45 (hex, n*v repeats v):
  //   0 400 90581 9859e ffc10 9063e 8841e a0300 885de 849fc 480fe 889dc 80904 410f8 88a02 88200
  //   contents of rom_46 (hex, n*v repeats v):
  //   0 81 40603 41a01 4030 f1a41 3f921 80207 77a21 78211 3f920 ffa22 7f202 ffa02 ffa22 ffa20
  //   contents of rom_47 (hex, n*v repeats v):
  //   0 407ff 81609 80601 14090 90641 88621 82210 88621 84611 88220 88a22 80a02 80a02 88a22 88220
  //   contents of rom_48 (hex, n*v repeats v):
  //   0 ffc01 84621 98661 44210 90641 88621 88240 88621 84611 88220 88a22 80a02 80a02 88a22 88220
  //   contents of rom_49 (hex, n*v repeats v):
  //   0 400 90581 9859e ffc10 9063e 8841e a0300 885de 849fc 480fe 889dc 80904 410f8 88a02 88200
  //   contents of rom_50 (hex, n*v repeats v):
  //   0 81 40603 41a01 4030 f1a41 3f921 80207 77a21 78211 3f920 ffa22 7f202 ffa02 ffa22 ffa20
  //   contents of rom_51 (hex, n*v repeats v):
  //   0 407ff 81609 80601 14090 90641 88621 82210 88621 84611 88220 88a22 80a02 80a02 88a22 88220
  //   contents of rom_52 (hex, n*v repeats v):
  //   0 ffc01 84621 98661 44210 90641 88621 88240 88621 84611 88220 88a22 80a02 80a02 88a22 88220
  //   contents of rom_53 (hex, n*v repeats v):
  //   0 400 90581 9859e ffc10 9063e 8841e a0300 885de 849fc 480fe 889dc 80904 410f8 88a02 88200
  //   contents of rom_54 (hex, n*v repeats v):
  //   0 81 40603 41a01 4030 f1a41 3f921 80207 77a21 78211 3f920 ffa22 7f202 ffa02 ffa22 ffa20
  //   contents of rom_55 (hex, n*v repeats v):
  //   0 407ff 81609 80601 14090 90641 88621 82210 88621 84611 88220 88a22 80a02 80a02 88a22 88220
  //   contents of rom_56 (hex, n*v repeats v):
  //   0 ffc01 84621 98661 44210 90641 88621 88240 88621 84611 88220 88a22 80a02 80a02 88a22 88220
  //   contents of rom_57 (hex, n*v repeats v):
  //   0 400 90581 9859e ffc10 9063e 8841e a0300 885de 849fc 480fe 889dc 80904 410f8 88a02 88200
  //   contents of rom_58 (hex, n*v repeats v):
  //   0 81 40603 41a01 4030 f1a41 3f921 80207 77a21 78211 3f920 ffa22 7f202 ffa02 ffa22 ffa20
  //   contents of rom_59 (hex, n*v repeats v):
  //   0 407ff 81609 80601 14090 90641 88621 82210 88621 84611 88220 88a22 80a02 80a02 88a22 88220
  //   contents of rom_60 (hex, n*v repeats v):
  //   0 ffc01 84621 98661 44210 90641 88621 88240 88621 84611 88220 88a22 80a02 80a02 88a22 88220
  //   contents of rom_61 (hex, n*v repeats v):
  //   0 400 90581 9859e ffc10 9063e 8841e a0300 885de 849fc 480fe 889dc 80904 410f8 88a02 88200
  //   contents of rom_62 (hex, n*v repeats v):
  //   0 81 40603 41a01 4030 f1a41 3f921 80207 77a21 78211 3f920 ffa22 7f202 ffa02 ffa22 ffa20
  //   contents of rom_63 (hex, n*v repeats v):
  //   0 407ff 81609 80601 14090 90641 88621 82210 88621 84611 88220 88a22 80a02 80a02 88a22 88220
  //   contents of rom_64 (hex, n*v repeats v):
  //   0 ffc01 84621 98661 44210 90641 88621 88240 88621 84611 88220 88a22 80a02 80a02 88a22 88220
  //   contents of rom_65 (hex, n*v repeats v):
  //   0 400 90581 9859e ffc10 9063e 8841e a0300 885de 849fc 480fe 889dc 80904 410f8 88a02 88200
  //   LEFT
  //   UP
  //   DOWN
  //   RIGHT
endmodule

module Digit (
  input  [3:0] in_1
);

  wire _12345;
  wire [19:0] rom_1_data;

  ROM #(.addrWidth(4), .dataWidth(20)) rom_1 (
    .addr(in_1), .data({rom_1_data[19:4], _12345, rom_1_data[2:0]}));  // open: sel
  LED led_1 (.in(rom_1_data[0]));
  LED led_2 (.in(rom_1_data[1]));
  LED led_3 (.in(rom_1_data[4]));
  LED led_4 (.in(rom_1_data[5]));
  LED led_5 (.in(rom_1_data[9]));
  LED led_6 (.in(rom_1_data[8]));
  LED led_7 (.in(rom_1_data[13]));
  LED led_8 (.in(rom_1_data[12]));
  LED led_9 (.in(rom_1_data[16]));
  LED led_10 (.in(rom_1_data[17]));
  LED led_11 (.in(rom_1_data[2]));
  LED led_12 (.in(rom_1_data[7]));
  LED led_13 (.in(rom_1_data[6]));
  LED led_14 (.in(rom_1_data[10]));
  LED led_15 (.in(rom_1_data[11]));
  LED led_16 (.in(rom_1_data[14]));
  LED led_17 (.in(rom_1_data[15]));
  LED led_18 (.in(rom_1_data[18]));
  LED led_19 (.in(rom_1_data[19]));

  // Notes on the sheet:
  //   contents of rom_1 (hex, n*v repeats v):
  //   f999f f4564 f1f8f f8f8f 88f99 f8f1f f9f1f 1248f f9f9f f8f9f 99f9f f9f11 f111f f9f88 f1f1f 11f1f
endmodule
